// Logisim project cpu21-riscv.circ as structural Verilog: 24 circuits, main circuit ◇单周期RISC-V
module \单周期RISC_V  (
  input  IR1,
  input  IR2,
  input  IR3,
  output RegWrite,
  output MemWrite,
  output [31:0] PC,
  output [31:0] IR,
  output [31:0] RDin,
  output [31:0] MDin,
  output [31:0] LedData
);

  wire AluSrcB, and_1_out, and_2_out, and_3_out, and_4_out, and_5_out, Beq, bltu, Bne, CLK, clock_1_out,
       comparator_1_eq, comparator_2_eq, comparator_2_lt, d_ff_1_q, ecall, equal, Go, halt, IR1_t, IR2_t,
       IR3_t, IRA, IRB, IRC, jal, jalr, lbu, MemToReg, nand_1_out, not_1_out, not_2_out, or_1_out,
       riscv_probe_1_p2, RST, S_type, tunnel, W1, W2, W3;
  wire [1:0] PCSrc;
  wire [1:1] or_5_out;
  wire [3:0] AluOp;
  wire [4:0] multiplexer_3_out, multiplexer_4_out;
  wire [7:0] multiplexer_7_out;
  wire [11:0] multiplexer_2_out;
  wire [12:0] CNT_num;
  wire [15:0] \总周期数 ;
  wire [31:0] ALU_result, bit_extender_1_out, bit_extender_2_out, bit_extender_3_out, bit_extender_4_out,
       \b分支 , \jal分支 , MDout, multiplexer_1_out, multiplexer_5_out, multiplexer_8_out, PC_4, regifile_1_r1,
       shifter_1_out, shifter_2_out;

  Button \u_继续运行  (.out(Go));
  Button _1 (.out(IRA));
  Button _2 (.out(IRB));
  Button _3 (.out(IRC));
  LED #(.active("true")) led_1 (.in(W1));
  LED #(.active("true")) led_2 (.in(W2));
  LED #(.active("true")) led_3 (.in(W3));
  Hex_Digit_Display hex_digit_display_1 (.value(LedData[31:28]));  // open: dp
  Hex_Digit_Display hex_digit_display_2 (.value(LedData[23:20]));  // open: dp
  Hex_Digit_Display hex_digit_display_3 (.value(LedData[27:24]));  // open: dp
  and and_1 (and_1_out, Beq, equal);
  and and_2 (and_2_out, ~equal, Bne);  // AND_Gate
  and and_3 (and_3_out, bltu, tunnel);
  Hex_Digit_Display hex_digit_display_4 (.value(LedData[19:16]));  // open: dp
  Hex_Digit_Display hex_digit_display_5 (.value(LedData[15:12]));  // open: dp
  or or_1 (or_1_out, and_1_out, and_2_out, and_3_out);
  Multiplexer #(.select(2), .width(32), .disabled("Z"), .enable("false")) multiplexer_1 (
    .in0(PC_4), .in1(ALU_result), .in2(\jal分支 ), .in3(\b分支 ), .out(multiplexer_1_out), .sel(PCSrc));
  Hex_Digit_Display hex_digit_display_6 (.value(LedData[7:4]));  // open: dp
  Hex_Digit_Display hex_digit_display_7 (.value(LedData[11:8]));  // open: dp
  // Probe on \总周期数 
  Priority_Encoder #(.select(2), .disabled("Z")) priority_encoder_1 (
    .in0(1'b1), .in1(jalr), .in2(jal), .in3(or_1_out), .out(PCSrc));  // open: gs, en_out, en_in
  Register #(.width(32), .trigger("rising"), .Select("low")) u_PC (
    .D(multiplexer_1_out), .en(not_1_out), .Q(PC), .clk(CLK), .clr(RST));
  not not_1 (not_1_out, halt);
  Hex_Digit_Display hex_digit_display_8 (.value(LedData[3:0]));  // open: dp
  // Probe on PC
  Adder #(.width(32)) adder_1 (.a(PC), .b(32'h4), .out(PC_4));  // open: cin, cout
  or or_2 (IR1_t, IR1, IRA);
  // RiscV_Probe riscv_probe_1: pin names not known; wires that end beside it: IR, riscv_probe_1_p2, 5'b10001
  or or_3 (IR2_t, IR2, IRB);
  ROM #(.addrWidth(10), .dataWidth(32), .Select("high")) rom_1 (.addr(PC[11:2]), .data(IR));
  or or_4 (IR3_t, IR3, IRC);
  Multiplexer #(.select(1), .width(12), .disabled("Z"), .enable("false")) multiplexer_2 (
    .in0(IR[31:20]), .in1({IR[31:25], IR[11:7]}), .out(multiplexer_2_out), .sel(S_type));
  \单周期硬布线控制器  \u_单周期硬布线控制器_1  (
    .Funct({IR[30], IR[25], IR[14:12]}), .OP(IR[6:2]), .ALU_OP(AluOp), .MemToReg(MemToReg),
    .MemWrite(MemWrite), .ALU_SRC(AluSrcB), .RegWrite(RegWrite), .ecall(ecall), .S_type(S_type), .Jalr(jalr),
    .Beq(Beq), .JAL(jal), .Bne(Bne), .in_3(IR[21]), .uret(riscv_probe_1_p2), .lbu(lbu), .bltu(bltu));  // open: Rs1Used, Rs2Used, csrrsi, csrrci
  Multiplexer #(.select(1), .width(5), .disabled("Z"), .enable("false")) multiplexer_3 (
    .in0(IR[19:15]), .in1(5'b10001), .out(multiplexer_3_out), .sel(ecall));
  Multiplexer #(.select(1), .width(5), .disabled("Z"), .enable("false")) multiplexer_4 (
    .in0(IR[24:20]), .in1(5'b01010), .out(multiplexer_4_out), .sel(ecall));
  assign bit_extender_1_out = {{20{multiplexer_2_out[11]}}, multiplexer_2_out};  // Bit_Extender bit_extender_1
  assign bit_extender_2_out = {{20{IR[31]}}, {IR[31], IR[7], IR[30:25], IR[11:8]}};  // Bit_Extender bit_extender_2
  assign bit_extender_3_out = {{12{IR[31]}}, {IR[31], IR[19:12], IR[20], IR[30:21]}};  // Bit_Extender bit_extender_3
  // Probe on multiplexer_3_out
  // Probe on multiplexer_4_out
  // Probe on IR[11:7]
  Shifter #(.width(32), .shift("ll")) shifter_1 (.in(bit_extender_2_out), .\dist (5'b00001), .out(shifter_1_out));
  Shifter #(.width(32), .shift("ll")) shifter_2 (.in(bit_extender_3_out), .\dist (5'b00001), .out(shifter_2_out));
  Adder #(.width(32)) adder_2 (.a(shifter_1_out), .b(PC), .out(\b分支 ));  // open: cin, cout
  Adder #(.width(32)) adder_3 (.a(shifter_2_out), .b(PC), .out(\jal分支 ));  // open: cin, cout
  Regifile regifile_1 (
    .Din(RDin), .Clk(CLK), .R1(regifile_1_r1), .R2(MDin), .WE(RegWrite), .W_num(IR[11:7]),
    .R1_num(multiplexer_3_out), .R2_num(multiplexer_4_out));
  Comparator #(.width(32), .mode("twosComplement")) comparator_1 (
    .a(regifile_1_r1), .b(32'h22), .eq(comparator_1_eq));  // open: gt, lt
  D_Flip_Flop #(.trigger("high"), .Pre_Clr_Positions("LEGACY"), .NegatePresetClear("false"), .enable("true"), .NewFFLayout("false")) d_ff_1 (.Q(d_ff_1_q));  // open: clk, D, Qn, preset, en, reset
  // Probe on 13'h60a
  Multiplexer #(.select(1), .width(32), .disabled("Z"), .enable("false")) multiplexer_5 (
    .in0(MDin), .in1(bit_extender_1_out), .out(multiplexer_5_out), .sel(AluSrcB));
  and and_4 (and_4_out, comparator_1_eq, ecall);
  Comparator #(.width(13), .mode("twosComplement")) comparator_2 (
    .a(CNT_num), .b(13'h60a), .eq(comparator_2_eq), .lt(comparator_2_lt));  // open: gt
  Clock #(.highDuration(1), .lowDuration(1)) clock_1 (.out(clock_1_out));
  ALU alu_1 (
    .X(regifile_1_r1), .Y(multiplexer_5_out), .AluOP(AluOp), .Equal(equal), .Result(ALU_result),
    .out_6(tunnel));  // open: Result_2, out_4
  and and_5 (and_5_out, ecall, ~comparator_1_eq);  // AND_Gate
  Register #(.width(32), .trigger("rising"), .Select("low")) register_1 (
    .D(MDin), .en(and_4_out), .Q(LedData), .clk(CLK));  // open: clr
  Counter #(.width(13), .max('h1fff), .ongoal("stay"), .trigger("rising"), .behavior("old")) counter_1 (
    .count(comparator_2_lt), .Q(CNT_num), .clk(clock_1_out));  // open: load, D, carry, clr, preset
  Multiplexer #(.select(1), .width(1), .disabled("Z"), .enable("false")) multiplexer_6 (
    .in0(and_5_out), .in1(1'b0), .out(halt), .sel(Go));
  nand nand_1 (nand_1_out, d_ff_1_q, comparator_2_eq);
  assign CLK = nand_1_out ? clock_1_out : 1'bz;  // Controlled_Buffer controlled_buffer_1
  Pull_Resistor #(.pull(1)) pull_resistor_1 (.node(CLK));
  Multiplexer #(.select(2), .width(8), .disabled("Z"), .enable("false")) multiplexer_7 (
    .in0(MDout[7:0]), .in1(MDout[15:8]), .in2(MDout[23:16]), .in3(MDout[31:24]), .out(multiplexer_7_out),
    .sel(ALU_result[1:0]));
  RAM #(.addrWidth(10), .dataWidth(32), .bus("separate"), .Select("high")) ram_1 (
    .addr(ALU_result[11:2]), .din(MDin), .data(MDout), .str(MemWrite), .clk(CLK));  // open: sel, ld, clr
  assign bit_extender_4_out = {{24{1'b0}}, multiplexer_7_out};  // Bit_Extender bit_extender_4
  Button button_1 (.out(RST));
  not not_2 (not_2_out, halt);
  Counter #(.width(16), .max('hffff), .ongoal("wrap"), .trigger("rising"), .behavior("new")) counter_2 (
    .count(not_2_out), .Q(\总周期数 ), .clk(CLK), .clr(RST));  // open: load, D, carry, preset, down
  Multiplexer #(.select(1), .width(32), .disabled("Z"), .enable("false")) multiplexer_8 (
    .in0(MDout), .in1(bit_extender_4_out), .out(multiplexer_8_out), .sel(lbu));
  Multiplexer #(.select(2), .width(32), .disabled("Z"), .enable("false")) multiplexer_9 (
    .in0(ALU_result), .in1(multiplexer_8_out), .in2(PC_4), .out(RDin), .sel({or_5_out[1], MemToReg}));  // open: in3
  or or_5 (or_5_out[1], jal, jalr);

  // Notes on the sheet:
  //   中断源
  //   中断等待指示
  //   数码管输出应该用寄存器锁存，否则显示数据只能一闪而过
  //   数码管输出
  //   指令探针
  //   指令存储器
  //   指令字
  //   contents of rom_1 (hex, n*v repeats v):
  //   100493 100006f 100493 200913 300993 100006f 100493 200913 300993 100006f 100493 200913 300993
  //   100006f 100493 200913 300993 29c000ef 100413 100493 1f49493 900533 2200893 73 24d493 48463 fedff06f
  //   900533 2200893 73 100493 249493 900533 2200893 73 48463 fedff06f 100493 1f49493 900533 2200893 73
  //   4034d493 900533 2200893 73 4044d493 900533 2200893 73 4044d493 900533 2200893 73 4044d493 900533
  //   2200893 73 4044d493 900533 2200893 73 4044d493 900533 2200893 73 4044d493 900533 2200893 73 4044d493
  //   900533 2200893 73 100413 1f41993 41f9d993 433 c00913 300b13 140413 f47413 800293 100313 499993
  //   89e9b3 1300533 2200893 73 406282b3 fe0294e3 140413 f00f93 1f47433 1c41413 800293 100313 49d993
  //   89e9b3 1300533 2200893 73 406282b3 fe0294e3 1c45413 406b0b33 b0463 f95ff06f 2b3 fff2c293 829293
  //   ff2e293 500533 2200893 73 fff00413 493 84a023 140413 448493 84a023 140413 448493 84a023 140413
  //   448493 84a023 140413 448493 84a023 140413 448493 84a023 140413 448493 84a023 140413 448493 84a023
  //   140413 448493 84a023 140413 448493 84a023 140413 448493 84a023 140413 448493 84a023 140413 448493
  //   84a023 140413 448493 84a023 140413 448493 84a023 140413 448493 84a023 140413 448493 140413 433
  //   3c00493 42983 4aa03 149a2b3 28663 134a023 1442023 ffc48493 fe9412e3 800533 2200893 73 440413 3c00493
  //   fc9416e3 a00893 73 413 140413 800533 2200893 73 240413 800533 2200893 73 340413 800533 2200893 73
  //   440413 800533 2200893 73 540413 800533 2200893 73 640413 800533 2200893 73 740413 800533 2200893 73
  //   840413 800533 2200893 2200893 73 8067
  //   rs1
  //   rs2
  //   rd
  //   imm-lw
  //   imm-sw
  //   imm-b
  //   imm-jal
  //   JAL
  //   JALR
  //   URET
  //   lbu
  //   bltu
  //   Beq
  //   Bne
  //   MemToReg
  //   MemWrite
  //   AluOP
  //   AluSrcB
  //   RegWrite
  //   为方便自动评测，需要输出PC，IR，寄存器堆写如数据RDin
  //   RAM写使能MemWrite、RAM写入数据MDin等信号
  //   R[rs1]
  //   R[rs2]
  //   控制位
  //   暂停节拍，不能为0
  //   戳工具置1进入计数暂停模式，ctrl+k时钟自动运行到对应节拍暂停
  //   ctrl+k关闭时钟连续运行，将控制位置零，进入单步调试模式调试
  //   用这个时钟源需要去掉电路中的其他时钟源
  //   数据存储器
  //   可计数暂停的时钟源
endmodule

// 单周期硬布线控制器
module \单周期硬布线控制器  (
  input  [4:0] OP,
  input  [4:0] Funct,
  input  in_3,
  output [3:0] ALU_OP,
  output uret,
  output MemToReg,
  output ecall,
  output MemWrite,
  output ALU_SRC,
  output RegWrite,
  output S_type,
  output Beq,
  output Bne,
  output Jalr,
  output JAL,
  output lbu,
  output bltu,
  output Rs1Used,
  output Rs2Used,
  output csrrsi,
  output csrrci
);

  wire \控制信号自动生成_1_ecall ;

  \运算控制器自动生成  \u_运算控制器自动生成_1  (
    .OP2(OP[0]), .OP3(OP[1]), .OP4(OP[2]), .OP5(OP[3]), .OP6(OP[4]), .F12(Funct[0]), .F13(Funct[1]),
    .F14(Funct[2]), .F25(Funct[3]), .F30(Funct[4]), .S0(ALU_OP[0]), .S1(ALU_OP[1]), .S2(ALU_OP[2]),
    .S3(ALU_OP[3]));
  \控制信号自动生成  \u_控制信号自动生成_1  (
    .OP2(OP[0]), .OP3(OP[1]), .OP4(OP[2]), .OP5(OP[3]), .OP6(OP[4]), .MemToReg(MemToReg), .F12(Funct[0]),
    .F13(Funct[1]), .F14(Funct[2]), .F25(Funct[3]), .F30(Funct[4]), .MemWrite(MemWrite), .ALU_SRC(ALU_SRC),
    .RegWrite(RegWrite), .ecall(\控制信号自动生成_1_ecall ), .S_Type(S_type), .BEQ(Beq), .BNE(Bne), .JALR(Jalr),
    .JAL(JAL), .lbu(lbu), .bltu(bltu), .Rs1Used(Rs1Used), .Rs2Used(Rs2Used), .csrrsi(csrrsi), .csrrci(csrrci));
  and and_1 (uret, in_3, \控制信号自动生成_1_ecall );
  and and_2 (ecall, ~in_3, \控制信号自动生成_1_ecall );  // AND_Gate

  // Other names for the same wires on the sheet: IR21 = in_3; OP_CODE[4:0] = OP

  // Notes on the sheet:
  //   控制信号生成，产生数据通路需要的其他控制信号
  //   运算器控制器，根据指令生成运算器功能选择信号
endmodule

// 运算器控制器
module \运算控制器自动生成  (
  input  OP2,
  input  OP3,
  input  OP4,
  input  OP5,
  input  OP6,
  input  F12,
  input  F13,
  input  F14,
  input  F25,
  input  F30,
  output S0,
  output S1,
  output S2,
  output S3
);

  wire and_1_out, and_2_out, and_3_out, and_4_out, and_5_out, and_6_out, and_7_out, and_8_out, and_9_out,
       and_10_out, and_11_out, and_12_out, and_13_out, and_14_out, and_15_out, and_16_out, and_17_out,
       and_18_out, and_19_out, and_20_out, and_21_out, and_22_out, and_23_out, and_24_out, and_25_out,
       and_26_out, and_27_out, and_28_out, and_29_out, and_30_out, and_31_out, and_32_out, and_33_out,
       and_34_out, and_35_out, and_36_out, and_37_out, and_38_out, not_1_out, not_2_out, not_3_out,
       not_4_out, not_5_out, not_6_out, not_7_out, not_8_out, not_9_out, not_10_out, not_11_out, not_12_out,
       not_13_out, not_14_out, not_15_out, not_16_out, not_17_out, not_18_out, not_19_out, not_20_out,
       not_21_out, not_22_out, not_23_out, not_24_out, not_25_out, not_26_out, not_27_out, not_28_out,
       not_29_out, not_30_out, not_31_out, not_32_out, not_33_out, not_34_out, not_35_out, not_36_out,
       not_37_out, not_38_out, not_39_out, not_40_out, not_41_out, not_42_out, not_43_out, not_44_out,
       not_45_out, not_46_out, not_47_out, not_48_out, not_49_out, not_50_out, not_51_out, not_52_out,
       not_53_out, not_54_out, not_55_out, not_56_out, not_57_out, not_58_out, not_59_out, not_60_out,
       not_61_out, not_62_out, not_63_out, not_64_out, not_65_out, not_66_out, not_67_out, not_68_out,
       not_69_out, not_70_out, not_71_out, not_72_out, not_73_out, not_74_out, not_75_out, not_76_out,
       not_77_out, not_78_out, not_79_out, not_80_out, not_81_out, not_82_out, not_83_out, not_84_out,
       not_85_out, not_86_out, not_87_out, not_88_out, not_89_out, not_90_out, not_91_out, not_92_out,
       not_93_out, not_94_out, not_95_out, not_96_out, not_97_out, not_98_out, not_99_out, not_100_out,
       not_101_out, not_102_out, not_103_out, not_104_out, not_105_out, not_106_out, not_107_out,
       not_108_out, not_109_out, not_110_out, not_111_out, not_112_out, not_113_out, not_114_out,
       not_115_out, not_116_out, not_117_out, not_118_out, not_119_out, not_120_out, not_121_out,
       not_122_out, not_123_out, not_124_out, not_125_out, not_126_out, not_127_out, not_128_out,
       not_129_out, not_130_out, not_131_out, not_132_out, not_133_out, not_134_out, not_135_out,
       not_136_out, not_137_out, not_138_out, not_139_out, not_140_out, not_141_out, not_142_out,
       not_143_out, not_144_out, not_145_out, not_146_out, not_147_out, not_148_out, not_149_out,
       not_150_out, not_151_out, not_152_out, not_153_out, not_154_out, not_155_out, not_156_out,
       not_157_out, not_158_out, not_159_out, not_160_out, not_161_out, not_162_out, not_163_out,
       not_164_out, not_165_out, not_166_out, not_167_out, not_168_out, not_169_out, not_170_out,
       not_171_out, not_172_out, not_173_out, not_174_out, not_175_out, not_176_out, not_177_out,
       not_178_out, not_179_out, not_180_out, not_181_out, not_182_out, not_183_out, not_184_out,
       not_185_out, not_186_out, not_187_out, not_188_out, not_189_out, not_190_out, not_191_out,
       not_192_out, not_193_out, not_194_out, not_195_out, not_196_out, not_197_out, not_198_out,
       not_199_out, not_200_out, not_201_out, not_202_out, not_203_out, not_204_out, not_205_out,
       not_206_out, not_207_out, not_208_out, not_209_out, not_210_out, not_211_out, not_212_out,
       not_213_out, not_214_out, not_215_out, not_216_out, not_217_out, not_218_out, not_219_out,
       not_220_out, not_221_out, not_222_out, not_223_out, not_224_out, not_225_out, not_226_out;

  not not_1 (not_1_out, F30);
  not not_2 (not_2_out, F25);
  not not_3 (not_3_out, F14);
  not not_4 (not_4_out, F13);
  not not_5 (not_5_out, F12);
  not not_6 (not_6_out, OP6);
  not not_7 (not_7_out, OP3);
  not not_8 (not_8_out, OP2);
  not not_9 (not_9_out, F30);
  not not_10 (not_10_out, F25);
  not not_11 (not_11_out, OP6);
  not not_12 (not_12_out, OP3);
  not not_13 (not_13_out, OP2);
  not not_14 (not_14_out, F30);
  not not_15 (not_15_out, F25);
  not not_16 (not_16_out, F14);
  not not_17 (not_17_out, F12);
  not not_18 (not_18_out, OP6);
  not not_19 (not_19_out, OP3);
  not not_20 (not_20_out, OP2);
  not not_21 (not_21_out, F14);
  not not_22 (not_22_out, F13);
  not not_23 (not_23_out, F12);
  not not_24 (not_24_out, OP6);
  not not_25 (not_25_out, OP5);
  not not_26 (not_26_out, OP3);
  not not_27 (not_27_out, OP2);
  not not_28 (not_28_out, OP6);
  not not_29 (not_29_out, OP5);
  not not_30 (not_30_out, OP3);
  not not_31 (not_31_out, OP2);
  not not_32 (not_32_out, F13);
  not not_33 (not_33_out, F12);
  not not_34 (not_34_out, OP6);
  not not_35 (not_35_out, OP5);
  not not_36 (not_36_out, OP3);
  not not_37 (not_37_out, OP2);
  not not_38 (not_38_out, F14);
  not not_39 (not_39_out, F12);
  not not_40 (not_40_out, OP6);
  not not_41 (not_41_out, OP5);
  not not_42 (not_42_out, OP3);
  not not_43 (not_43_out, OP2);
  not not_44 (not_44_out, F25);
  not not_45 (not_45_out, F13);
  not not_46 (not_46_out, OP6);
  not not_47 (not_47_out, OP5);
  not not_48 (not_48_out, OP3);
  not not_49 (not_49_out, OP2);
  not not_50 (not_50_out, F14);
  not not_51 (not_51_out, F12);
  not not_52 (not_52_out, OP6);
  not not_53 (not_53_out, OP5);
  not not_54 (not_54_out, OP4);
  not not_55 (not_55_out, OP3);
  not not_56 (not_56_out, OP2);
  not not_57 (not_57_out, F14);
  not not_58 (not_58_out, F12);
  not not_59 (not_59_out, OP6);
  not not_60 (not_60_out, OP4);
  not not_61 (not_61_out, OP3);
  not not_62 (not_62_out, OP2);
  not not_63 (not_63_out, F14);
  not not_64 (not_64_out, F13);
  not not_65 (not_65_out, F12);
  not not_66 (not_66_out, OP4);
  not not_67 (not_67_out, OP3);
  not not_68 (not_68_out, F13);
  not not_69 (not_69_out, F12);
  not not_70 (not_70_out, OP6);
  not not_71 (not_71_out, OP5);
  not not_72 (not_72_out, OP4);
  not not_73 (not_73_out, OP3);
  not not_74 (not_74_out, OP2);
  not not_75 (not_75_out, F25);
  not not_76 (not_76_out, F14);
  not not_77 (not_77_out, F13);
  not not_78 (not_78_out, F12);
  not not_79 (not_79_out, OP6);
  not not_80 (not_80_out, OP3);
  not not_81 (not_81_out, OP2);
  not not_82 (not_82_out, F30);
  not not_83 (not_83_out, F25);
  not not_84 (not_84_out, OP6);
  not not_85 (not_85_out, OP3);
  not not_86 (not_86_out, OP2);
  not not_87 (not_87_out, F30);
  not not_88 (not_88_out, F25);
  not not_89 (not_89_out, F14);
  not not_90 (not_90_out, F12);
  not not_91 (not_91_out, OP6);
  not not_92 (not_92_out, OP3);
  not not_93 (not_93_out, OP2);
  not not_94 (not_94_out, OP6);
  not not_95 (not_95_out, OP5);
  not not_96 (not_96_out, OP3);
  not not_97 (not_97_out, OP2);
  not not_98 (not_98_out, F14);
  not not_99 (not_99_out, F12);
  not not_100 (not_100_out, OP6);
  not not_101 (not_101_out, OP5);
  not not_102 (not_102_out, OP3);
  not not_103 (not_103_out, OP2);
  not not_104 (not_104_out, F30);
  not not_105 (not_105_out, F25);
  not not_106 (not_106_out, F13);
  not not_107 (not_107_out, OP6);
  not not_108 (not_108_out, OP5);
  not not_109 (not_109_out, OP3);
  not not_110 (not_110_out, OP2);
  not not_111 (not_111_out, F30);
  not not_112 (not_112_out, F25);
  not not_113 (not_113_out, F14);
  not not_114 (not_114_out, F13);
  not not_115 (not_115_out, F12);
  not not_116 (not_116_out, OP6);
  not not_117 (not_117_out, OP3);
  not not_118 (not_118_out, OP2);
  not not_119 (not_119_out, F25);
  not not_120 (not_120_out, F14);
  not not_121 (not_121_out, F13);
  not not_122 (not_122_out, F12);
  not not_123 (not_123_out, OP6);
  not not_124 (not_124_out, OP3);
  not not_125 (not_125_out, OP2);
  not not_126 (not_126_out, F30);
  not not_127 (not_127_out, F25);
  not not_128 (not_128_out, OP6);
  not not_129 (not_129_out, OP3);
  not not_130 (not_130_out, OP2);
  not not_131 (not_131_out, F30);
  not not_132 (not_132_out, F25);
  not not_133 (not_133_out, F14);
  not not_134 (not_134_out, OP6);
  not not_135 (not_135_out, OP3);
  not not_136 (not_136_out, OP2);
  not not_137 (not_137_out, F14);
  not not_138 (not_138_out, F13);
  not not_139 (not_139_out, F12);
  not not_140 (not_140_out, OP6);
  not not_141 (not_141_out, OP5);
  not not_142 (not_142_out, OP3);
  not not_143 (not_143_out, OP2);
  not not_144 (not_144_out, OP6);
  not not_145 (not_145_out, OP5);
  not not_146 (not_146_out, OP3);
  not not_147 (not_147_out, OP2);
  not not_148 (not_148_out, F14);
  not not_149 (not_149_out, F12);
  not not_150 (not_150_out, OP6);
  not not_151 (not_151_out, OP5);
  not not_152 (not_152_out, OP4);
  not not_153 (not_153_out, OP3);
  not not_154 (not_154_out, OP2);
  not not_155 (not_155_out, F14);
  not not_156 (not_156_out, F12);
  not not_157 (not_157_out, OP6);
  not not_158 (not_158_out, OP4);
  not not_159 (not_159_out, OP3);
  not not_160 (not_160_out, OP2);
  not not_161 (not_161_out, F14);
  not not_162 (not_162_out, F13);
  not not_163 (not_163_out, F12);
  not not_164 (not_164_out, OP4);
  not not_165 (not_165_out, OP3);
  not not_166 (not_166_out, F14);
  not not_167 (not_167_out, OP6);
  not not_168 (not_168_out, OP5);
  not not_169 (not_169_out, OP3);
  not not_170 (not_170_out, OP2);
  not not_171 (not_171_out, F13);
  not not_172 (not_172_out, F12);
  not not_173 (not_173_out, OP6);
  not not_174 (not_174_out, OP5);
  not not_175 (not_175_out, OP4);
  not not_176 (not_176_out, OP3);
  not not_177 (not_177_out, OP2);
  not not_178 (not_178_out, F12);
  not not_179 (not_179_out, OP4);
  not not_180 (not_180_out, OP3);
  not not_181 (not_181_out, OP2);
  not not_182 (not_182_out, F30);
  not not_183 (not_183_out, F25);
  not not_184 (not_184_out, F12);
  not not_185 (not_185_out, OP6);
  not not_186 (not_186_out, OP3);
  not not_187 (not_187_out, OP2);
  not not_188 (not_188_out, F30);
  not not_189 (not_189_out, F25);
  not not_190 (not_190_out, F14);
  not not_191 (not_191_out, F12);
  not not_192 (not_192_out, OP6);
  not not_193 (not_193_out, OP3);
  not not_194 (not_194_out, OP2);
  not not_195 (not_195_out, F30);
  not not_196 (not_196_out, F25);
  not not_197 (not_197_out, F14);
  not not_198 (not_198_out, OP6);
  not not_199 (not_199_out, OP3);
  not not_200 (not_200_out, OP2);
  not not_201 (not_201_out, F12);
  not not_202 (not_202_out, OP6);
  not not_203 (not_203_out, OP5);
  not not_204 (not_204_out, OP3);
  not not_205 (not_205_out, OP2);
  not not_206 (not_206_out, F13);
  not not_207 (not_207_out, F12);
  not not_208 (not_208_out, OP6);
  not not_209 (not_209_out, OP5);
  not not_210 (not_210_out, OP3);
  not not_211 (not_211_out, OP2);
  not not_212 (not_212_out, F14);
  not not_213 (not_213_out, F12);
  not not_214 (not_214_out, OP6);
  not not_215 (not_215_out, OP5);
  not not_216 (not_216_out, OP3);
  not not_217 (not_217_out, OP2);
  not not_218 (not_218_out, F14);
  not not_219 (not_219_out, OP6);
  not not_220 (not_220_out, OP5);
  not not_221 (not_221_out, OP3);
  not not_222 (not_222_out, OP2);
  not not_223 (not_223_out, F12);
  not not_224 (not_224_out, OP4);
  not not_225 (not_225_out, OP3);
  not not_226 (not_226_out, OP2);
  and and_1 (and_1_out, not_1_out, not_2_out, not_3_out, not_4_out, not_5_out, not_6_out, OP5, OP4, not_7_out, not_8_out);
  and and_2 (and_2_out, not_9_out, not_10_out, F14, F13, F12, not_11_out, OP5, OP4, not_12_out, not_13_out);
  and and_3 (and_3_out, not_14_out, not_15_out, not_16_out, F13, not_17_out, not_18_out, OP5, OP4, not_19_out, not_20_out);
  and and_4 (and_4_out, not_21_out, not_22_out, not_23_out, not_24_out, not_25_out, OP4, not_26_out, not_27_out);
  and and_5 (and_5_out, F14, F13, F12, not_28_out, not_29_out, OP4, not_30_out, not_31_out);
  and and_6 (and_6_out, F14, not_32_out, not_33_out, not_34_out, not_35_out, OP4, not_36_out, not_37_out);
  and and_7 (and_7_out, not_38_out, F13, not_39_out, not_40_out, not_41_out, OP4, not_42_out, not_43_out);
  and and_8 (and_8_out, F30, not_44_out, F14, not_45_out, F12, not_46_out, not_47_out, OP4, not_48_out, not_49_out);
  and and_9 (and_9_out, not_50_out, F13, not_51_out, not_52_out, not_53_out, not_54_out, not_55_out, not_56_out);
  and and_10 (and_10_out, not_57_out, F13, not_58_out, not_59_out, OP5, not_60_out, not_61_out, not_62_out);
  and and_11 (and_11_out, not_63_out, not_64_out, not_65_out, OP6, OP5, not_66_out, not_67_out, OP2);
  and and_12 (and_12_out, F14, not_68_out, not_69_out, not_70_out, not_71_out, not_72_out, not_73_out, not_74_out);
  and and_13 (and_13_out, F30, not_75_out, not_76_out, not_77_out, not_78_out, not_79_out, OP5, OP4, not_80_out, not_81_out);
  and and_14 (and_14_out, not_82_out, not_83_out, F14, F13, F12, not_84_out, OP5, OP4, not_85_out, not_86_out);
  and and_15 (and_15_out, not_87_out, not_88_out, not_89_out, F13, not_90_out, not_91_out, OP5, OP4, not_92_out, not_93_out);
  and and_16 (and_16_out, F14, F13, F12, not_94_out, not_95_out, OP4, not_96_out, not_97_out);
  and and_17 (and_17_out, not_98_out, F13, not_99_out, not_100_out, not_101_out, OP4, not_102_out, not_103_out);
  and and_18 (and_18_out, not_104_out, not_105_out, F14, not_106_out, F12, not_107_out, not_108_out, OP4, not_109_out, not_110_out);
  and and_19 (and_19_out, not_111_out, not_112_out, not_113_out, not_114_out, not_115_out, not_116_out, OP5, OP4, not_117_out, not_118_out);
  and and_20 (and_20_out, F30, not_119_out, not_120_out, not_121_out, not_122_out, not_123_out, OP5, OP4, not_124_out, not_125_out);
  and and_21 (and_21_out, not_126_out, not_127_out, F14, F13, F12, not_128_out, OP5, OP4, not_129_out, not_130_out);
  and and_22 (and_22_out, not_131_out, not_132_out, not_133_out, F13, F12, not_134_out, OP5, OP4, not_135_out, not_136_out);
  and and_23 (and_23_out, not_137_out, not_138_out, not_139_out, not_140_out, not_141_out, OP4, not_142_out, not_143_out);
  and and_24 (and_24_out, F14, F13, F12, not_144_out, not_145_out, OP4, not_146_out, not_147_out);
  and and_25 (and_25_out, not_148_out, F13, not_149_out, not_150_out, not_151_out, not_152_out, not_153_out, not_154_out);
  and and_26 (and_26_out, not_155_out, F13, not_156_out, not_157_out, OP5, not_158_out, not_159_out, not_160_out);
  and and_27 (and_27_out, not_161_out, not_162_out, not_163_out, OP6, OP5, not_164_out, not_165_out, OP2);
  and and_28 (and_28_out, not_166_out, F13, F12, not_167_out, not_168_out, OP4, not_169_out, not_170_out);
  and and_29 (and_29_out, F14, not_171_out, not_172_out, not_173_out, not_174_out, not_175_out, not_176_out, not_177_out);
  and and_30 (and_30_out, F14, F13, not_178_out, OP6, OP5, not_179_out, not_180_out, not_181_out);
  and and_31 (and_31_out, not_182_out, not_183_out, F14, F13, not_184_out, not_185_out, OP5, OP4, not_186_out, not_187_out);
  and and_32 (and_32_out, not_188_out, not_189_out, not_190_out, F13, not_191_out, not_192_out, OP5, OP4, not_193_out, not_194_out);
  and and_33 (and_33_out, not_195_out, not_196_out, not_197_out, F13, F12, not_198_out, OP5, OP4, not_199_out, not_200_out);
  and and_34 (and_34_out, F14, F13, not_201_out, not_202_out, not_203_out, OP4, not_204_out, not_205_out);
  and and_35 (and_35_out, F14, not_206_out, not_207_out, not_208_out, not_209_out, OP4, not_210_out, not_211_out);
  and and_36 (and_36_out, not_212_out, F13, not_213_out, not_214_out, not_215_out, OP4, not_216_out, not_217_out);
  and and_37 (and_37_out, not_218_out, F13, F12, not_219_out, not_220_out, OP4, not_221_out, not_222_out);
  and and_38 (and_38_out, F14, F13, not_223_out, OP6, OP5, not_224_out, not_225_out, not_226_out);
  or or_1 (S0, and_1_out, and_2_out, and_3_out, and_4_out, and_5_out, and_6_out, and_7_out, and_8_out, and_9_out, and_10_out, and_11_out, and_12_out);
  or or_2 (S1, and_13_out, and_14_out, and_15_out, and_16_out, and_17_out, and_18_out);
  or or_3 (S2, and_19_out, and_20_out, and_21_out, and_22_out, and_23_out, and_24_out, and_25_out, and_26_out, and_27_out, and_28_out, and_29_out, and_30_out);
  or or_4 (S3, and_31_out, and_32_out, and_33_out, and_34_out, and_35_out, and_36_out, and_37_out, and_38_out);
endmodule

// 控制信号生成
module \控制信号自动生成  (
  input  OP2,
  input  OP3,
  input  OP4,
  input  OP5,
  input  OP6,
  input  F12,
  input  F13,
  input  F14,
  input  F25,
  input  F30,
  output MemToReg,
  output MemWrite,
  output ALU_SRC,
  output RegWrite,
  output ecall,
  output S_Type,
  output BEQ,
  output BNE,
  output JALR,
  output JAL,
  output lbu,
  output bltu,
  output Rs1Used,
  output Rs2Used,
  output csrrsi,
  output csrrci
);

  wire and_1_out, and_2_out, and_4_out, and_5_out, and_6_out, and_7_out, and_8_out, and_9_out, and_10_out,
       and_11_out, and_12_out, and_13_out, and_14_out, and_15_out, and_16_out, and_17_out, and_18_out,
       and_19_out, and_20_out, and_29_out, and_30_out, and_31_out, and_32_out, and_33_out, and_34_out,
       and_35_out, and_36_out, and_37_out, and_38_out, and_39_out, and_40_out, and_41_out, and_42_out,
       and_43_out, and_44_out, and_45_out, not_1_out, not_2_out, not_3_out, not_4_out, not_5_out, not_6_out,
       not_7_out, not_8_out, not_9_out, not_10_out, not_11_out, not_12_out, not_13_out, not_14_out,
       not_15_out, not_16_out, not_17_out, not_18_out, not_19_out, not_20_out, not_21_out, not_22_out,
       not_23_out, not_24_out, not_25_out, not_26_out, not_27_out, not_28_out, not_29_out, not_30_out,
       not_31_out, not_32_out, not_33_out, not_34_out, not_35_out, not_36_out, not_37_out, not_38_out,
       not_39_out, not_40_out, not_41_out, not_42_out, not_43_out, not_44_out, not_45_out, not_46_out,
       not_47_out, not_48_out, not_49_out, not_50_out, not_51_out, not_52_out, not_53_out, not_54_out,
       not_55_out, not_56_out, not_57_out, not_58_out, not_59_out, not_60_out, not_61_out, not_62_out,
       not_63_out, not_64_out, not_65_out, not_66_out, not_67_out, not_68_out, not_69_out, not_70_out,
       not_71_out, not_72_out, not_73_out, not_74_out, not_75_out, not_76_out, not_77_out, not_78_out,
       not_79_out, not_80_out, not_81_out, not_82_out, not_83_out, not_84_out, not_85_out, not_86_out,
       not_87_out, not_88_out, not_89_out, not_90_out, not_91_out, not_92_out, not_93_out, not_94_out,
       not_95_out, not_96_out, not_97_out, not_98_out, not_99_out, not_100_out, not_101_out, not_102_out,
       not_103_out, not_104_out, not_105_out, not_106_out, not_107_out, not_108_out, not_109_out,
       not_110_out, not_111_out, not_112_out, not_113_out, not_114_out, not_115_out, not_116_out,
       not_117_out, not_118_out, not_119_out, not_120_out, not_121_out, not_122_out, not_123_out,
       not_124_out, not_125_out, not_126_out, not_127_out, not_128_out, not_129_out, not_130_out,
       not_131_out, not_132_out, not_133_out, not_134_out, not_135_out, not_136_out, not_137_out,
       not_138_out, not_139_out, not_140_out, not_141_out, not_142_out, not_143_out, not_144_out,
       not_145_out, not_146_out, not_147_out, not_148_out, not_149_out, not_150_out, not_151_out,
       not_152_out, not_153_out, not_154_out, not_155_out, not_156_out, not_157_out, not_158_out,
       not_159_out, not_160_out, not_161_out, not_162_out, not_163_out, not_164_out, not_165_out,
       not_166_out, not_167_out, not_168_out, not_169_out, not_170_out, not_171_out, not_172_out,
       not_173_out, not_174_out, not_175_out, not_176_out, not_177_out, not_178_out, not_179_out,
       not_180_out, not_181_out, not_182_out, not_183_out, not_184_out, not_185_out, not_186_out,
       not_187_out, not_188_out, not_189_out, not_190_out, not_191_out, not_192_out, not_193_out,
       not_194_out, not_195_out, not_196_out, not_197_out, not_198_out, not_199_out, not_200_out,
       not_201_out, not_202_out, not_203_out, not_204_out, not_205_out, not_206_out, not_207_out,
       not_208_out, not_209_out, not_210_out, not_211_out, not_212_out, not_213_out, not_214_out,
       not_215_out, not_216_out, not_217_out, not_218_out, not_219_out, not_220_out, not_221_out,
       not_222_out, not_223_out, not_224_out, not_225_out, not_226_out, not_227_out, not_228_out,
       not_229_out, not_230_out, not_231_out, not_232_out, not_233_out, not_234_out, not_235_out,
       not_236_out, not_237_out, not_238_out, not_239_out, not_240_out, not_241_out, not_242_out, not_243_out;

  not not_1 (not_1_out, OP2);
  not not_2 (not_2_out, OP3);
  not not_3 (not_3_out, OP4);
  not not_4 (not_4_out, OP5);
  not not_5 (not_5_out, OP6);
  not not_6 (not_6_out, F12);
  not not_7 (not_7_out, F13);
  not not_8 (not_8_out, OP2);
  not not_9 (not_9_out, OP3);
  not not_10 (not_10_out, OP4);
  not not_11 (not_11_out, OP5);
  not not_12 (not_12_out, OP6);
  not not_13 (not_13_out, F12);
  not not_14 (not_14_out, F14);
  not not_15 (not_15_out, OP2);
  not not_16 (not_16_out, OP3);
  not not_17 (not_17_out, OP4);
  not not_18 (not_18_out, OP6);
  not not_19 (not_19_out, F12);
  not not_20 (not_20_out, F14);
  not not_21 (not_21_out, OP2);
  not not_22 (not_22_out, OP3);
  not not_23 (not_23_out, OP5);
  not not_24 (not_24_out, OP6);
  not not_25 (not_25_out, F12);
  not not_26 (not_26_out, F13);
  not not_27 (not_27_out, OP2);
  not not_28 (not_28_out, OP3);
  not not_29 (not_29_out, OP4);
  not not_30 (not_30_out, OP6);
  not not_31 (not_31_out, F12);
  not not_32 (not_32_out, F14);
  not not_33 (not_33_out, OP2);
  not not_34 (not_34_out, OP3);
  not not_35 (not_35_out, OP5);
  not not_36 (not_36_out, OP6);
  not not_37 (not_37_out, F12);
  not not_38 (not_38_out, OP2);
  not not_39 (not_39_out, OP3);
  not not_40 (not_40_out, OP5);
  not not_41 (not_41_out, OP6);
  not not_42 (not_42_out, F25);
  not not_43 (not_43_out, F30);
  not not_44 (not_44_out, OP2);
  not not_45 (not_45_out, OP3);
  not not_46 (not_46_out, OP5);
  not not_47 (not_47_out, OP6);
  not not_48 (not_48_out, F25);
  not not_49 (not_49_out, OP2);
  not not_50 (not_50_out, OP3);
  not not_51 (not_51_out, OP5);
  not not_52 (not_52_out, OP6);
  not not_53 (not_53_out, OP3);
  not not_54 (not_54_out, OP4);
  not not_55 (not_55_out, F12);
  not not_56 (not_56_out, F13);
  not not_57 (not_57_out, F14);
  not not_58 (not_58_out, OP2);
  not not_59 (not_59_out, OP3);
  not not_60 (not_60_out, OP5);
  not not_61 (not_61_out, OP6);
  not not_62 (not_62_out, F12);
  not not_63 (not_63_out, F13);
  not not_64 (not_64_out, OP2);
  not not_65 (not_65_out, OP3);
  not not_66 (not_66_out, OP5);
  not not_67 (not_67_out, OP6);
  not not_68 (not_68_out, F12);
  not not_69 (not_69_out, F14);
  not not_70 (not_70_out, OP2);
  not not_71 (not_71_out, OP3);
  not not_72 (not_72_out, OP5);
  not not_73 (not_73_out, OP6);
  not not_74 (not_74_out, F12);
  not not_75 (not_75_out, OP2);
  not not_76 (not_76_out, OP3);
  not not_77 (not_77_out, OP6);
  not not_78 (not_78_out, F12);
  not not_79 (not_79_out, F13);
  not not_80 (not_80_out, F14);
  not not_81 (not_81_out, F25);
  not not_82 (not_82_out, OP2);
  not not_83 (not_83_out, OP3);
  not not_84 (not_84_out, OP6);
  not not_85 (not_85_out, F14);
  not not_86 (not_86_out, F25);
  not not_87 (not_87_out, F30);
  not not_88 (not_88_out, OP2);
  not not_89 (not_89_out, OP3);
  not not_90 (not_90_out, OP5);
  not not_91 (not_91_out, OP6);
  not not_92 (not_92_out, F25);
  not not_93 (not_93_out, OP2);
  not not_94 (not_94_out, OP3);
  not not_95 (not_95_out, OP5);
  not not_96 (not_96_out, OP6);
  not not_97 (not_97_out, OP2);
  not not_98 (not_98_out, OP3);
  not not_99 (not_99_out, OP6);
  not not_100 (not_100_out, F25);
  not not_101 (not_101_out, F30);
  not not_102 (not_102_out, OP4);
  not not_103 (not_103_out, F12);
  not not_104 (not_104_out, F13);
  not not_105 (not_105_out, F14);
  not not_106 (not_106_out, OP4);
  not not_107 (not_107_out, OP2);
  not not_108 (not_108_out, OP3);
  not not_109 (not_109_out, F12);
  not not_110 (not_110_out, F13);
  not not_111 (not_111_out, F14);
  not not_112 (not_112_out, F25);
  not not_113 (not_113_out, F30);
  not not_114 (not_114_out, OP2);
  not not_115 (not_115_out, OP3);
  not not_116 (not_116_out, OP4);
  not not_117 (not_117_out, OP6);
  not not_118 (not_118_out, F12);
  not not_119 (not_119_out, F14);
  not not_120 (not_120_out, OP2);
  not not_121 (not_121_out, OP3);
  not not_122 (not_122_out, OP4);
  not not_123 (not_123_out, F12);
  not not_124 (not_124_out, F13);
  not not_125 (not_125_out, F14);
  not not_126 (not_126_out, OP2);
  not not_127 (not_127_out, OP3);
  not not_128 (not_128_out, OP4);
  not not_129 (not_129_out, F13);
  not not_130 (not_130_out, F14);
  not not_131 (not_131_out, OP3);
  not not_132 (not_132_out, OP4);
  not not_133 (not_133_out, F12);
  not not_134 (not_134_out, F13);
  not not_135 (not_135_out, F14);
  not not_136 (not_136_out, OP4);
  not not_137 (not_137_out, OP2);
  not not_138 (not_138_out, OP3);
  not not_139 (not_139_out, OP4);
  not not_140 (not_140_out, OP5);
  not not_141 (not_141_out, OP6);
  not not_142 (not_142_out, F12);
  not not_143 (not_143_out, F13);
  not not_144 (not_144_out, OP2);
  not not_145 (not_145_out, OP3);
  not not_146 (not_146_out, OP4);
  not not_147 (not_147_out, F12);
  not not_148 (not_148_out, OP2);
  not not_149 (not_149_out, OP3);
  not not_150 (not_150_out, OP5);
  not not_151 (not_151_out, OP6);
  not not_152 (not_152_out, F12);
  not not_153 (not_153_out, F13);
  not not_154 (not_154_out, OP2);
  not not_155 (not_155_out, OP3);
  not not_156 (not_156_out, OP4);
  not not_157 (not_157_out, OP6);
  not not_158 (not_158_out, F12);
  not not_159 (not_159_out, F14);
  not not_160 (not_160_out, OP2);
  not not_161 (not_161_out, OP3);
  not not_162 (not_162_out, OP4);
  not not_163 (not_163_out, F13);
  not not_164 (not_164_out, F14);
  not not_165 (not_165_out, OP3);
  not not_166 (not_166_out, OP4);
  not not_167 (not_167_out, F12);
  not not_168 (not_168_out, F13);
  not not_169 (not_169_out, F14);
  not not_170 (not_170_out, OP2);
  not not_171 (not_171_out, OP3);
  not not_172 (not_172_out, OP4);
  not not_173 (not_173_out, F12);
  not not_174 (not_174_out, OP2);
  not not_175 (not_175_out, OP3);
  not not_176 (not_176_out, OP5);
  not not_177 (not_177_out, OP6);
  not not_178 (not_178_out, F12);
  not not_179 (not_179_out, OP2);
  not not_180 (not_180_out, OP3);
  not not_181 (not_181_out, OP6);
  not not_182 (not_182_out, F12);
  not not_183 (not_183_out, F13);
  not not_184 (not_184_out, F14);
  not not_185 (not_185_out, F25);
  not not_186 (not_186_out, OP2);
  not not_187 (not_187_out, OP3);
  not not_188 (not_188_out, OP6);
  not not_189 (not_189_out, F14);
  not not_190 (not_190_out, F25);
  not not_191 (not_191_out, F30);
  not not_192 (not_192_out, OP2);
  not not_193 (not_193_out, OP3);
  not not_194 (not_194_out, OP5);
  not not_195 (not_195_out, OP6);
  not not_196 (not_196_out, F25);
  not not_197 (not_197_out, OP2);
  not not_198 (not_198_out, OP3);
  not not_199 (not_199_out, OP5);
  not not_200 (not_200_out, OP6);
  not not_201 (not_201_out, OP2);
  not not_202 (not_202_out, OP3);
  not not_203 (not_203_out, OP6);
  not not_204 (not_204_out, F25);
  not not_205 (not_205_out, F30);
  not not_206 (not_206_out, OP2);
  not not_207 (not_207_out, OP3);
  not not_208 (not_208_out, OP4);
  not not_209 (not_209_out, OP6);
  not not_210 (not_210_out, F12);
  not not_211 (not_211_out, F14);
  not not_212 (not_212_out, OP2);
  not not_213 (not_213_out, OP3);
  not not_214 (not_214_out, OP4);
  not not_215 (not_215_out, F13);
  not not_216 (not_216_out, F14);
  not not_217 (not_217_out, OP2);
  not not_218 (not_218_out, OP3);
  not not_219 (not_219_out, OP4);
  not not_220 (not_220_out, F12);
  not not_221 (not_221_out, OP2);
  not not_222 (not_222_out, OP3);
  not not_223 (not_223_out, OP6);
  not not_224 (not_224_out, F12);
  not not_225 (not_225_out, F13);
  not not_226 (not_226_out, F14);
  not not_227 (not_227_out, F25);
  not not_228 (not_228_out, OP2);
  not not_229 (not_229_out, OP3);
  not not_230 (not_230_out, OP6);
  not not_231 (not_231_out, F14);
  not not_232 (not_232_out, F25);
  not not_233 (not_233_out, F30);
  not not_234 (not_234_out, OP2);
  not not_235 (not_235_out, OP3);
  not not_236 (not_236_out, OP6);
  not not_237 (not_237_out, F25);
  not not_238 (not_238_out, F30);
  not not_239 (not_239_out, F12);
  not not_240 (not_240_out, OP3);
  not not_241 (not_241_out, OP2);
  not not_242 (not_242_out, OP3);
  not not_243 (not_243_out, OP2);
  and and_1 (and_1_out, not_1_out, not_2_out, not_3_out, not_4_out, not_5_out, not_6_out, not_7_out, F14);
  and and_2 (and_2_out, not_8_out, not_9_out, not_10_out, not_11_out, not_12_out, not_13_out, F13, not_14_out);
  and and_3 (MemWrite, not_15_out, not_16_out, not_17_out, OP5, not_18_out, not_19_out, F13, not_20_out);
  and and_4 (and_4_out, not_21_out, not_22_out, not_23_out, not_24_out, not_25_out, not_26_out, F14);
  and and_5 (and_5_out, not_27_out, not_28_out, not_29_out, not_30_out, not_31_out, F13, not_32_out);
  and and_6 (and_6_out, not_33_out, not_34_out, OP4, not_35_out, not_36_out, not_37_out);
  and and_7 (and_7_out, not_38_out, not_39_out, OP4, not_40_out, not_41_out, not_42_out, not_43_out);
  and and_8 (and_8_out, not_44_out, not_45_out, OP4, not_46_out, not_47_out, F14, not_48_out);
  and and_9 (and_9_out, not_49_out, not_50_out, OP4, not_51_out, not_52_out, F13);
  and and_10 (and_10_out, OP2, not_53_out, not_54_out, OP5, OP6, not_55_out, not_56_out, not_57_out);
  and and_11 (and_11_out, not_58_out, not_59_out, not_60_out, not_61_out, not_62_out, not_63_out, F14);
  and and_12 (and_12_out, not_64_out, not_65_out, not_66_out, not_67_out, not_68_out, F13, not_69_out);
  and and_13 (and_13_out, not_70_out, not_71_out, OP4, not_72_out, not_73_out, not_74_out);
  and and_14 (and_14_out, not_75_out, not_76_out, OP4, not_77_out, not_78_out, not_79_out, not_80_out, not_81_out);
  and and_15 (and_15_out, not_82_out, not_83_out, OP4, not_84_out, not_85_out, not_86_out, not_87_out);
  and and_16 (and_16_out, not_88_out, not_89_out, OP4, not_90_out, not_91_out, F14, not_92_out);
  and and_17 (and_17_out, not_93_out, not_94_out, OP4, not_95_out, not_96_out, F13);
  and and_18 (and_18_out, not_97_out, not_98_out, OP4, not_99_out, F13, not_100_out, not_101_out);
  and and_19 (and_19_out, OP2, not_102_out, OP5, OP6, not_103_out, not_104_out, not_105_out);
  and and_20 (and_20_out, OP2, OP3, not_106_out, OP5, OP6);
  and and_21 (ecall, not_107_out, not_108_out, OP4, OP5, OP6, not_109_out, not_110_out, not_111_out, not_112_out, not_113_out);
  and and_22 (S_Type, not_114_out, not_115_out, not_116_out, OP5, not_117_out, not_118_out, F13, not_119_out);
  and and_23 (BEQ, not_120_out, not_121_out, not_122_out, OP5, OP6, not_123_out, not_124_out, not_125_out);
  and and_24 (BNE, not_126_out, not_127_out, not_128_out, OP5, OP6, F12, not_129_out, not_130_out);
  and and_25 (JALR, OP2, not_131_out, not_132_out, OP5, OP6, not_133_out, not_134_out, not_135_out);
  and and_26 (JAL, OP2, OP3, not_136_out, OP5, OP6);
  and and_27 (lbu, not_137_out, not_138_out, not_139_out, not_140_out, not_141_out, not_142_out, not_143_out, F14);
  and and_28 (bltu, not_144_out, not_145_out, not_146_out, OP5, OP6, not_147_out, F13, F14);
  and and_29 (and_29_out, not_148_out, not_149_out, not_150_out, not_151_out, not_152_out, not_153_out, F14);
  and and_30 (and_30_out, not_154_out, not_155_out, not_156_out, not_157_out, not_158_out, F13, not_159_out);
  and and_31 (and_31_out, not_160_out, not_161_out, not_162_out, OP5, OP6, not_163_out, not_164_out);
  and and_32 (and_32_out, not_165_out, not_166_out, OP5, OP6, not_167_out, not_168_out, not_169_out);
  and and_33 (and_33_out, not_170_out, not_171_out, not_172_out, OP5, OP6, not_173_out, F13, F14);
  and and_34 (and_34_out, not_174_out, not_175_out, OP4, not_176_out, not_177_out, not_178_out);
  and and_35 (and_35_out, not_179_out, not_180_out, OP4, not_181_out, not_182_out, not_183_out, not_184_out, not_185_out);
  and and_36 (and_36_out, not_186_out, not_187_out, OP4, not_188_out, not_189_out, not_190_out, not_191_out);
  and and_37 (and_37_out, not_192_out, not_193_out, OP4, not_194_out, not_195_out, F14, not_196_out);
  and and_38 (and_38_out, not_197_out, not_198_out, OP4, not_199_out, not_200_out, F13);
  and and_39 (and_39_out, not_201_out, not_202_out, OP4, not_203_out, F13, not_204_out, not_205_out);
  and and_40 (and_40_out, not_206_out, not_207_out, not_208_out, OP5, not_209_out, not_210_out, F13, not_211_out);
  and and_41 (and_41_out, not_212_out, not_213_out, not_214_out, OP5, OP6, not_215_out, not_216_out);
  and and_42 (and_42_out, not_217_out, not_218_out, not_219_out, OP5, OP6, not_220_out, F13, F14);
  and and_43 (and_43_out, not_221_out, not_222_out, OP4, OP5, not_223_out, not_224_out, not_225_out, not_226_out, not_227_out);
  and and_44 (and_44_out, not_228_out, not_229_out, OP4, OP5, not_230_out, not_231_out, not_232_out, not_233_out);
  and and_45 (and_45_out, not_234_out, not_235_out, OP4, OP5, not_236_out, F13, not_237_out, not_238_out);
  and and_46 (csrrsi, F14, F13, not_239_out, OP6, OP5, OP4, not_240_out, not_241_out);
  and and_47 (csrrci, F14, F13, F12, OP6, OP5, OP4, not_242_out, not_243_out);
  or or_1 (MemToReg, and_1_out, and_2_out);
  or or_2 (ALU_SRC, and_4_out, and_5_out, and_6_out, and_7_out, and_8_out, and_9_out, and_10_out);
  or or_3 (Rs2Used, and_40_out, and_41_out, and_42_out, and_43_out, and_44_out, and_45_out);
  or or_4 (RegWrite, and_11_out, and_12_out, and_13_out, and_14_out, and_15_out, and_16_out, and_17_out, and_18_out, and_19_out, and_20_out);
  or or_5 (Rs1Used, and_29_out, and_30_out, and_31_out, and_32_out, and_33_out, and_34_out, and_35_out, and_36_out, and_37_out, and_38_out, and_39_out);
endmodule

// ALU
module ALU (
  input  [31:0] X,
  input  [31:0] Y,
  input  [3:0] AluOP,
  output out_4,
  output Equal,
  output out_6,
  output [31:0] Result,
  output [31:0] Result_2
);

  wire [0:0] comparator_1_lt, comparator_2_lt;
  wire [31:0] adder_1_out, AND_out, divider_1_out, divider_1_rem, multiplier_1_cout, multiplier_1_out,
       NOR_out, OR_out, shifter_1_out, shifter_2_out, shifter_3_out, subtractor_1_out, XOR_out;

  assign AND_out = X & Y;  // AND_Gate AND, 32 bits wide
  assign OR_out = X | Y;  // OR_Gate OR, 32 bits wide
  Shifter #(.width(32), .shift("ll")) shifter_1 (.in(X), .\dist (Y[4:0]), .out(shifter_1_out));
  Shifter #(.width(32), .shift("ar")) shifter_2 (.in(X), .\dist (Y[4:0]), .out(shifter_2_out));
  Shifter #(.width(32), .shift("lr")) shifter_3 (.in(X), .\dist (Y[4:0]), .out(shifter_3_out));
  Multiplier #(.width(32)) multiplier_1 (.a(X), .b(Y), .out(multiplier_1_out), .cout(multiplier_1_cout));  // open: cin
  Divider #(.width(32)) divider_1 (.a(X), .b(Y), .out(divider_1_out), .rem(divider_1_rem));  // open: upper
  Adder #(.width(32)) adder_1 (.a(X), .b(Y), .out(adder_1_out));  // open: cin, cout
  Subtractor #(.width(32)) subtractor_1 (.a(X), .b(Y), .out(subtractor_1_out));  // open: bin, bout
  assign XOR_out = X ^ Y;  // XOR_Gate XOR, 32 bits wide
  assign NOR_out = ~(X | Y);  // NOR_Gate NOR, 32 bits wide
  Comparator #(.width(32), .mode("twosComplement")) comparator_1 (
    .a(X), .b(Y), .eq(Equal), .lt(comparator_1_lt[0]));  // open: gt
  Comparator #(.width(32), .mode("unsigned")) comparator_2 (.a(X), .b(Y), .lt(comparator_2_lt[0]));  // open: gt, eq
  Multiplexer #(.select(4), .width(32), .disabled("Z"), .enable("false")) multiplexer_1 (
    .in0(shifter_1_out), .in1(shifter_2_out), .in2(shifter_3_out), .in3(multiplier_1_out),
    .in4(divider_1_out), .in5(adder_1_out), .in6(subtractor_1_out), .in7(AND_out), .in8(OR_out),
    .in9(XOR_out), .in10(NOR_out), .in11({{31{1'b0}}, comparator_1_lt[0]}),
    .in12({{31{1'b0}}, comparator_2_lt[0]}), .in13({32{1'b0}}), .in14({32{1'b0}}), .in15({32{1'b0}}),
    .out(Result), .sel(AluOP));
  Multiplexer #(.select(4), .width(32), .disabled("Z"), .enable("false")) multiplexer_2 (
    .in0({32{1'b0}}), .in1({32{1'b0}}), .in2({32{1'b0}}), .in3(multiplier_1_cout), .in4(divider_1_rem),
    .in5({32{1'b0}}), .in6({32{1'b0}}), .in7({32{1'b0}}), .in8({32{1'b0}}), .in9({32{1'b0}}),
    .in10({32{1'b0}}), .in11({32{1'b0}}), .in12({32{1'b0}}), .in13({32{1'b0}}), .in14({32{1'b0}}),
    .in15({32{1'b0}}), .out(Result_2), .sel(AluOP));
  Multiplexer #(.select(4), .width(1), .disabled("Z"), .enable("false")) multiplexer_3 (
    .in0(1'b0), .in1(1'b0), .in2(1'b0), .in3(1'b0), .in4(1'b0), .in5(1'b0), .in6(1'b0), .in7(1'b0),
    .in8(1'b0), .in9(1'b0), .in10(1'b0), .in11(comparator_1_lt[0]), .in12(comparator_2_lt[0]), .in13(1'b0),
    .in14(1'b0), .in15(1'b0), .out(out_6), .sel(AluOP));
  not not_1 (out_4, out_6);

  // Other names for the same wires on the sheet: Result2[31:0] = Result_2; S[3:0] = AluOP; tunnel = out_6;
  //   tunnel_t = out_4

  // Notes on the sheet:
  //   不要改变此引脚区域内容，也不要改变ALU封装形式
  //   输入引脚
  //   输出引脚
endmodule

module Regifile (
  input  [31:0] Din,
  input  Clk,
  input  WE,
  input  [4:0] W_num,
  input  [4:0] R2_num,
  input  [4:0] R1_num,
  output [31:0] R1,
  output [31:0] R2
);

  // RegisterFile registerfile_1: pin names not known; wires that end beside it: Din, Clk, WE, W_num, R1_num, R2_num, R1, R2
endmodule

module \理想流水线  (
  output RegWrite,
  output MemWrite,
  output [31:0] IF_PC,
  output [31:0] ID_PC,
  output [31:0] EX_PC,
  output [31:0] M_PC,
  output [31:0] WB_PC,
  output [31:0] RDin,
  output [31:0] MDin,
  output [31:0] LedData
);

  wire and_1_out, and_2_out, and_3_out, Beq, Bne, CLK, clock_1_out, clock_2_out, comparator_1_eq,
       comparator_1_lt, comparator_2_eq, d_ff_1_q, ecall, equal, EX_halt, EX_MEM_halt_2, EX_MEM_jal_2,
       EX_MEM_jalr_2, EX_MEM_memtoreg_2, EX_MEM_regwrite_2, Go, halt, ID_EX_alusrcb_2, ID_EX_beq_2,
       ID_EX_bne_2, ID_EX_jal_2, ID_EX_memtoreg_2, ID_EX_memwrite_2, ID_EX_regwrite_2, IR1, IR2, IR3, jal,
       jalr, mem_wb_1_halt_2, mem_wb_1_jal_2, mem_wb_1_jalr_2, nand_1_out, not_1_out, not_2_out, not_3_out,
       not_4_out, not_5_out, not_6_out, RST, S_type, W1, W2, W3, \单周期硬布线控制器_1_alu_src , \单周期硬布线控制器_1_bltu ,
       \单周期硬布线控制器_1_ecall , \单周期硬布线控制器_1_lbu , \单周期硬布线控制器_1_memtoreg , \单周期硬布线控制器_1_memwrite ,
       \单周期硬布线控制器_1_regwrite , \单周期硬布线控制器_1_uret ;
  wire [0:0] or_1_out;
  wire [1:0] mem_wb_1_memtoreg_2, PCSrc;
  wire [3:0] ID_EX_aluop_2, \单周期硬布线控制器_1_alu_op ;
  wire [4:0] EX_MEM_rd_2, ID_EX_rd_2, multiplexer_2_out, multiplexer_3_out, WB_W_num;
  wire [11:0] multiplexer_4_out;
  wire [12:0] CNT_num;
  wire [15:0] \LoadUse次数 , \总周期数 , \插入气泡数 , \无条件分支数 , \条件分支成功数 ;
  wire [31:0] ALU_result, bit_extender_1_out, bit_extender_2_out, bit_extender_3_out, branch_add, EX_IR,
       EX_MEM_aluresuult_2, EX_PC_4, ID_EX_imm_2, ID_EX_r1_2, ID_EX_r2_2, ID_IR, ID_PC_4, IF_IR, IF_PC_4,
       MEM_IR, MEM_PC_4, mem_wb_1_aluresuult_2, mem_wb_1_mdout_2, mem_wb_1_pc_4_2, multiplexer_1_out,
       multiplexer_5_out, multiplexer_6_out, ram_1_data, regifile_1_r1, regifile_1_r2, shifter_1_out, WB_IR;

  Button \u_总复位  (.out(RST));
  Button _1 (.out(IR1));
  Button _2 (.out(IR2));
  Button _3 (.out(IR3));
  // Probe on \总周期数 
  // Probe on \总周期数 
  Button \u_继续运行  (.out(Go));
  LED #(.active("true")) led_1 (.in(W1));
  LED #(.active("true")) led_2 (.in(W2));
  LED #(.active("true")) led_3 (.in(W3));
  Hex_Digit_Display hex_digit_display_1 (.value(LedData[31:28]));  // open: dp
  // Probe on IF_PC[19:0]
  // RiscV_Probe riscv_probe_1: pin names not known; wires that end beside it: IF_IR
  Hex_Digit_Display hex_digit_display_2 (.value(LedData[27:24]));  // open: dp
  Hex_Digit_Display hex_digit_display_3 (.value(LedData[23:20]));  // open: dp
  // Probe on ID_PC[19:0]
  // RiscV_Probe riscv_probe_2: pin names not known; wires that end beside it: ID_IR
  Multiplexer #(.select(2), .width(32), .disabled("Z"), .enable("false")) multiplexer_1 (
    .in0(IF_PC_4), .in1(ALU_result), .in2(branch_add), .out(multiplexer_1_out), .sel(PCSrc));  // open: in3
  Hex_Digit_Display hex_digit_display_4 (.value(LedData[15:12]));  // open: dp
  Hex_Digit_Display hex_digit_display_5 (.value(LedData[19:16]));  // open: dp
  Register #(.width(32), .trigger("rising"), .Select("low")) PC (
    .D(multiplexer_1_out), .en(not_1_out), .Q(IF_PC), .clk(CLK), .clr(RST));
  not not_1 (not_1_out, halt);
  Hex_Digit_Display hex_digit_display_6 (.value(LedData[11:8]));  // open: dp
  Hex_Digit_Display hex_digit_display_7 (.value(LedData[7:4]));  // open: dp
  Clock #(.highDuration(1), .lowDuration(1)) clock_1 (.out(clock_1_out));
  // Probe on EX_PC[19:0]
  // RiscV_Probe riscv_probe_3: pin names not known; wires that end beside it: clock_1_out, EX_IR, CLK
  Hex_Digit_Display hex_digit_display_8 (.value(LedData[3:0]));  // open: dp
  Adder #(.width(32)) adder_1 (.a(IF_PC), .b(32'h4), .out(IF_PC_4));  // open: cin, cout
  // Probe on \总周期数 
  // Probe on M_PC[19:0]
  // RiscV_Probe riscv_probe_4: pin names not known; wires that end beside it: MEM_IR
  // Probe on \总周期数 
  // Probe on \无条件分支数 
  // Probe on \条件分支成功数 
  // Probe on \插入气泡数 
  // Probe on \LoadUse次数 
  // RiscV_Probe riscv_probe_5: pin names not known; wires that end beside it: IF_IR
  ROM #(.addrWidth(10), .dataWidth(32), .Select("high")) rom_1 (.addr(IF_PC[11:2]), .data(IF_IR));
  // Probe on IF_PC[11:0]
  // Probe on WB_PC[19:0]
  // RiscV_Probe riscv_probe_6: pin names not known; wires that end beside it: WB_IR
  // Probe on ID_PC[11:0]
  // Probe on EX_PC[11:0]
  IF_ID IF_ID (
    .IR(IF_IR), .PC(IF_PC), .PC_4(IF_PC_4), .Clk(CLK), .IR_2(ID_IR), .PC_2(ID_PC), .PC_4_2(ID_PC_4),
    .en(not_2_out), .reset(RST), .flush(1'b0));  // open: PredictJump, PredictJump_2
  not not_2 (not_2_out, halt);
  // Probe on M_PC[11:0]
  D_Flip_Flop #(.trigger("high"), .Pre_Clr_Positions("LEGACY"), .NegatePresetClear("false"), .enable("true"), .NewFFLayout("false")) d_ff_1 (.Q(d_ff_1_q));  // open: clk, D, Qn, preset, en, reset
  // Probe on 13'h12
  // Probe on WB_PC[11:0]
  Comparator #(.width(13), .mode("twosComplement")) comparator_1 (
    .a(CNT_num), .b(13'h12), .eq(comparator_1_eq), .lt(comparator_1_lt));  // open: gt
  Clock #(.highDuration(1), .lowDuration(1)) clock_2 (.out(clock_2_out));
  nand nand_1 (nand_1_out, d_ff_1_q, comparator_1_eq);
  Counter #(.width(13), .max('h1fff), .ongoal("stay"), .trigger("rising"), .behavior("old")) counter_1 (
    .count(comparator_1_lt), .Q(CNT_num), .clk(clock_2_out));  // open: load, D, carry, clr, preset
  assign CLK = nand_1_out ? clock_2_out : 1'bz;  // Controlled_Buffer controlled_buffer_1
  \单周期硬布线控制器  \u_单周期硬布线控制器_1  (
    .Funct({ID_IR[30], ID_IR[25], ID_IR[14:12]}), .OP(ID_IR[6:2]), .ALU_OP(\单周期硬布线控制器_1_alu_op ),
    .MemToReg(\单周期硬布线控制器_1_memtoreg ), .MemWrite(\单周期硬布线控制器_1_memwrite ), .ALU_SRC(\单周期硬布线控制器_1_alu_src ),
    .RegWrite(\单周期硬布线控制器_1_regwrite ), .ecall(\单周期硬布线控制器_1_ecall ), .S_type(S_type), .Jalr(jalr), .Beq(Beq),
    .JAL(jal), .Bne(Bne), .in_3(ID_IR[21]), .uret(\单周期硬布线控制器_1_uret ), .lbu(\单周期硬布线控制器_1_lbu ),
    .bltu(\单周期硬布线控制器_1_bltu ));  // open: Rs1Used, Rs2Used, csrrsi, csrrci
  Multiplexer #(.select(1), .width(5), .disabled("Z"), .enable("false")) multiplexer_2 (
    .in0(ID_IR[19:15]), .in1(5'b10001), .out(multiplexer_2_out), .sel(\单周期硬布线控制器_1_ecall ));
  Multiplexer #(.select(1), .width(5), .disabled("Z"), .enable("false")) multiplexer_3 (
    .in0(ID_IR[24:20]), .in1(5'b01010), .out(multiplexer_3_out), .sel(\单周期硬布线控制器_1_ecall ));
  Multiplexer #(.select(1), .width(12), .disabled("Z"), .enable("false")) multiplexer_4 (
    .in0(ID_IR[31:20]), .in1({ID_IR[31:25], ID_IR[11:7]}), .out(multiplexer_4_out), .sel(S_type));
  assign bit_extender_1_out = {{20{multiplexer_4_out[11]}}, multiplexer_4_out};  // Bit_Extender bit_extender_1
  assign bit_extender_2_out = {{20{ID_IR[31]}}, {ID_IR[31], ID_IR[7], ID_IR[30:25], ID_IR[11:8]}};  // Bit_Extender bit_extender_2
  assign bit_extender_3_out = {{12{ID_IR[31]}}, {ID_IR[31], ID_IR[19:12], ID_IR[20], ID_IR[30:21]}};  // Bit_Extender bit_extender_3
  Pull_Resistor #(.pull(1)) pull_resistor_1 (.node(CLK));
  // Probe on multiplexer_2_out
  // Probe on multiplexer_3_out
  Multiplexer #(.select(2), .width(32), .disabled("Z"), .enable("false")) multiplexer_5 (
    .in0(bit_extender_1_out), .in1(bit_extender_2_out), .in2(bit_extender_3_out), .out(multiplexer_5_out),
    .sel({jal, or_1_out[0]}));  // open: in3
  or or_1 (or_1_out[0], Bne, Beq);
  Button button_1 (.out(RST));
  not not_3 (not_3_out, halt);
  Regifile regifile_1 (
    .Din(RDin), .Clk(CLK), .R1(regifile_1_r1), .R2(regifile_1_r2), .WE(RegWrite), .W_num(WB_W_num),
    .R1_num(multiplexer_2_out), .R2_num(multiplexer_3_out));
  Counter #(.width(16), .max('hffff), .ongoal("wrap"), .trigger("rising"), .behavior("new")) counter_2 (
    .count(not_3_out), .Q(\总周期数 ), .clk(CLK), .clr(RST));  // open: load, D, carry, preset, down
  ID_EX ID_EX (
    .ecall(\单周期硬布线控制器_1_ecall ), .Beq(Beq), .Bne(Bne), .MemToReg(\单周期硬布线控制器_1_memtoreg ),
    .MemWrite(\单周期硬布线控制器_1_memwrite ), .RegWrite(\单周期硬布线控制器_1_regwrite ), .AluSrcB(\单周期硬布线控制器_1_alu_src ),
    .jal(jal), .jalr(jalr), .rd(ID_IR[11:7]), .AluOP(\单周期硬布线控制器_1_alu_op ), .imm(multiplexer_5_out),
    .PC(ID_PC), .PC_4(ID_PC_4), .reset(RST), .en(not_4_out), .Clk(CLK), .ecall_2(ecall), .Beq_2(ID_EX_beq_2),
    .Bne_2(ID_EX_bne_2), .MemToReg_2(ID_EX_memtoreg_2), .MemWrite_2(ID_EX_memwrite_2),
    .RegWrite_2(ID_EX_regwrite_2), .AluSrcB_2(ID_EX_alusrcb_2), .jal_2(ID_EX_jal_2), .jalr_2(PCSrc[0]),
    .rd_2(ID_EX_rd_2), .AluOP_2(ID_EX_aluop_2), .imm_2(ID_EX_imm_2), .PC_2(EX_PC), .PC_4_2(EX_PC_4),
    .R1(regifile_1_r1), .R1_2(ID_EX_r1_2), .R2(regifile_1_r2), .R2_2(ID_EX_r2_2), .IR(ID_IR), .IR_2(EX_IR),
    .flush(1'b0));  // open: lbu, lbu_2, bltu, bltu_2, Rs1Forward, Rs1Forward_2, Rs2Forward, Rs2Forward_2, uret, uret_2, PredictJump, PredictJump_2
  not not_4 (not_4_out, halt);
  or or_2 (PCSrc[1], ID_EX_jal_2, and_1_out, and_2_out);
  and and_1 (and_1_out, ID_EX_beq_2, equal);
  Shifter #(.width(32), .shift("ll")) shifter_1 (.in(ID_EX_imm_2), .\dist (5'b00001), .out(shifter_1_out));
  and and_2 (and_2_out, ~equal, ID_EX_bne_2);  // AND_Gate
  Multiplexer #(.select(1), .width(32), .disabled("Z"), .enable("false")) multiplexer_6 (
    .in0(ID_EX_r2_2), .in1(ID_EX_imm_2), .out(multiplexer_6_out), .sel(ID_EX_alusrcb_2));
  Adder #(.width(32)) adder_2 (.a(shifter_1_out), .b(EX_PC), .out(branch_add));  // open: cin, cout
  Comparator #(.width(32), .mode("twosComplement")) comparator_2 (
    .a(ID_EX_r1_2), .b(32'h22), .eq(comparator_2_eq));  // open: gt, lt
  and and_3 (and_3_out, comparator_2_eq, ecall);
  ALU alu_1 (
    .X(ID_EX_r1_2), .Y(multiplexer_6_out), .AluOP(ID_EX_aluop_2), .Equal(equal), .Result(ALU_result));  // open: Result_2, out_4, out_6
  and and_4 (EX_halt, ecall, ~comparator_2_eq);  // AND_Gate
  Register #(.width(32), .trigger("rising"), .Select("low")) register_1 (
    .D(ID_EX_r2_2), .en(and_3_out), .Q(LedData), .clk(CLK));  // open: clr
  not not_5 (not_5_out, halt);
  EX_MEM EX_MEM (
    .MemToReg(ID_EX_memtoreg_2), .MemWrite(ID_EX_memwrite_2), .RegWrite(ID_EX_regwrite_2), .halt(EX_halt),
    .rd(ID_EX_rd_2), .PC(EX_PC), .PC_4(EX_PC_4), .IR(EX_IR), .MDin(ID_EX_r2_2), .AluResuult(ALU_result),
    .MemToReg_2(EX_MEM_memtoreg_2), .MemWrite_2(MemWrite), .RegWrite_2(EX_MEM_regwrite_2),
    .halt_2(EX_MEM_halt_2), .rd_2(EX_MEM_rd_2), .PC_2(M_PC), .PC_4_2(MEM_PC_4), .IR_2(MEM_IR), .MDin_2(MDin),
    .AluResuult_2(EX_MEM_aluresuult_2), .reset(RST), .en(not_5_out), .Clk(CLK), .jal(ID_EX_jal_2),
    .jal_2(EX_MEM_jal_2), .jalr(PCSrc[0]), .jalr_2(EX_MEM_jalr_2), .flush(1'b0));  // open: lbu, lbu_2
  RAM #(.addrWidth(10), .dataWidth(32), .bus("separate"), .Select("high")) ram_1 (
    .addr(EX_MEM_aluresuult_2[11:2]), .din(MDin), .data(ram_1_data), .str(MemWrite), .clk(CLK));  // open: sel, ld, clr
  MEM_WB mem_wb_1 (
    .jal(EX_MEM_jal_2), .jalr(EX_MEM_jalr_2), .MemToReg(EX_MEM_memtoreg_2), .RegWrite(EX_MEM_regwrite_2),
    .halt(EX_MEM_halt_2), .rd(EX_MEM_rd_2), .PC(M_PC), .PC_4(MEM_PC_4), .IR(MEM_IR),
    .AluResuult(EX_MEM_aluresuult_2), .jal_2(mem_wb_1_jal_2), .jalr_2(mem_wb_1_jalr_2),
    .MemToReg_2(mem_wb_1_memtoreg_2[0]), .RegWrite_2(RegWrite), .halt_2(mem_wb_1_halt_2), .rd_2(WB_W_num),
    .PC_2(WB_PC), .PC_4_2(mem_wb_1_pc_4_2), .IR_2(WB_IR), .AluResuult_2(mem_wb_1_aluresuult_2), .reset(RST),
    .en(not_6_out), .Clk(CLK), .MDout(ram_1_data), .MDout_2(mem_wb_1_mdout_2));
  not not_6 (not_6_out, halt);
  or or_3 (mem_wb_1_memtoreg_2[1], mem_wb_1_jalr_2, mem_wb_1_jal_2);
  D_Flip_Flop #(.trigger("rising"), .Pre_Clr_Positions("ABOVE_BELOW"), .NegatePresetClear("false"), .enable("true"), .NewFFLayout("true")) d_ff_2 (
    .clk(mem_wb_1_halt_2), .D(1'b1), .Q(halt), .en(1'b1), .reset(Go));  // open: Qn, preset
  Multiplexer #(.select(2), .width(32), .disabled("Z"), .enable("false")) multiplexer_7 (
    .in0(mem_wb_1_aluresuult_2), .in1(mem_wb_1_mdout_2), .in2(mem_wb_1_pc_4_2), .out(RDin),
    .sel(mem_wb_1_memtoreg_2));  // open: in3

  // Other names for the same wires on the sheet: MEM_PC[31:0] = M_PC

  // Notes on the sheet:
  //   中断源
  //   时空图监测，可删除
  //   中断等待指示
  //   数码管输出
  //   指令存储器
  //   指令探针
  //   contents of rom_1 (hex, n*v repeats v):
  //   413 493 913 993 46413 14e493 296913 39e993 842023 942223 1242423 1342623 a00893 493 913 993 73
  //   控制位
  //   流水调试日志用
  //   暂停节拍，不能为0
  //   指令字
  //   戳工具置1进入计数暂停模式，ctrl+k时钟自动运行到对应节拍暂停
  //   ctrl+k关闭时钟连续运行，将控制位置零，进入单步调试模式调试
  //   用这个时钟源需要去掉电路中的其他时钟源
  //   rs1
  //   rs2
  //   rd
  //   imm-lw
  //   imm-sw
  //   imm-b
  //   imm-jal
  //   可计数暂停的时钟源
  //   JAL
  //   JALR
  //   URET
  //   lbu
  //   bltu
  //   Beq
  //   Bne
  //   MemToReg
  //   MemWrite
  //   AluOP
  //   AluSrcB
  //   RegWrite
  //   注意：测试流水线时，需将寄存器堆改为下跳沿触发
  //   为方便自动评测，需要输出流水线各段保存的PC值，注意是PC不是PC+4，另外ID段寄存器写入信息，Mem段内存写入信息也要输出
  //   R[rs1]
  //   R[rs2]
  //   数据存储器
endmodule

module \气泡流水线  (
  output RegWrite,
  output MemWrite,
  output [31:0] IF_PC,
  output [31:0] ID_PC,
  output [31:0] EX_PC,
  output [31:0] M_PC,
  output [31:0] WB_PC,
  output [31:0] RDin,
  output [31:0] MDin,
  output [31:0] LedData
);

  wire and_1_out, and_2_out, and_3_out, and_4_out, and_5_out, Beq, bltu, Bne, BranchTaken, CLK, clock_1_out,
       clock_2_out, comparator_1_eq, comparator_1_lt, comparator_2_eq, d_ff_1_q, ecall, equal, EX_ecall,
       EX_halt, EX_MEM_halt_2, EX_MEM_jal_2, EX_MEM_jalr_2, EX_MEM_memtoreg_2, EX_RegWrite, flush, Go, halt,
       ID_EX_alusrcb_2, ID_EX_beq_2, ID_EX_bltu_2, ID_EX_bne_2, ID_EX_jal_2, ID_EX_lbu_2, ID_EX_memtoreg_2,
       ID_EX_memwrite_2, IR1, IR2, IR3, jal, jalr, lbu, MEM_lbu, MEM_RegWrite, mem_wb_1_halt_2,
       mem_wb_1_jal_2, mem_wb_1_jalr_2, nand_1_out, nor_1_out, nor_2_out, not_1_out, not_2_out, not_3_out,
       not_4_out, Rs1Used, Rs2Used, RST, S_type, stall, tunnel, W1, W2, W3, \单周期硬布线控制器_1_alu_src ,
       \单周期硬布线控制器_1_memtoreg , \单周期硬布线控制器_1_memwrite , \单周期硬布线控制器_1_regwrite , \单周期硬布线控制器_1_uret ;
  wire [0:0] or_1_out;
  wire [1:0] mem_wb_1_memtoreg_2, PCSrc;
  wire [3:0] ID_EX_aluop_2, \单周期硬布线控制器_1_alu_op ;
  wire [4:0] EX_WriteReg_num, MEM_WriteReg_num, rs1, rs2, WB_W_num;
  wire [7:0] multiplexer_7_out;
  wire [11:0] multiplexer_4_out;
  wire [12:0] CNT_num;
  wire [15:0] \LoadUse次数 , \总周期数 , \插入气泡数 , \无条件分支数 , \条件分支成功数 ;
  wire [31:0] ALU_result, bit_extender_1_out, bit_extender_2_out, bit_extender_3_out, bit_extender_4_out,
       branch_add, EX_IR, EX_MEM_aluresuult_2, EX_PC_4, ID_EX_imm_2, ID_EX_r1_2, ID_EX_r2_2, ID_IR, ID_PC_4,
       IF_IR, IF_PC_4, MEM_IR, MEM_PC_4, mem_wb_1_aluresuult_2, mem_wb_1_mdout_2, mem_wb_1_pc_4_2,
       multiplexer_1_out, multiplexer_5_out, multiplexer_6_out, multiplexer_8_out, ram_1_data, regifile_1_r1,
       regifile_1_r2, shifter_1_out, WB_IR;

  Button \u_总复位  (.out(RST));
  Button _1 (.out(IR1));
  Button _2 (.out(IR2));
  Button _3 (.out(IR3));
  // Probe on \总周期数 
  // Probe on \总周期数 
  Button \u_继续运行  (.out(Go));
  LED #(.active("true")) led_1 (.in(W1));
  LED #(.active("true")) led_2 (.in(W2));
  LED #(.active("true")) led_3 (.in(W3));
  Hex_Digit_Display hex_digit_display_1 (.value(LedData[31:28]));  // open: dp
  // Probe on IF_PC[19:0]
  // RiscV_Probe riscv_probe_1: pin names not known; wires that end beside it: IF_IR
  Hex_Digit_Display hex_digit_display_2 (.value(LedData[27:24]));  // open: dp
  Hex_Digit_Display hex_digit_display_3 (.value(LedData[23:20]));  // open: dp
  // Probe on ID_PC[19:0]
  // RiscV_Probe riscv_probe_2: pin names not known; wires that end beside it: ID_IR
  Multiplexer #(.select(2), .width(32), .disabled("Z"), .enable("false")) multiplexer_1 (
    .in0(IF_PC_4), .in1(ALU_result), .in2(branch_add), .out(multiplexer_1_out), .sel(PCSrc));  // open: in3
  Hex_Digit_Display hex_digit_display_4 (.value(LedData[15:12]));  // open: dp
  Hex_Digit_Display hex_digit_display_5 (.value(LedData[19:16]));  // open: dp
  Register #(.width(32), .trigger("rising"), .Select("low")) PC (
    .D(multiplexer_1_out), .en(nor_1_out), .Q(IF_PC), .clk(CLK), .clr(RST));
  nor nor_1 (nor_1_out, stall, halt);
  Hex_Digit_Display hex_digit_display_6 (.value(LedData[11:8]));  // open: dp
  Hex_Digit_Display hex_digit_display_7 (.value(LedData[7:4]));  // open: dp
  Clock #(.highDuration(1), .lowDuration(1)) clock_1 (.out(clock_1_out));
  // Probe on EX_PC[19:0]
  // RiscV_Probe riscv_probe_3: pin names not known; wires that end beside it: clock_1_out, EX_IR, CLK
  Hex_Digit_Display hex_digit_display_8 (.value(LedData[3:0]));  // open: dp
  \气泡处理逻辑  \u_气泡处理逻辑_1  (
    .EX_RegWrite(EX_RegWrite), .MEM_RegWrite(MEM_RegWrite), .EX_WriteReg_num(EX_WriteReg_num),
    .MEM_WriteReg_num(MEM_WriteReg_num), .Rs1Used(Rs1Used), .Rs1(rs1), .BranchTaken(BranchTaken),
    .Rs2Used(Rs2Used), .Rs2(rs2), .ecall(ecall), .Flush(flush), .Stall(stall));
  Adder #(.width(32)) adder_1 (.a(IF_PC), .b(32'h4), .out(IF_PC_4));  // open: cin, cout
  // Probe on \总周期数 
  // Probe on M_PC[19:0]
  // RiscV_Probe riscv_probe_4: pin names not known; wires that end beside it: MEM_IR
  // Probe on \总周期数 
  // Probe on \无条件分支数 
  // Probe on \条件分支成功数 
  // Probe on \插入气泡数 
  // Probe on \LoadUse次数 
  // RiscV_Probe riscv_probe_5: pin names not known; wires that end beside it: IF_IR
  ROM #(.addrWidth(10), .dataWidth(32), .Select("high")) rom_1 (.addr(IF_PC[11:2]), .data(IF_IR));
  // Probe on IF_PC[11:0]
  // Probe on WB_PC[19:0]
  // RiscV_Probe riscv_probe_6: pin names not known; wires that end beside it: WB_IR
  nor nor_2 (nor_2_out, stall, halt);
  // Probe on ID_PC[11:0]
  // Probe on EX_PC[11:0]
  IF_ID IF_ID (
    .IR(IF_IR), .PC(IF_PC), .PC_4(IF_PC_4), .Clk(and_1_out), .IR_2(ID_IR), .PC_2(ID_PC), .PC_4_2(ID_PC_4),
    .en(nor_2_out), .reset(RST), .flush(BranchTaken));  // open: PredictJump, PredictJump_2
  and and_1 (and_1_out, CLK, ~halt);  // AND_Gate
  // Probe on M_PC[11:0]
  D_Flip_Flop #(.trigger("high"), .Pre_Clr_Positions("LEGACY"), .NegatePresetClear("false"), .enable("true"), .NewFFLayout("false")) d_ff_1 (.Q(d_ff_1_q));  // open: clk, D, Qn, preset, en, reset
  // Probe on 13'h19
  // Probe on WB_PC[11:0]
  Comparator #(.width(13), .mode("twosComplement")) comparator_1 (
    .a(CNT_num), .b(13'h19), .eq(comparator_1_eq), .lt(comparator_1_lt));  // open: gt
  Clock #(.highDuration(1), .lowDuration(1)) clock_2 (.out(clock_2_out));
  nand nand_1 (nand_1_out, d_ff_1_q, comparator_1_eq);
  Counter #(.width(13), .max('h1fff), .ongoal("stay"), .trigger("rising"), .behavior("old")) counter_1 (
    .count(comparator_1_lt), .Q(CNT_num), .clk(clock_2_out));  // open: load, D, carry, clr, preset
  assign CLK = nand_1_out ? clock_2_out : 1'bz;  // Controlled_Buffer controlled_buffer_1
  \单周期硬布线控制器  \u_单周期硬布线控制器_1  (
    .Funct({ID_IR[30], ID_IR[25], ID_IR[14:12]}), .OP(ID_IR[6:2]), .ALU_OP(\单周期硬布线控制器_1_alu_op ),
    .MemToReg(\单周期硬布线控制器_1_memtoreg ), .MemWrite(\单周期硬布线控制器_1_memwrite ), .ALU_SRC(\单周期硬布线控制器_1_alu_src ),
    .RegWrite(\单周期硬布线控制器_1_regwrite ), .ecall(ecall), .S_type(S_type), .Jalr(jalr), .Beq(Beq), .JAL(jal),
    .Bne(Bne), .in_3(ID_IR[21]), .uret(\单周期硬布线控制器_1_uret ), .lbu(lbu), .bltu(bltu), .Rs1Used(Rs1Used),
    .Rs2Used(Rs2Used));  // open: csrrsi, csrrci
  Multiplexer #(.select(1), .width(5), .disabled("Z"), .enable("false")) multiplexer_2 (
    .in0(ID_IR[19:15]), .in1(5'b10001), .out(rs1), .sel(ecall));
  Multiplexer #(.select(1), .width(5), .disabled("Z"), .enable("false")) multiplexer_3 (
    .in0(ID_IR[24:20]), .in1(5'b01010), .out(rs2), .sel(ecall));
  assign bit_extender_1_out = {{20{multiplexer_4_out[11]}}, multiplexer_4_out};  // Bit_Extender bit_extender_1
  Multiplexer #(.select(1), .width(12), .disabled("Z"), .enable("false")) multiplexer_4 (
    .in0(ID_IR[31:20]), .in1({ID_IR[31:25], ID_IR[11:7]}), .out(multiplexer_4_out), .sel(S_type));
  assign bit_extender_2_out = {{20{ID_IR[31]}}, {ID_IR[31], ID_IR[7], ID_IR[30:25], ID_IR[11:8]}};  // Bit_Extender bit_extender_2
  assign bit_extender_3_out = {{12{ID_IR[31]}}, {ID_IR[31], ID_IR[19:12], ID_IR[20], ID_IR[30:21]}};  // Bit_Extender bit_extender_3
  Pull_Resistor #(.pull(1)) pull_resistor_1 (.node(CLK));
  Multiplexer #(.select(2), .width(32), .disabled("Z"), .enable("false")) multiplexer_5 (
    .in0(bit_extender_1_out), .in1(bit_extender_2_out), .in2(bit_extender_3_out), .out(multiplexer_5_out),
    .sel({jal, or_1_out[0]}));  // open: in3
  or or_1 (or_1_out[0], Bne, bltu, Beq);
  Button button_1 (.out(RST));
  Regifile regifile_1 (
    .Din(RDin), .Clk(CLK), .R1(regifile_1_r1), .R2(regifile_1_r2), .WE(RegWrite), .W_num(WB_W_num),
    .R1_num(rs1), .R2_num(rs2));
  not not_1 (not_1_out, halt);
  Counter #(.width(16), .max('hffff), .ongoal("wrap"), .trigger("rising"), .behavior("new")) counter_2 (
    .count(not_1_out), .Q(\总周期数 ), .clk(CLK), .clr(RST));  // open: load, D, carry, preset, down
  ID_EX ID_EX (
    .ecall(ecall), .Beq(Beq), .Bne(Bne), .MemToReg(\单周期硬布线控制器_1_memtoreg ),
    .MemWrite(\单周期硬布线控制器_1_memwrite ), .RegWrite(\单周期硬布线控制器_1_regwrite ), .AluSrcB(\单周期硬布线控制器_1_alu_src ),
    .jal(jal), .jalr(jalr), .rd(ID_IR[11:7]), .AluOP(\单周期硬布线控制器_1_alu_op ), .imm(multiplexer_5_out),
    .PC(ID_PC), .PC_4(ID_PC_4), .reset(RST), .en(not_2_out), .Clk(CLK), .ecall_2(EX_ecall),
    .Beq_2(ID_EX_beq_2), .Bne_2(ID_EX_bne_2), .MemToReg_2(ID_EX_memtoreg_2), .MemWrite_2(ID_EX_memwrite_2),
    .RegWrite_2(EX_RegWrite), .AluSrcB_2(ID_EX_alusrcb_2), .jal_2(ID_EX_jal_2), .jalr_2(PCSrc[0]),
    .rd_2(EX_WriteReg_num), .AluOP_2(ID_EX_aluop_2), .imm_2(ID_EX_imm_2), .PC_2(EX_PC), .PC_4_2(EX_PC_4),
    .R1(regifile_1_r1), .R1_2(ID_EX_r1_2), .R2(regifile_1_r2), .R2_2(ID_EX_r2_2), .IR(ID_IR), .IR_2(EX_IR),
    .flush(flush), .lbu(lbu), .lbu_2(ID_EX_lbu_2), .bltu(bltu), .bltu_2(ID_EX_bltu_2));  // open: Rs1Forward, Rs1Forward_2, Rs2Forward, Rs2Forward_2, uret, uret_2, PredictJump, PredictJump_2
  not not_2 (not_2_out, halt);
  or or_2 (PCSrc[1], ID_EX_jal_2, and_2_out, and_3_out, and_4_out);
  and and_2 (and_2_out, ID_EX_beq_2, equal);
  Shifter #(.width(32), .shift("ll")) shifter_1 (.in(ID_EX_imm_2), .\dist (5'b00001), .out(shifter_1_out));
  and and_3 (and_3_out, ~equal, ID_EX_bne_2);  // AND_Gate
  and and_4 (and_4_out, ID_EX_bltu_2, tunnel);
  Multiplexer #(.select(1), .width(32), .disabled("Z"), .enable("false")) multiplexer_6 (
    .in0(ID_EX_r2_2), .in1(ID_EX_imm_2), .out(multiplexer_6_out), .sel(ID_EX_alusrcb_2));
  Adder #(.width(32)) adder_2 (.a(shifter_1_out), .b(EX_PC), .out(branch_add));  // open: cin, cout
  Comparator #(.width(32), .mode("twosComplement")) comparator_2 (
    .a(ID_EX_r1_2), .b(32'h22), .eq(comparator_2_eq));  // open: gt, lt
  and and_5 (and_5_out, comparator_2_eq, EX_ecall);
  or or_3 (BranchTaken, PCSrc[1], PCSrc[0]);
  ALU alu_1 (
    .X(ID_EX_r1_2), .Y(multiplexer_6_out), .AluOP(ID_EX_aluop_2), .Equal(equal), .Result(ALU_result),
    .out_6(tunnel));  // open: Result_2, out_4
  and and_6 (EX_halt, EX_ecall, ~comparator_2_eq);  // AND_Gate
  Register #(.width(32), .trigger("rising"), .Select("low")) register_1 (
    .D(ID_EX_r2_2), .en(and_5_out), .Q(LedData), .clk(CLK));  // open: clr
  not not_3 (not_3_out, halt);
  EX_MEM EX_MEM (
    .MemToReg(ID_EX_memtoreg_2), .MemWrite(ID_EX_memwrite_2), .RegWrite(EX_RegWrite), .halt(EX_halt),
    .rd(EX_WriteReg_num), .PC(EX_PC), .PC_4(EX_PC_4), .IR(EX_IR), .MDin(ID_EX_r2_2), .AluResuult(ALU_result),
    .MemToReg_2(EX_MEM_memtoreg_2), .MemWrite_2(MemWrite), .RegWrite_2(MEM_RegWrite), .halt_2(EX_MEM_halt_2),
    .rd_2(MEM_WriteReg_num), .PC_2(M_PC), .PC_4_2(MEM_PC_4), .IR_2(MEM_IR), .MDin_2(MDin),
    .AluResuult_2(EX_MEM_aluresuult_2), .reset(RST), .en(not_3_out), .Clk(CLK), .jal(ID_EX_jal_2),
    .jal_2(EX_MEM_jal_2), .jalr(PCSrc[0]), .jalr_2(EX_MEM_jalr_2), .lbu(ID_EX_lbu_2), .lbu_2(MEM_lbu),
    .flush(1'b0));
  RAM #(.addrWidth(10), .dataWidth(32), .bus("separate"), .Select("high")) ram_1 (
    .addr(EX_MEM_aluresuult_2[11:2]), .din(MDin), .data(ram_1_data), .str(MemWrite), .clk(CLK));  // open: sel, ld, clr
  Multiplexer #(.select(2), .width(8), .disabled("Z"), .enable("false")) multiplexer_7 (
    .in0(ram_1_data[7:0]), .in1(ram_1_data[15:8]), .in2(ram_1_data[23:16]), .in3(ram_1_data[31:24]),
    .out(multiplexer_7_out), .sel(EX_MEM_aluresuult_2[1:0]));
  assign bit_extender_4_out = {{24{1'b0}}, multiplexer_7_out};  // Bit_Extender bit_extender_4
  MEM_WB mem_wb_1 (
    .jal(EX_MEM_jal_2), .jalr(EX_MEM_jalr_2), .MemToReg(EX_MEM_memtoreg_2), .RegWrite(MEM_RegWrite),
    .halt(EX_MEM_halt_2), .rd(MEM_WriteReg_num), .PC(M_PC), .PC_4(MEM_PC_4), .IR(MEM_IR),
    .AluResuult(EX_MEM_aluresuult_2), .jal_2(mem_wb_1_jal_2), .jalr_2(mem_wb_1_jalr_2),
    .MemToReg_2(mem_wb_1_memtoreg_2[0]), .RegWrite_2(RegWrite), .halt_2(mem_wb_1_halt_2), .rd_2(WB_W_num),
    .PC_2(WB_PC), .PC_4_2(mem_wb_1_pc_4_2), .IR_2(WB_IR), .AluResuult_2(mem_wb_1_aluresuult_2), .reset(RST),
    .en(not_4_out), .Clk(CLK), .MDout(multiplexer_8_out), .MDout_2(mem_wb_1_mdout_2));
  Multiplexer #(.select(1), .width(32), .disabled("Z"), .enable("false")) multiplexer_8 (
    .in0(ram_1_data), .in1(bit_extender_4_out), .out(multiplexer_8_out), .sel(MEM_lbu));
  not not_4 (not_4_out, halt);
  or or_4 (mem_wb_1_memtoreg_2[1], mem_wb_1_jalr_2, mem_wb_1_jal_2);
  D_Flip_Flop #(.trigger("rising"), .Pre_Clr_Positions("ABOVE_BELOW"), .NegatePresetClear("false"), .enable("true"), .NewFFLayout("true")) d_ff_2 (
    .clk(mem_wb_1_halt_2), .D(1'b1), .Q(halt), .en(1'b1), .reset(Go));  // open: Qn, preset
  Multiplexer #(.select(2), .width(32), .disabled("Z"), .enable("false")) multiplexer_9 (
    .in0(mem_wb_1_aluresuult_2), .in1(mem_wb_1_mdout_2), .in2(mem_wb_1_pc_4_2), .out(RDin),
    .sel(mem_wb_1_memtoreg_2));  // open: in3

  // Other names for the same wires on the sheet: MEM_PC[31:0] = M_PC

  // Notes on the sheet:
  //   中断源
  //   时空图监测，可删除
  //   中断等待指示
  //   数码管输出
  //   指令存储器
  //   指令探针
  //   contents of rom_1 (hex, n*v repeats v):
  //   100493 100006f 100493 200913 300993 100006f 100493 200913 300993 100006f 100493 200913 300993
  //   100006f 100493 200913 300993 3c4000ef 100413 100493 1f49493 900533 2200893 73 24d493 48463 fedff06f
  //   900533 2200893 73 100493 249493 900533 2200893 73 48463 fedff06f 100493 1f49493 900533 2200893 73
  //   4034d493 900533 2200893 73 4044d493 900533 2200893 73 4044d493 900533 2200893 73 4044d493 900533
  //   2200893 73 4044d493 900533 2200893 73 4044d493 900533 2200893 73 4044d493 900533 2200893 73 4044d493
  //   900533 2200893 73 100413 1f41993 41f9d993 433 c00913 300b13 140413 f47413 800293 100313 499993
  //   89e9b3 1300533 2200893 73 406282b3 fe0294e3 140413 f00f93 1f47433 1c41413 800293 100313 49d993
  //   89e9b3 1300533 2200893 73 406282b3 fe0294e3 1c45413 406b0b33 b0463 f95ff06f 2b3 fff2c293 829293
  //   ff2e293 500533 2200893 73 fff00413 493 84a023 140413 448493 84a023 140413 448493 84a023 140413
  //   448493 84a023 140413 448493 84a023 140413 448493 84a023 140413 448493 84a023 140413 448493 84a023
  //   140413 448493 84a023 140413 448493 84a023 140413 448493 84a023 140413 448493 84a023 140413 448493
  //   84a023 140413 448493 84a023 140413 448493 84a023 140413 448493 84a023 140413 448493 140413 433
  //   3c00493 42983 4aa03 149a2b3 28663 134a023 1442023 ffc48493 fe9412e3 800533 2200893 73 440413 3c00493
  //   fc9416e3 3200893 73 100293 300313 800493 849493 7648493 900533 2200893 73 800e13 5494b3 6494b3
  //   900533 2200893 73 fffe0e13 fe0e14e3 a00893 73 fff00293 313 1900413 841413 9700493 940533 2200893 73
  //   5484b3 494b313 fe0306e3 a00893 73 313 1000e13 8400493 849493 8348493 400913 891913 490913 849493
  //   8248493 849493 8148493 891913 490913 891913 490913 932023 12484b3 430313 fffe0e13 fe0e18e3 2000e13
  //   313 34483 900533 2200893 73 130313 fffe0e13 fe0e14e3 a00893 73 ff100493 900533 2200893 73 148493
  //   fe9068e3 900533 2200893 73 a00893 73 413 140413 800533 2200893 73 240413 800533 2200893 73 340413
  //   800533 2200893 73 440413 800533 2200893 73 540413 800533 2200893 73 640413 800533 2200893 73 740413
  //   800533 2200893 73 840413 800533 2200893 2200893 73 8067
  //   控制位
  //   流水调试日志用
  //   暂停节拍，不能为0
  //   指令字
  //   戳工具置1进入计数暂停模式，ctrl+k时钟自动运行到对应节拍暂停
  //   ctrl+k关闭时钟连续运行，将控制位置零，进入单步调试模式调试
  //   rs1
  //   rs2
  //   rd
  //   imm-lw
  //   imm-sw
  //   imm-b
  //   imm-jal
  //   可计数暂停的时钟源
  //   JAL
  //   JALR
  //   URET
  //   lbu
  //   bltu
  //   Beq
  //   Bne
  //   MemToReg
  //   MemWrite
  //   AluOP
  //   AluSrcB
  //   RegWrite
  //   注意：测试流水线时，需将寄存器堆改为下跳沿触发
  //   为方便自动评测，需要输出流水线各段保存的PC值，注意是PC不是PC+4，另外ID段寄存器写入信息，Mem段内存写入信息也要输出
  //   R[rs1]
  //   R[rs2]
  //   数据存储器
endmodule

module \重定向流水线  (
  output RegWrite,
  output MemWrite,
  output [31:0] IF_PC,
  output [31:0] ID_PC,
  output [31:0] EX_PC,
  output [31:0] M_PC,
  output [31:0] WB_PC,
  output [31:0] RDin,
  output [31:0] MDin,
  output [31:0] LedData
);

  wire and_1_out, and_2_out, and_3_out, and_4_out, and_5_out, Beq, bltu, Bne, BranchTaken, CLK, clock_1_out,
       clock_2_out, comparator_1_eq, comparator_1_lt, comparator_2_eq, d_ff_1_q, ecall, equal, EX_ecall,
       EX_halt, EX_MEM_halt_2, EX_MEM_jal_2, EX_MEM_jalr_2, EX_MEM_memtoreg_2, EX_MemToReg, EX_RegWrite,
       flush, Go, halt, ID_EX_alusrcb_2, ID_EX_beq_2, ID_EX_bltu_2, ID_EX_bne_2, ID_EX_jal_2, ID_EX_lbu_2,
       ID_EX_memwrite_2, IR1, IR2, IR3, jal, jalr, lbu, MEM_lbu, MEM_RegWrite, mem_wb_1_halt_2,
       mem_wb_1_jal_2, mem_wb_1_jalr_2, nand_1_out, nor_1_out, nor_2_out, not_1_out, not_2_out, not_3_out,
       not_4_out, Rs1Used, Rs2Used, RST, S_type, stall, tunnel, W1, W2, W3, \单周期硬布线控制器_1_alu_src ,
       \单周期硬布线控制器_1_memtoreg , \单周期硬布线控制器_1_memwrite , \单周期硬布线控制器_1_regwrite , \单周期硬布线控制器_1_uret ;
  wire [0:0] or_1_out;
  wire [1:0] ID_EX_rs1forward_2, ID_EX_rs2forward_2, mem_wb_1_memtoreg_2, PCSrc, Rs1Forward, Rs2Forward;
  wire [3:0] ID_EX_aluop_2, \单周期硬布线控制器_1_alu_op ;
  wire [4:0] EX_WriteReg_num, MEM_WriteReg_num, rs1, rs2, WB_W_num;
  wire [7:0] multiplexer_9_out;
  wire [11:0] multiplexer_2_out;
  wire [12:0] CNT_num;
  wire [15:0] \LoadUse次数 , \总周期数 , \插入气泡数 , \无条件分支数 , \条件分支成功数 ;
  wire [31:0] ALU_result, bit_extender_1_out, bit_extender_2_out, bit_extender_3_out, bit_extender_4_out,
       branch_add, EX_IR, EX_PC_4, ID_EX_imm_2, ID_EX_r1_2, ID_EX_r2_2, ID_IR, ID_PC_4, IF_IR, IF_PC_4,
       MEM_AluResult, MEM_IR, MEM_PC_4, mem_wb_1_aluresuult_2, mem_wb_1_mdout_2, mem_wb_1_pc_4_2,
       multiplexer_1_out, multiplexer_5_out, multiplexer_6_out, multiplexer_7_out, multiplexer_8_out,
       multiplexer_10_out, ram_1_data, regifile_1_r1, regifile_1_r2, shifter_1_out, WB_IR;

  Button \u_总复位  (.out(RST));
  Button _1 (.out(IR1));
  Button _2 (.out(IR2));
  Button _3 (.out(IR3));
  // Probe on \总周期数 
  // Probe on \总周期数 
  Button \u_继续运行  (.out(Go));
  LED #(.active("true")) led_1 (.in(W1));
  LED #(.active("true")) led_2 (.in(W2));
  LED #(.active("true")) led_3 (.in(W3));
  Hex_Digit_Display hex_digit_display_1 (.value(LedData[31:28]));  // open: dp
  // Probe on IF_PC[19:0]
  // RiscV_Probe riscv_probe_1: pin names not known; wires that end beside it: IF_IR
  Hex_Digit_Display hex_digit_display_2 (.value(LedData[23:20]));  // open: dp
  Hex_Digit_Display hex_digit_display_3 (.value(LedData[27:24]));  // open: dp
  // Probe on ID_PC[19:0]
  // RiscV_Probe riscv_probe_2: pin names not known; wires that end beside it: ID_IR
  Hex_Digit_Display hex_digit_display_4 (.value(LedData[15:12]));  // open: dp
  Hex_Digit_Display hex_digit_display_5 (.value(LedData[19:16]));  // open: dp
  Multiplexer #(.select(2), .width(32), .disabled("Z"), .enable("false")) multiplexer_1 (
    .in0(IF_PC_4), .in1(ALU_result), .in2(branch_add), .out(multiplexer_1_out), .sel(PCSrc));  // open: in3
  nor nor_1 (nor_1_out, stall, halt);
  Hex_Digit_Display hex_digit_display_6 (.value(LedData[7:4]));  // open: dp
  Hex_Digit_Display hex_digit_display_7 (.value(LedData[11:8]));  // open: dp
  Clock #(.highDuration(1), .lowDuration(1)) clock_1 (.out(clock_1_out));
  // Probe on EX_PC[19:0]
  // RiscV_Probe riscv_probe_3: pin names not known; wires that end beside it: clock_1_out, EX_IR, CLK
  Register #(.width(32), .trigger("rising"), .Select("low")) PC (
    .D(multiplexer_1_out), .en(nor_1_out), .Q(IF_PC), .clk(CLK), .clr(RST));
  Hex_Digit_Display hex_digit_display_8 (.value(LedData[3:0]));  // open: dp
  \重定向相关处理逻辑  \u_重定向相关处理逻辑_1  (
    .Rs1Used(Rs1Used), .Rs1(rs1), .EX_WriteReg_num(EX_WriteReg_num), .EX_MemToReg(EX_MemToReg),
    .Rs2Used(Rs2Used), .Rs2(rs2), .MEM_WriteReg_num(MEM_WriteReg_num), .BranchTaken(BranchTaken),
    .EX_RegWrite(EX_RegWrite), .MEM_RegWrite(MEM_RegWrite), .ecall(ecall), .Stall(stall), .Flush(flush),
    .Rs1Foward(Rs1Forward), .Rs2Foward(Rs2Forward));
  Adder #(.width(32)) adder_1 (.a(IF_PC), .b(32'h4), .out(IF_PC_4));  // open: cin, cout
  // Probe on \总周期数 
  // Probe on M_PC[19:0]
  // RiscV_Probe riscv_probe_4: pin names not known; wires that end beside it: MEM_IR
  // Probe on \总周期数 
  // Probe on \无条件分支数 
  // Probe on \条件分支成功数 
  // Probe on \插入气泡数 
  // Probe on \LoadUse次数 
  // RiscV_Probe riscv_probe_5: pin names not known; wires that end beside it: IF_IR
  // Probe on IF_PC[11:0]
  // Probe on WB_PC[19:0]
  // RiscV_Probe riscv_probe_6: pin names not known; wires that end beside it: WB_IR
  ROM #(.addrWidth(10), .dataWidth(32), .Select("high")) rom_1 (.addr(IF_PC[11:2]), .data(IF_IR));
  nor nor_2 (nor_2_out, stall, halt);
  // Probe on EX_PC[11:0]
  // Probe on ID_PC[11:0]
  IF_ID IF_ID (
    .IR(IF_IR), .PC(IF_PC), .PC_4(IF_PC_4), .Clk(and_1_out), .IR_2(ID_IR), .PC_2(ID_PC), .PC_4_2(ID_PC_4),
    .en(nor_2_out), .reset(RST), .flush(BranchTaken));  // open: PredictJump, PredictJump_2
  and and_1 (and_1_out, CLK, ~halt);  // AND_Gate
  // Probe on M_PC[11:0]
  D_Flip_Flop #(.trigger("high"), .Pre_Clr_Positions("LEGACY"), .NegatePresetClear("false"), .enable("true"), .NewFFLayout("false")) d_ff_1 (.Q(d_ff_1_q));  // open: clk, D, Qn, preset, en, reset
  // Probe on 13'h342
  // Probe on WB_PC[11:0]
  Comparator #(.width(13), .mode("twosComplement")) comparator_1 (
    .a(CNT_num), .b(13'h342), .eq(comparator_1_eq), .lt(comparator_1_lt));  // open: gt
  Clock #(.highDuration(1), .lowDuration(1)) clock_2 (.out(clock_2_out));
  nand nand_1 (nand_1_out, d_ff_1_q, comparator_1_eq);
  Counter #(.width(13), .max('h1fff), .ongoal("stay"), .trigger("rising"), .behavior("old")) counter_1 (
    .count(comparator_1_lt), .Q(CNT_num), .clk(clock_2_out));  // open: load, D, carry, clr, preset
  assign CLK = nand_1_out ? clock_2_out : 1'bz;  // Controlled_Buffer controlled_buffer_1
  Multiplexer #(.select(1), .width(12), .disabled("Z"), .enable("false")) multiplexer_2 (
    .in0(ID_IR[31:20]), .in1({ID_IR[31:25], ID_IR[11:7]}), .out(multiplexer_2_out), .sel(S_type));
  Pull_Resistor #(.pull(1)) pull_resistor_1 (.node(CLK));
  \单周期硬布线控制器  \u_单周期硬布线控制器_1  (
    .Funct({ID_IR[30], ID_IR[25], ID_IR[14:12]}), .OP(ID_IR[6:2]), .ALU_OP(\单周期硬布线控制器_1_alu_op ),
    .MemToReg(\单周期硬布线控制器_1_memtoreg ), .MemWrite(\单周期硬布线控制器_1_memwrite ), .ALU_SRC(\单周期硬布线控制器_1_alu_src ),
    .RegWrite(\单周期硬布线控制器_1_regwrite ), .ecall(ecall), .S_type(S_type), .Jalr(jalr), .Beq(Beq), .JAL(jal),
    .Bne(Bne), .in_3(ID_IR[21]), .uret(\单周期硬布线控制器_1_uret ), .lbu(lbu), .bltu(bltu), .Rs1Used(Rs1Used),
    .Rs2Used(Rs2Used));  // open: csrrsi, csrrci
  Multiplexer #(.select(1), .width(5), .disabled("Z"), .enable("false")) multiplexer_3 (
    .in0(ID_IR[19:15]), .in1(5'b10001), .out(rs1), .sel(ecall));
  Multiplexer #(.select(1), .width(5), .disabled("Z"), .enable("false")) multiplexer_4 (
    .in0(ID_IR[24:20]), .in1(5'b01010), .out(rs2), .sel(ecall));
  assign bit_extender_1_out = {{20{multiplexer_2_out[11]}}, multiplexer_2_out};  // Bit_Extender bit_extender_1
  assign bit_extender_2_out = {{20{ID_IR[31]}}, {ID_IR[31], ID_IR[7], ID_IR[30:25], ID_IR[11:8]}};  // Bit_Extender bit_extender_2
  assign bit_extender_3_out = {{12{ID_IR[31]}}, {ID_IR[31], ID_IR[19:12], ID_IR[20], ID_IR[30:21]}};  // Bit_Extender bit_extender_3
  Multiplexer #(.select(2), .width(32), .disabled("Z"), .enable("false")) multiplexer_5 (
    .in0(bit_extender_1_out), .in1(bit_extender_2_out), .in2(bit_extender_3_out), .out(multiplexer_5_out),
    .sel({jal, or_1_out[0]}));  // open: in3
  or or_1 (or_1_out[0], Bne, bltu, Beq);
  Button button_1 (.out(RST));
  Regifile regifile_1 (
    .Din(RDin), .Clk(CLK), .R1(regifile_1_r1), .R2(regifile_1_r2), .WE(RegWrite), .W_num(WB_W_num),
    .R1_num(rs1), .R2_num(rs2));
  not not_1 (not_1_out, halt);
  Counter #(.width(16), .max('hffff), .ongoal("wrap"), .trigger("rising"), .behavior("new")) counter_2 (
    .count(not_1_out), .Q(\总周期数 ), .clk(CLK), .clr(RST));  // open: load, D, carry, preset, down
  // Probe on Rs1Forward
  ID_EX ID_EX (
    .ecall(ecall), .Beq(Beq), .Bne(Bne), .MemToReg(\单周期硬布线控制器_1_memtoreg ),
    .MemWrite(\单周期硬布线控制器_1_memwrite ), .RegWrite(\单周期硬布线控制器_1_regwrite ), .AluSrcB(\单周期硬布线控制器_1_alu_src ),
    .jal(jal), .jalr(jalr), .rd(ID_IR[11:7]), .AluOP(\单周期硬布线控制器_1_alu_op ), .imm(multiplexer_5_out),
    .PC(ID_PC), .PC_4(ID_PC_4), .reset(RST), .en(not_2_out), .Clk(CLK), .ecall_2(EX_ecall),
    .Beq_2(ID_EX_beq_2), .Bne_2(ID_EX_bne_2), .MemToReg_2(EX_MemToReg), .MemWrite_2(ID_EX_memwrite_2),
    .RegWrite_2(EX_RegWrite), .AluSrcB_2(ID_EX_alusrcb_2), .jal_2(ID_EX_jal_2), .jalr_2(PCSrc[0]),
    .rd_2(EX_WriteReg_num), .AluOP_2(ID_EX_aluop_2), .imm_2(ID_EX_imm_2), .PC_2(EX_PC), .PC_4_2(EX_PC_4),
    .R1(regifile_1_r1), .R1_2(ID_EX_r1_2), .R2(regifile_1_r2), .R2_2(ID_EX_r2_2), .IR(ID_IR), .IR_2(EX_IR),
    .flush(flush), .lbu(lbu), .lbu_2(ID_EX_lbu_2), .bltu(bltu), .bltu_2(ID_EX_bltu_2),
    .Rs1Forward(Rs1Forward), .Rs1Forward_2(ID_EX_rs1forward_2), .Rs2Forward(Rs2Forward),
    .Rs2Forward_2(ID_EX_rs2forward_2));  // open: uret, uret_2, PredictJump, PredictJump_2
  // Probe on Rs2Forward
  not not_2 (not_2_out, halt);
  and and_2 (and_2_out, ID_EX_beq_2, equal);
  or or_2 (PCSrc[1], ID_EX_jal_2, and_2_out, and_3_out, and_4_out);
  and and_3 (and_3_out, ~equal, ID_EX_bne_2);  // AND_Gate
  or or_3 (BranchTaken, PCSrc[1], PCSrc[0]);
  and and_4 (and_4_out, ID_EX_bltu_2, tunnel);
  Multiplexer #(.select(2), .width(32), .disabled("Z"), .enable("false")) multiplexer_6 (
    .in0(ID_EX_r1_2), .in1(RDin), .in2(MEM_AluResult), .out(multiplexer_6_out), .sel(ID_EX_rs1forward_2));  // open: in3
  Multiplexer #(.select(2), .width(32), .disabled("Z"), .enable("false")) multiplexer_7 (
    .in0(ID_EX_r2_2), .in1(RDin), .in2(MEM_AluResult), .out(multiplexer_7_out), .sel(ID_EX_rs2forward_2));  // open: in3
  Shifter #(.width(32), .shift("ll")) shifter_1 (.in(ID_EX_imm_2), .\dist (5'b00001), .out(shifter_1_out));
  Multiplexer #(.select(1), .width(32), .disabled("Z"), .enable("false")) multiplexer_8 (
    .in0(multiplexer_7_out), .in1(ID_EX_imm_2), .out(multiplexer_8_out), .sel(ID_EX_alusrcb_2));
  Adder #(.width(32)) adder_2 (.a(shifter_1_out), .b(EX_PC), .out(branch_add));  // open: cin, cout
  Comparator #(.width(32), .mode("twosComplement")) comparator_2 (
    .a(multiplexer_6_out), .b(32'h22), .eq(comparator_2_eq));  // open: gt, lt
  ALU alu_1 (
    .X(multiplexer_6_out), .Y(multiplexer_8_out), .AluOP(ID_EX_aluop_2), .Equal(equal), .Result(ALU_result),
    .out_6(tunnel));  // open: Result_2, out_4
  and and_5 (and_5_out, comparator_2_eq, EX_ecall);
  and and_6 (EX_halt, EX_ecall, ~comparator_2_eq);  // AND_Gate
  Register #(.width(32), .trigger("rising"), .Select("low")) register_1 (
    .D(multiplexer_7_out), .en(and_5_out), .Q(LedData), .clk(CLK));  // open: clr
  not not_3 (not_3_out, halt);
  EX_MEM EX_MEM (
    .MemToReg(EX_MemToReg), .MemWrite(ID_EX_memwrite_2), .RegWrite(EX_RegWrite), .halt(EX_halt),
    .rd(EX_WriteReg_num), .PC(EX_PC), .PC_4(EX_PC_4), .IR(EX_IR), .MDin(multiplexer_7_out),
    .AluResuult(ALU_result), .MemToReg_2(EX_MEM_memtoreg_2), .MemWrite_2(MemWrite),
    .RegWrite_2(MEM_RegWrite), .halt_2(EX_MEM_halt_2), .rd_2(MEM_WriteReg_num), .PC_2(M_PC),
    .PC_4_2(MEM_PC_4), .IR_2(MEM_IR), .MDin_2(MDin), .AluResuult_2(MEM_AluResult), .reset(RST),
    .en(not_3_out), .Clk(CLK), .jal(ID_EX_jal_2), .jal_2(EX_MEM_jal_2), .jalr(PCSrc[0]),
    .jalr_2(EX_MEM_jalr_2), .lbu(ID_EX_lbu_2), .lbu_2(MEM_lbu), .flush(1'b0));
  // Probe on MEM_AluResult
  RAM #(.addrWidth(10), .dataWidth(32), .bus("separate"), .Select("high")) ram_1 (
    .addr(MEM_AluResult[11:2]), .din(MDin), .data(ram_1_data), .str(MemWrite), .clk(CLK));  // open: sel, ld, clr
  // Probe on MEM_WriteReg_num
  Multiplexer #(.select(2), .width(8), .disabled("Z"), .enable("false")) multiplexer_9 (
    .in0(ram_1_data[7:0]), .in1(ram_1_data[15:8]), .in2(ram_1_data[23:16]), .in3(ram_1_data[31:24]),
    .out(multiplexer_9_out), .sel(MEM_AluResult[1:0]));
  assign bit_extender_4_out = {{24{1'b0}}, multiplexer_9_out};  // Bit_Extender bit_extender_4
  Multiplexer #(.select(1), .width(32), .disabled("Z"), .enable("false")) multiplexer_10 (
    .in0(ram_1_data), .in1(bit_extender_4_out), .out(multiplexer_10_out), .sel(MEM_lbu));
  MEM_WB mem_wb_1 (
    .jal(EX_MEM_jal_2), .jalr(EX_MEM_jalr_2), .MemToReg(EX_MEM_memtoreg_2), .RegWrite(MEM_RegWrite),
    .halt(EX_MEM_halt_2), .rd(MEM_WriteReg_num), .PC(M_PC), .PC_4(MEM_PC_4), .IR(MEM_IR),
    .AluResuult(MEM_AluResult), .jal_2(mem_wb_1_jal_2), .jalr_2(mem_wb_1_jalr_2),
    .MemToReg_2(mem_wb_1_memtoreg_2[0]), .RegWrite_2(RegWrite), .halt_2(mem_wb_1_halt_2), .rd_2(WB_W_num),
    .PC_2(WB_PC), .PC_4_2(mem_wb_1_pc_4_2), .IR_2(WB_IR), .AluResuult_2(mem_wb_1_aluresuult_2), .reset(RST),
    .en(not_4_out), .Clk(CLK), .MDout(multiplexer_10_out), .MDout_2(mem_wb_1_mdout_2));
  not not_4 (not_4_out, halt);
  or or_4 (mem_wb_1_memtoreg_2[1], mem_wb_1_jalr_2, mem_wb_1_jal_2);
  D_Flip_Flop #(.trigger("rising"), .Pre_Clr_Positions("ABOVE_BELOW"), .NegatePresetClear("false"), .enable("true"), .NewFFLayout("true")) d_ff_2 (
    .clk(mem_wb_1_halt_2), .D(1'b1), .Q(halt), .en(1'b1), .reset(Go));  // open: Qn, preset
  Multiplexer #(.select(2), .width(32), .disabled("Z"), .enable("false")) multiplexer_11 (
    .in0(mem_wb_1_aluresuult_2), .in1(mem_wb_1_mdout_2), .in2(mem_wb_1_pc_4_2), .out(RDin),
    .sel(mem_wb_1_memtoreg_2));  // open: in3

  // Other names for the same wires on the sheet: MEM_PC[31:0] = M_PC

  // Notes on the sheet:
  //   中断源
  //   时空图监测，可删除
  //   中断等待指示
  //   数码管输出
  //   指令探针
  //   指令存储器
  //   contents of rom_1 (hex, n*v repeats v):
  //   100493 100006f 100493 200913 300993 100006f 100493 200913 300993 100006f 100493 200913 300993
  //   100006f 100493 200913 300993 3c4000ef 100413 100493 1f49493 900533 2200893 73 24d493 48463 fedff06f
  //   900533 2200893 73 100493 249493 900533 2200893 73 48463 fedff06f 100493 1f49493 900533 2200893 73
  //   4034d493 900533 2200893 73 4044d493 900533 2200893 73 4044d493 900533 2200893 73 4044d493 900533
  //   2200893 73 4044d493 900533 2200893 73 4044d493 900533 2200893 73 4044d493 900533 2200893 73 4044d493
  //   900533 2200893 73 100413 1f41993 41f9d993 433 c00913 300b13 140413 f47413 800293 100313 499993
  //   89e9b3 1300533 2200893 73 406282b3 fe0294e3 140413 f00f93 1f47433 1c41413 800293 100313 49d993
  //   89e9b3 1300533 2200893 73 406282b3 fe0294e3 1c45413 406b0b33 b0463 f95ff06f 2b3 fff2c293 829293
  //   ff2e293 500533 2200893 73 fff00413 493 84a023 140413 448493 84a023 140413 448493 84a023 140413
  //   448493 84a023 140413 448493 84a023 140413 448493 84a023 140413 448493 84a023 140413 448493 84a023
  //   140413 448493 84a023 140413 448493 84a023 140413 448493 84a023 140413 448493 84a023 140413 448493
  //   84a023 140413 448493 84a023 140413 448493 84a023 140413 448493 84a023 140413 448493 140413 433
  //   3c00493 42983 4aa03 149a2b3 28663 134a023 1442023 ffc48493 fe9412e3 800533 2200893 73 440413 3c00493
  //   fc9416e3 3200893 73 100293 300313 800493 849493 7648493 900533 2200893 73 800e13 5494b3 6494b3
  //   900533 2200893 73 fffe0e13 fe0e14e3 a00893 73 fff00293 313 1900413 841413 9700493 940533 2200893 73
  //   5484b3 494b313 fe0306e3 a00893 73 313 1000e13 8400493 849493 8348493 400913 891913 490913 849493
  //   8248493 849493 8148493 891913 490913 891913 490913 932023 12484b3 430313 fffe0e13 fe0e18e3 2000e13
  //   313 34483 900533 2200893 73 130313 fffe0e13 fe0e14e3 a00893 73 ff100493 900533 2200893 73 148493
  //   fe9068e3 900533 2200893 73 a00893 73 413 140413 800533 2200893 73 240413 800533 2200893 73 340413
  //   800533 2200893 73 440413 800533 2200893 73 540413 800533 2200893 73 640413 800533 2200893 73 740413
  //   800533 2200893 73 840413 800533 2200893 2200893 73 8067
  //   控制位
  //   流水调试日志用
  //   暂停节拍，不能为0
  //   指令字
  //   戳工具置1进入计数暂停模式，ctrl+k时钟自动运行到对应节拍暂停
  //   ctrl+k关闭时钟连续运行，将控制位置零，进入单步调试模式调试
  //   rs1
  //   rs2
  //   rd
  //   imm-lw
  //   imm-sw
  //   imm-b
  //   imm-jal
  //   可计数暂停的时钟源
  //   JAL
  //   JALR
  //   URET
  //   lbu
  //   bltu
  //   Beq
  //   Bne
  //   MemToReg
  //   MemWrite
  //   AluOP
  //   AluSrcB
  //   RegWrite
  //   注意：测试流水线时，需将寄存器堆改为下跳沿触发
  //   为方便自动评测，需要输出流水线各段保存的PC值，注意是PC不是PC+4，另外ID段寄存器写入信息，Mem段内存写入信息也要输出
  //   R[rs1]
  //   R[rs2]
  //   数据存储器
endmodule

module \中断按键参考电路  (
  input  \同步清零信号 ,
  output \与中断屏蔽位与 
);

  wire \_1号中断_out , and_1_out, clock_1_out, d_ff_1_q, or_1_out, or_2_out;

  Clock #(.highDuration(1), .lowDuration(1)) clock_1 (.out(clock_1_out));
  Button \_1号中断  (.out(\_1号中断_out ));
  LED #(.active("true")) \_1号中断等待指示灯  (.in(or_1_out));
  or or_1 (or_1_out, \与中断屏蔽位与 , d_ff_1_q);
  D_Flip_Flop #(.trigger("rising"), .Pre_Clr_Positions("LEGACY"), .NegatePresetClear("false"), .enable("true"), .NewFFLayout("false")) d_ff_1 (
    .clk(\_1号中断_out ), .D(1'b1), .Q(d_ff_1_q), .reset(\与中断屏蔽位与 ));  // open: Qn, preset, en
  or or_2 (or_2_out, d_ff_1_q, \与中断屏蔽位与 );
  and and_1 (and_1_out, or_2_out, ~\同步清零信号 );  // AND_Gate
  D_Flip_Flop #(.trigger("rising"), .Pre_Clr_Positions("LEGACY"), .NegatePresetClear("false"), .enable("true"), .NewFFLayout("false")) IR1 (
    .clk(clock_1_out), .D(and_1_out), .Q(\与中断屏蔽位与 ));  // open: Qn, preset, en, reset

  // Notes on the sheet:
  //   中断信号采样参考电路
  //   Reset 
endmodule
module \单周期_单级中断  (
  input  IR1,
  input  IR2,
  input  IR3,
  output RegWrite,
  output MemWrite,
  output [31:0] PC,
  output [31:0] IR,
  output [31:0] RDin,
  output [31:0] MDin,
  output [31:0] LedData
);

  wire AluSrcB, and_1_out, and_2_out, and_3_out, and_4_out, and_5_out, and_6_out, and_7_out, and_9_out,
       and_10_out, Beq, bltu, Bne, clear1, clear2, clear3, CLK, clock_2_out, comparator_1_eq,
       comparator_2_eq, comparator_3_eq, comparator_4_eq, comparator_5_eq, comparator_6_eq, comparator_6_lt,
       d_ff_2_q, decoder_1_out1, decoder_1_out2, decoder_1_out3, ecall, equal, Go, halt, IE, INT, IR1_t,
       IR2_t, IR3_t, IRA, IRB, IRC, jal, jalr, lbu, MemToReg, nand_1_out, not_1_out, not_2_out, or_1_out,
       or_2_out, or_4_out, or_6_out, or_8_out, or_11_out, or_12_out, or_13_out, register_1_q, register_2_q,
       register_3_q, register_4_q, register_5_q, register_6_q, RST, S_type, tunnel, uret, W1, W2, W3, \中断信号 ;
  wire [1:0] PCSrc, register_7_q, \中断号 ;
  wire [1:1] or_15_out;
  wire [3:0] AluOp;
  wire [4:0] multiplexer_4_out, multiplexer_5_out;
  wire [7:0] multiplexer_10_out;
  wire [11:0] multiplexer_6_out;
  wire [12:0] CNT_num;
  wire [15:0] \总周期数 ;
  wire [31:0] ALU_result, bit_extender_1_out, bit_extender_2_out, bit_extender_3_out, bit_extender_4_out,
       \b分支 , INT_PC, \jal分支 , MDout, multiplexer_2_out, multiplexer_3_out, multiplexer_8_out,
       multiplexer_11_out, PC_4, regifile_1_r1, RET_PC, shifter_1_out, shifter_2_out, \断点 ;

  Clock #(.highDuration(1), .lowDuration(1)) clock_1 ();  // open: out
  Button _1 ();  // open: out
  Button _2 ();  // open: out
  Button _3 ();  // open: out
  Button \u_继续运行  (.out(Go));
  LED #(.active("true")) led_1 (.in(W1));
  LED #(.active("true")) led_2 (.in(W2));
  LED #(.active("true")) led_3 (.in(W3));
  Hex_Digit_Display hex_digit_display_1 (.value(LedData[31:28]));  // open: dp
  and and_1 (and_1_out, Beq, equal);
  and and_2 (and_2_out, ~equal, Bne);  // AND_Gate
  and and_3 (and_3_out, bltu, tunnel);
  Multiplexer #(.select(2), .width(32), .disabled("Z"), .enable("false")) multiplexer_1 (
    .in0(PC_4), .in1(ALU_result), .in2(\jal分支 ), .in3(\b分支 ), .out(\断点 ), .sel(PCSrc));
  Hex_Digit_Display hex_digit_display_2 (.value(LedData[27:24]));  // open: dp
  Hex_Digit_Display hex_digit_display_3 (.value(LedData[23:20]));  // open: dp
  Comparator #(.width(16), .mode("twosComplement")) comparator_1 (
    .a(16'h23b), .b(\总周期数 ), .eq(comparator_1_eq));  // open: gt, lt
  Comparator #(.width(16), .mode("twosComplement")) comparator_2 (
    .a(\总周期数 ), .b(16'h1), .eq(comparator_2_eq));  // open: gt, lt
  Comparator #(.width(16), .mode("twosComplement")) comparator_3 (
    .a(\总周期数 ), .b(16'h4), .eq(comparator_3_eq));  // open: gt, lt
  Comparator #(.width(16), .mode("twosComplement")) comparator_4 (
    .a(\总周期数 ), .b(16'h7), .eq(comparator_4_eq));  // open: gt, lt
  or or_1 (or_1_out, and_1_out, and_2_out, and_3_out);
  Multiplexer #(.select(1), .width(32), .disabled("Z"), .enable("false")) multiplexer_2 (
    .in0(\断点 ), .in1(INT_PC), .out(multiplexer_2_out), .sel(INT));
  Hex_Digit_Display hex_digit_display_4 (.value(LedData[15:12]));  // open: dp
  Hex_Digit_Display hex_digit_display_5 (.value(LedData[19:16]));  // open: dp
  or or_2 (or_2_out, comparator_1_eq, comparator_2_eq);
  assign IRA = or_2_out ? ~CLK : 1'bz;  // Controlled_Inverter controlled_inverter_1
  assign IRB = comparator_3_eq ? ~CLK : 1'bz;  // Controlled_Inverter controlled_inverter_2
  assign IRC = comparator_4_eq ? ~CLK : 1'bz;  // Controlled_Inverter controlled_inverter_3
  Priority_Encoder #(.select(2), .disabled("Z")) priority_encoder_1 (
    .in0(1'b1), .in1(jalr), .in2(jal), .in3(or_1_out), .out(PCSrc));  // open: gs, en_out, en_in
  Multiplexer #(.select(1), .width(32), .disabled("Z"), .enable("false")) multiplexer_3 (
    .in0(multiplexer_2_out), .in1(RET_PC), .out(multiplexer_3_out), .sel(uret));
  Hex_Digit_Display hex_digit_display_6 (.value(LedData[11:8]));  // open: dp
  Hex_Digit_Display hex_digit_display_7 (.value(LedData[7:4]));  // open: dp
  // Probe on \总周期数 
  Pull_Resistor #(.pull(0)) pull_resistor_1 (.node(IRA));
  Pull_Resistor #(.pull(0)) pull_resistor_2 (.node(IRB));
  Pull_Resistor #(.pull(0)) pull_resistor_3 (.node(IRC));
  not not_1 (not_1_out, halt);
  Hex_Digit_Display hex_digit_display_8 (.value(LedData[3:0]));  // open: dp
  Register #(.width(32), .trigger("rising"), .Select("low")) u_PC (
    .D(multiplexer_3_out), .en(not_1_out), .Q(PC), .clk(CLK), .clr(RST));
  // Probe on PC
  Adder #(.width(32)) adder_1 (.a(PC), .b(32'h4), .out(PC_4));  // open: cin, cout
  or or_3 (IR1_t, IR1, IRA);
  Register #(.width(1), .trigger("rising"), .Select("low")) register_1 (
    .D(1'b1), .Q(register_1_q), .clk(IR1_t), .clr(or_4_out));  // open: en
  or or_4 (or_4_out, register_4_q, RST);
  or or_5 (W1, register_4_q, register_1_q);
  or or_6 (or_6_out, register_5_q, RST);
  or or_7 (W2, register_5_q, register_2_q);
  or or_8 (or_8_out, register_6_q, RST);
  or or_9 (W3, register_6_q, register_3_q);
  or or_10 (IR2_t, IR2, IRB);
  or or_11 (or_11_out, register_1_q, register_4_q);
  Register #(.width(1), .trigger("rising"), .Select("low")) register_2 (
    .D(1'b1), .Q(register_2_q), .clk(IR2_t), .clr(or_6_out));  // open: en
  Register #(.width(1), .trigger("rising"), .Select("low")) register_3 (
    .D(1'b1), .Q(register_3_q), .clk(IR3_t), .clr(or_8_out));  // open: en
  // RiscV_Probe riscv_probe_1: pin names not known; wires that end beside it: IR, 5'b10001
  and and_4 (and_4_out, or_11_out, ~clear1);  // AND_Gate
  or or_12 (or_12_out, register_2_q, register_5_q);
  or or_13 (or_13_out, register_3_q, register_6_q);
  ROM #(.addrWidth(10), .dataWidth(32), .Select("high")) rom_1 (.addr(PC[11:2]), .data(IR));
  or or_14 (IR3_t, IR3, IRC);
  Register #(.width(1), .trigger("rising"), .Select("low")) register_4 (
    .D(and_4_out), .Q(register_4_q), .clk(CLK), .clr(RST));  // open: en
  Register #(.width(1), .trigger("rising"), .Select("low")) register_5 (
    .D(and_5_out), .Q(register_5_q), .clk(CLK), .clr(RST));  // open: en
  and and_5 (and_5_out, or_12_out, ~clear2);  // AND_Gate
  and and_6 (and_6_out, or_13_out, ~clear3);  // AND_Gate
  Register #(.width(1), .trigger("rising"), .Select("low")) register_6 (
    .D(and_6_out), .Q(register_6_q), .clk(CLK), .clr(RST));  // open: en
  \单周期硬布线控制器  \u_单周期硬布线控制器_1  (
    .Funct({IR[30], IR[25], IR[14:12]}), .OP(IR[6:2]), .ALU_OP(AluOp), .MemToReg(MemToReg),
    .MemWrite(MemWrite), .ALU_SRC(AluSrcB), .RegWrite(RegWrite), .ecall(ecall), .S_type(S_type), .Jalr(jalr),
    .Beq(Beq), .JAL(jal), .Bne(Bne), .in_3(IR[21]), .uret(uret), .lbu(lbu), .bltu(bltu));  // open: Rs1Used, Rs2Used, csrrsi, csrrci
  Multiplexer #(.select(1), .width(5), .disabled("Z"), .enable("false")) multiplexer_4 (
    .in0(IR[19:15]), .in1(5'b10001), .out(multiplexer_4_out), .sel(ecall));
  Multiplexer #(.select(1), .width(5), .disabled("Z"), .enable("false")) multiplexer_5 (
    .in0(IR[24:20]), .in1(5'b01010), .out(multiplexer_5_out), .sel(ecall));
  Multiplexer #(.select(1), .width(12), .disabled("Z"), .enable("false")) multiplexer_6 (
    .in0(IR[31:20]), .in1({IR[31:25], IR[11:7]}), .out(multiplexer_6_out), .sel(S_type));
  assign bit_extender_1_out = {{20{multiplexer_6_out[11]}}, multiplexer_6_out};  // Bit_Extender bit_extender_1
  assign bit_extender_2_out = {{20{IR[31]}}, {IR[31], IR[7], IR[30:25], IR[11:8]}};  // Bit_Extender bit_extender_2
  assign bit_extender_3_out = {{12{IR[31]}}, {IR[31], IR[19:12], IR[20], IR[30:21]}};  // Bit_Extender bit_extender_3
  Priority_Encoder #(.select(2), .disabled("Z")) priority_encoder_2 (
    .in1(register_4_q), .in2(register_5_q), .in3(register_6_q), .out(\中断号 ), .gs(\中断信号 ));  // open: in0, en_out, en_in
  // Probe on multiplexer_4_out
  // Probe on multiplexer_5_out
  // Probe on IR[11:7]
  Shifter #(.width(32), .shift("ll")) shifter_1 (.in(bit_extender_2_out), .\dist (5'b00001), .out(shifter_1_out));
  Shifter #(.width(32), .shift("ll")) shifter_2 (.in(bit_extender_3_out), .\dist (5'b00001), .out(shifter_2_out));
  Adder #(.width(32)) adder_2 (.a(shifter_1_out), .b(PC), .out(\b分支 ));  // open: cin, cout
  Adder #(.width(32)) adder_3 (.a(shifter_2_out), .b(PC), .out(\jal分支 ));  // open: cin, cout
  Multiplexer #(.select(2), .width(32), .disabled("Z"), .enable("false")) multiplexer_7 (
    .in1(32'h30ac), .in2(32'h3150), .in3(32'h31f4), .out(INT_PC), .sel(\中断号 ));  // open: in0
  and and_7 (and_7_out, \中断信号 , ~uret);  // AND_Gate
  Regifile regifile_1 (
    .Din(RDin), .Clk(CLK), .R1(regifile_1_r1), .R2(MDin), .WE(RegWrite), .W_num(IR[11:7]),
    .R1_num(multiplexer_4_out), .R2_num(multiplexer_5_out));
  and and_8 (INT, \中断信号 , IE);
  D_Flip_Flop #(.trigger("rising"), .Pre_Clr_Positions("LEGACY"), .NegatePresetClear("false"), .enable("true"), .NewFFLayout("false")) d_ff_1 (
    .clk(CLK), .D(and_7_out), .Qn(IE));  // open: Q, preset, en, reset
  not not_2 (not_2_out, halt);
  Counter #(.width(16), .max('hffff), .ongoal("wrap"), .trigger("falling"), .behavior("new")) counter_1 (
    .count(not_2_out), .Q(\总周期数 ), .clk(CLK), .clr(RST));  // open: load, D, carry, preset, down
  Multiplexer #(.select(1), .width(32), .disabled("Z"), .enable("false")) multiplexer_8 (
    .in0(MDin), .in1(bit_extender_1_out), .out(multiplexer_8_out), .sel(AluSrcB));
  Comparator #(.width(32), .mode("twosComplement")) comparator_5 (
    .a(regifile_1_r1), .b(32'h22), .eq(comparator_5_eq));  // open: gt, lt
  Register #(.width(2), .trigger("rising"), .Select("low")) register_7 (
    .D(\中断号 ), .en(INT), .Q(register_7_q), .clk(CLK), .clr(RST));
  ALU alu_1 (
    .X(regifile_1_r1), .Y(multiplexer_8_out), .AluOP(AluOp), .Equal(equal), .Result(ALU_result),
    .out_6(tunnel));  // open: Result_2, out_4
  and and_9 (and_9_out, ecall, ~comparator_5_eq);  // AND_Gate
  Register #(.width(32), .trigger("rising"), .Select("low")) register_8 (
    .D(MDin), .en(and_10_out), .Q(LedData), .clk(CLK));  // open: clr
  and and_10 (and_10_out, comparator_5_eq, ecall);
  Button button_1 (.out(RST));
  Decoder #(.select(2), .tristate("false"), .disabled("Z"), .enable("false")) decoder_1 (
    .out1(decoder_1_out1), .out2(decoder_1_out2), .out3(decoder_1_out3), .sel(register_7_q));  // open: out0
  Register #(.width(32), .trigger("rising"), .Select("low")) mEPC (
    .D(\断点 ), .en(INT), .Q(RET_PC), .clk(CLK), .clr(RST));
  Multiplexer #(.select(1), .width(1), .disabled("Z"), .enable("false")) multiplexer_9 (
    .in0(and_9_out), .in1(1'b0), .out(halt), .sel(Go));
  D_Flip_Flop #(.trigger("high"), .Pre_Clr_Positions("LEGACY"), .NegatePresetClear("false"), .enable("true"), .NewFFLayout("false")) d_ff_2 (.Q(d_ff_2_q));  // open: clk, D, Qn, preset, en, reset
  // Probe on 13'hbb
  and and_11 (clear1, decoder_1_out1, uret);
  and and_12 (clear2, decoder_1_out2, uret);
  and and_13 (clear3, decoder_1_out3, uret);
  Comparator #(.width(13), .mode("twosComplement")) comparator_6 (
    .a(CNT_num), .b(13'hbb), .eq(comparator_6_eq), .lt(comparator_6_lt));  // open: gt
  Clock #(.highDuration(1), .lowDuration(1)) clock_2 (.out(clock_2_out));
  Multiplexer #(.select(2), .width(8), .disabled("Z"), .enable("false")) multiplexer_10 (
    .in0(MDout[7:0]), .in1(MDout[15:8]), .in2(MDout[23:16]), .in3(MDout[31:24]), .out(multiplexer_10_out),
    .sel(ALU_result[1:0]));
  RAM #(.addrWidth(10), .dataWidth(32), .bus("separate"), .Select("high")) ram_1 (
    .addr(ALU_result[11:2]), .din(MDin), .data(MDout), .str(MemWrite), .clk(CLK));  // open: sel, ld, clr
  Counter #(.width(13), .max('h1fff), .ongoal("stay"), .trigger("rising"), .behavior("old")) counter_2 (
    .count(comparator_6_lt), .Q(CNT_num), .clk(clock_2_out));  // open: load, D, carry, clr, preset
  assign bit_extender_4_out = {{24{1'b0}}, multiplexer_10_out};  // Bit_Extender bit_extender_4
  Multiplexer #(.select(1), .width(32), .disabled("Z"), .enable("false")) multiplexer_11 (
    .in0(MDout), .in1(bit_extender_4_out), .out(multiplexer_11_out), .sel(lbu));
  nand nand_1 (nand_1_out, d_ff_2_q, comparator_6_eq);
  Multiplexer #(.select(2), .width(32), .disabled("Z"), .enable("false")) multiplexer_12 (
    .in0(ALU_result), .in1(multiplexer_11_out), .in2(PC_4), .out(RDin), .sel({or_15_out[1], MemToReg}));  // open: in3
  assign CLK = nand_1_out ? clock_2_out : 1'bz;  // Controlled_Buffer controlled_buffer_1
  Pull_Resistor #(.pull(1)) pull_resistor_4 (.node(CLK));
  or or_15 (or_15_out[1], jal, jalr);

  // Notes on the sheet:
  //   中断源
  //   中断等待指示
  //   总复位信号应将除ROM以外所有存储组件全部清零
  //   单级中断测试信号模拟器
  //   数码管输出
  //   数码管输出应该用寄存器锁存，否则显示数据只能一闪而过
  //   指令探针
  //   指令存储器
  //   rs1
  //   rs2
  //   指令字
  //   contents of rom_1 (hex, n*v repeats v):
  //   7d000113 100413 1f41993 41f9d993 433 c00913 800b13 140413 f47413 800293 100313 499993 89e9b3 1300533
  //   2200893 73 406282b3 fe0294e3 140413 f00f93 1f47433 1c41413 800293 100313 49d993 89e9b3 1300533
  //   2200893 73 406282b3 fe0294e3 1c45413 406b0b33 b0463 f95ff06f 2b3 fff2c293 1029293 fff2e293 500533
  //   2200893 73 f5dff06f 1112023 410113 a12023 410113 812023 410113 1312023 410113 1412023 410113 1512023
  //   410113 1612023 410113 100b13 300a13 100a93 1600433 441413 14469b3 1300533 2200893 73 fe0416e3
  //   415a0a33 fe0a10e3 ffc10113 12b03 ffc10113 12a83 ffc10113 12a03 ffc10113 12983 ffc10113 12403
  //   ffc10113 12503 ffc10113 12883 200073 1112023 410113 a12023 410113 812023 410113 1312023 410113
  //   1412023 410113 1512023 410113 1612023 410113 200b13 300a13 100a93 1600433 441413 14469b3 1300533
  //   2200893 73 fe0416e3 415a0a33 fe0a10e3 ffc10113 12b03 ffc10113 12a83 ffc10113 12a03 ffc10113 12983
  //   ffc10113 12403 ffc10113 12503 ffc10113 12883 200073 1112023 410113 a12023 410113 812023 410113
  //   1312023 410113 1412023 410113 1512023 410113 1612023 410113 300b13 300a13 100a93 1600433 441413
  //   14469b3 1300533 2200893 73 fe0416e3 415a0a33 fe0a10e3 ffc10113 12b03 ffc10113 12a83 ffc10113 12a03
  //   ffc10113 12983 ffc10113 12403 ffc10113 12503 ffc10113 12883 200073
  //   rd
  //   JAL
  //   JALR
  //   URET
  //   lbu
  //   bltu
  //   imm-lw
  //   imm-sw
  //   imm-b
  //   imm-jal
  //   Beq
  //   Bne
  //   AluOP
  //   AluSrcB
  //   RegWrite
  //   MemToReg
  //   MemWrite
  //   为方便自动评测，需要输出PC，IR，寄存器堆写如数据RDin
  //   RAM写使能MemWrite、RAM写入数据MDin等信号
  //   注意：测试单周期+单级中断时，需将寄存器堆改为上跳沿触发
  //   R[rs1]
  //   R[rs2]
  //   控制位
  //   暂停节拍，不能为0
  //   数据存储器
  //   戳工具置1进入计数暂停模式，ctrl+k时钟自动运行到对应节拍暂停
  //   ctrl+k关闭时钟连续运行，将控制位置零，进入单步调试模式调试
  //   用这个时钟源需要去掉电路中的其他时钟源
  //   可计数暂停的时钟源
endmodule

module \单周期_多级中断  (
  input  IR1,
  input  IR2,
  input  IR3,
  output RegWrite,
  output MemWrite,
  output [31:0] PC,
  output [31:0] IR,
  output [31:0] RDin,
  output [31:0] MDin,
  output [31:0] LedData
);

  wire AluSrcB, and_1_out, and_2_out, and_3_out, and_4_out, and_6_out, and_7_out, and_8_out, and_9_out,
       and_10_out, and_11_out, and_12_out, and_13_out, and_14_out, and_15_out, and_16_out, Beq, bltu, Bne,
       clear1, clear2, clear3, CLK, clock_2_out, comparator_1_eq, comparator_2_eq, comparator_3_eq,
       comparator_4_eq, comparator_5_eq, comparator_7_eq, comparator_8_eq, comparator_8_lt, csrrci, csrrsi,
       d_ff_1_q, d_ff_3_q, decoder_1_out1, decoder_1_out2, decoder_1_out3, decoder_2_out1, decoder_2_out2,
       decoder_2_out3, decoder_3_out1, decoder_3_out2, decoder_3_out3, ecall, equal, flag1_q, flag2_q,
       flag3_q, Go, halt, IE, INT, IR1_t, IR2_t, IR3_t, IRA, IRB, IRC, jal, jalr, lbu, MemToReg, nand_1_out,
       not_1_out, not_2_out, not_3_out, not_4_out, not_5_out, or_1_out, or_2_out, or_3_out, or_4_out,
       or_5_out, or_11_out, or_12_out, or_13_out, or_14_out, or_15_out, or_16_out, or_19_out, register_1_q,
       register_2_q, register_3_q, register_4_q, register_5_q, register_6_q, RST, S_type, tunnel, uret, W1,
       W2, W3, \中断信号 , \存在更高优先级中断 ;
  wire [1:0] PCSrc, \中断号 , \当前运行中断号 ;
  wire [1:1] or_20_out;
  wire [3:0] AluOp;
  wire [4:0] multiplexer_4_out, multiplexer_5_out;
  wire [7:0] multiplexer_11_out;
  wire [11:0] multiplexer_6_out;
  wire [12:0] CNT_num;
  wire [15:0] \总周期数 ;
  wire [31:0] ALU_result, bit_extender_1_out, bit_extender_2_out, bit_extender_3_out, bit_extender_4_out,
       \b分支 , INT_PC, \jal分支 , MDout, mEPC1_q, mEPC2_q, mEPC3_q, multiplexer_2_out, multiplexer_3_out,
       multiplexer_8_out, multiplexer_12_out, PC_4, regifile_1_r1, RET_PC, shifter_1_out, shifter_2_out,
       tunnel_t, \断点 ;

  Clock #(.highDuration(1), .lowDuration(1)) clock_1 ();  // open: out
  Button _1 ();  // open: out
  Button _2 ();  // open: out
  Button _3 ();  // open: out
  Button \u_继续运行  (.out(Go));
  LED #(.active("true")) led_1 (.in(W1));
  LED #(.active("true")) led_2 (.in(W2));
  LED #(.active("true")) led_3 (.in(W3));
  Hex_Digit_Display hex_digit_display_1 (.value(LedData[31:28]));  // open: dp
  Comparator #(.width(16), .mode("twosComplement")) comparator_1 (
    .a(\总周期数 ), .b(16'h7), .eq(comparator_1_eq));  // open: gt, lt
  Comparator #(.width(16), .mode("twosComplement")) comparator_2 (
    .a(\总周期数 ), .b(16'h241), .eq(comparator_2_eq));  // open: gt, lt
  and and_1 (and_1_out, ~csrrsi, ~uret);  // AND_Gate
  or or_1 (or_1_out, d_ff_1_q, csrrci);
  D_Flip_Flop #(.trigger("falling"), .Pre_Clr_Positions("LEGACY"), .NegatePresetClear("false"), .enable("true"), .NewFFLayout("false")) d_ff_1 (
    .clk(INT), .D(1'b1), .Q(d_ff_1_q), .reset(csrrsi));  // open: Qn, preset, en
  Hex_Digit_Display hex_digit_display_2 (.value(LedData[27:24]));  // open: dp
  Hex_Digit_Display hex_digit_display_3 (.value(LedData[23:20]));  // open: dp
  Comparator #(.width(16), .mode("twosComplement")) comparator_3 (
    .a(16'h258), .b(\总周期数 ), .eq(comparator_3_eq));  // open: gt, lt
  or or_2 (or_2_out, comparator_3_eq, comparator_4_eq);
  Comparator #(.width(16), .mode("twosComplement")) comparator_4 (
    .a(\总周期数 ), .b(16'h1), .eq(comparator_4_eq));  // open: gt, lt
  Comparator #(.width(16), .mode("twosComplement")) comparator_5 (
    .a(\总周期数 ), .b(16'h4), .eq(comparator_5_eq));  // open: gt, lt
  or or_3 (or_3_out, comparator_1_eq, comparator_2_eq);
  D_Flip_Flop #(.trigger("rising"), .Pre_Clr_Positions("LEGACY"), .NegatePresetClear("false"), .enable("true"), .NewFFLayout("false")) d_ff_2 (
    .clk(CLK), .D(and_1_out), .Qn(IE), .preset(or_1_out), .en(or_4_out));  // open: Q, reset
  or or_4 (or_4_out, csrrsi, uret);
  and and_2 (and_2_out, Beq, equal);
  and and_3 (and_3_out, ~equal, Bne);  // AND_Gate
  and and_4 (and_4_out, bltu, tunnel);
  Multiplexer #(.select(2), .width(32), .disabled("Z"), .enable("false")) multiplexer_1 (
    .in0(PC_4), .in1(ALU_result), .in2(\jal分支 ), .in3(\b分支 ), .out(\断点 ), .sel(PCSrc));
  Hex_Digit_Display hex_digit_display_4 (.value(LedData[15:12]));  // open: dp
  Hex_Digit_Display hex_digit_display_5 (.value(LedData[19:16]));  // open: dp
  Pull_Resistor #(.pull(0)) pull_resistor_1 (.node(IRA));
  assign IRA = or_2_out ? ~CLK : 1'bz;  // Controlled_Inverter controlled_inverter_1
  Pull_Resistor #(.pull(0)) pull_resistor_2 (.node(IRB));
  assign IRB = comparator_5_eq ? ~CLK : 1'bz;  // Controlled_Inverter controlled_inverter_2
  Pull_Resistor #(.pull(0)) pull_resistor_3 (.node(IRC));
  assign IRC = or_3_out ? ~CLK : 1'bz;  // Controlled_Inverter controlled_inverter_3
  or or_5 (or_5_out, and_2_out, and_3_out, and_4_out);
  Multiplexer #(.select(1), .width(32), .disabled("Z"), .enable("false")) multiplexer_2 (
    .in0(\断点 ), .in1(INT_PC), .out(multiplexer_2_out), .sel(INT));
  Hex_Digit_Display hex_digit_display_6 (.value(LedData[11:8]));  // open: dp
  Hex_Digit_Display hex_digit_display_7 (.value(LedData[7:4]));  // open: dp
  // Probe on \总周期数 
  and and_5 (INT, IE, \存在更高优先级中断 );
  Priority_Encoder #(.select(2), .disabled("Z")) priority_encoder_1 (
    .in0(1'b1), .in1(jalr), .in2(jal), .in3(or_5_out), .out(PCSrc));  // open: gs, en_out, en_in
  Multiplexer #(.select(1), .width(32), .disabled("Z"), .enable("false")) multiplexer_3 (
    .in0(multiplexer_2_out), .in1(RET_PC), .out(multiplexer_3_out), .sel(uret));
  Hex_Digit_Display hex_digit_display_8 (.value(LedData[3:0]));  // open: dp
  not not_1 (not_1_out, halt);
  Register #(.width(32), .trigger("rising"), .Select("low")) u_PC (
    .D(multiplexer_3_out), .en(not_1_out), .Q(PC), .clk(CLK), .clr(RST));
  or or_6 (IR1_t, IR1, IRA);
  or or_7 (W1, register_4_q, register_1_q);
  or or_8 (W2, register_5_q, register_2_q);
  or or_9 (W3, register_6_q, register_3_q);
  // Probe on PC
  Adder #(.width(32)) adder_1 (.a(PC), .b(32'h4), .out(PC_4));  // open: cin, cout
  or or_10 (IR2_t, IR2, IRB);
  Register #(.width(1), .trigger("rising"), .Select("low")) register_1 (
    .D(1'b1), .Q(register_1_q), .clk(IR1_t), .clr(or_11_out));  // open: en
  or or_11 (or_11_out, register_4_q, RST);
  Register #(.width(1), .trigger("rising"), .Select("low")) register_2 (
    .D(1'b1), .Q(register_2_q), .clk(IR2_t), .clr(or_12_out));  // open: en
  or or_12 (or_12_out, register_5_q, RST);
  Register #(.width(1), .trigger("rising"), .Select("low")) register_3 (
    .D(1'b1), .Q(register_3_q), .clk(IR3_t), .clr(or_13_out));  // open: en
  or or_13 (or_13_out, register_6_q, RST);
  or or_14 (or_14_out, register_1_q, register_4_q);
  or or_15 (or_15_out, register_2_q, register_5_q);
  or or_16 (or_16_out, register_3_q, register_6_q);
  // RiscV_Probe riscv_probe_1: pin names not known; wires that end beside it: IR, tunnel_t, 5'b10001
  or or_17 (IR3_t, IR3, IRC);
  and and_6 (and_6_out, or_14_out, ~clear1);  // AND_Gate
  and and_7 (and_7_out, or_15_out, ~clear2);  // AND_Gate
  and and_8 (and_8_out, or_16_out, ~clear3);  // AND_Gate
  ROM #(.addrWidth(10), .dataWidth(32), .Select("high")) rom_1 (.addr(PC[11:2]), .data(IR));
  Register #(.width(1), .trigger("rising"), .Select("low")) register_4 (
    .D(and_6_out), .Q(register_4_q), .clk(CLK), .clr(RST));  // open: en
  Register #(.width(1), .trigger("rising"), .Select("low")) register_5 (
    .D(and_7_out), .Q(register_5_q), .clk(CLK), .clr(RST));  // open: en
  Register #(.width(1), .trigger("rising"), .Select("low")) register_6 (
    .D(and_8_out), .Q(register_6_q), .clk(CLK), .clr(RST));  // open: en
  \单周期硬布线控制器  \u_单周期硬布线控制器_1  (
    .Funct({IR[30], IR[25], IR[14:12]}), .OP(IR[6:2]), .ALU_OP(AluOp), .MemToReg(MemToReg),
    .MemWrite(MemWrite), .ALU_SRC(AluSrcB), .RegWrite(RegWrite), .ecall(ecall), .S_type(S_type), .Jalr(jalr),
    .Beq(Beq), .JAL(jal), .Bne(Bne), .in_3(IR[21]), .uret(uret), .lbu(lbu), .bltu(bltu), .csrrsi(csrrsi),
    .csrrci(csrrci));  // open: Rs1Used, Rs2Used
  Multiplexer #(.select(1), .width(5), .disabled("Z"), .enable("false")) multiplexer_4 (
    .in0(IR[19:15]), .in1(5'b10001), .out(multiplexer_4_out), .sel(ecall));
  Multiplexer #(.select(1), .width(5), .disabled("Z"), .enable("false")) multiplexer_5 (
    .in0(IR[24:20]), .in1(5'b01010), .out(multiplexer_5_out), .sel(ecall));
  assign bit_extender_1_out = {{20{multiplexer_6_out[11]}}, multiplexer_6_out};  // Bit_Extender bit_extender_1
  Multiplexer #(.select(1), .width(12), .disabled("Z"), .enable("false")) multiplexer_6 (
    .in0(IR[31:20]), .in1({IR[31:25], IR[11:7]}), .out(multiplexer_6_out), .sel(S_type));
  assign bit_extender_2_out = {{20{IR[31]}}, {IR[31], IR[7], IR[30:25], IR[11:8]}};  // Bit_Extender bit_extender_2
  assign bit_extender_3_out = {{12{IR[31]}}, {IR[31], IR[19:12], IR[20], IR[30:21]}};  // Bit_Extender bit_extender_3
  Priority_Encoder #(.select(2), .disabled("Z")) priority_encoder_2 (
    .in0(1'b1), .in1(register_4_q), .in2(register_5_q), .in3(register_6_q), .out(\中断号 ));  // open: gs, en_out, en_in
  or or_18 (\中断信号 , register_4_q, register_5_q, register_6_q);
  // Probe on multiplexer_4_out
  // Probe on multiplexer_5_out
  // Probe on IR[11:7]
  Shifter #(.width(32), .shift("ll")) shifter_1 (.in(bit_extender_2_out), .\dist (5'b00001), .out(shifter_1_out));
  Shifter #(.width(32), .shift("ll")) shifter_2 (.in(bit_extender_3_out), .\dist (5'b00001), .out(shifter_2_out));
  Decoder #(.select(2), .tristate("false"), .disabled("Z"), .enable("false")) decoder_1 (
    .out1(decoder_1_out1), .out2(decoder_1_out2), .out3(decoder_1_out3), .sel(\中断号 ));  // open: out0
  Adder #(.width(32)) adder_2 (.a(shifter_1_out), .b(PC), .out(\b分支 ));  // open: cin, cout
  Adder #(.width(32)) adder_3 (.a(shifter_2_out), .b(PC), .out(\jal分支 ));  // open: cin, cout
  Multiplexer #(.select(2), .width(32), .disabled("Z"), .enable("false")) multiplexer_7 (
    .in1(32'h30ac), .in2(32'h3158), .in3(32'h3204), .out(INT_PC), .sel(\中断号 ));  // open: in0
  Regifile regifile_1 (
    .Din(RDin), .Clk(CLK), .R1(regifile_1_r1), .R2(MDin), .WE(RegWrite), .W_num(IR[11:7]),
    .R1_num(multiplexer_4_out), .R2_num(multiplexer_5_out));
  Comparator #(.width(2), .mode("unsigned")) comparator_6 (.a(\中断号 ), .b(\当前运行中断号 ), .gt(\存在更高优先级中断 ));  // open: eq, lt
  and and_9 (and_9_out, INT, decoder_1_out1);
  and and_10 (and_10_out, decoder_1_out2, INT);
  and and_11 (and_11_out, decoder_1_out3, INT);
  not not_2 (not_2_out, halt);
  Counter #(.width(16), .max('hffff), .ongoal("wrap"), .trigger("falling"), .behavior("new")) counter_1 (
    .count(not_2_out), .Q(\总周期数 ), .clk(CLK), .clr(RST));  // open: load, D, carry, preset, down
  Register #(.width(32), .trigger("rising"), .Select("low")) mEPC1 (
    .D(\断点 ), .en(and_9_out), .Q(mEPC1_q), .clk(CLK), .clr(RST));
  Register #(.width(32), .trigger("rising"), .Select("low")) mEPC2 (
    .D(\断点 ), .en(and_10_out), .Q(mEPC2_q), .clk(CLK), .clr(RST));
  Register #(.width(32), .trigger("rising"), .Select("low")) mEPC3 (
    .D(\断点 ), .en(and_11_out), .Q(mEPC3_q), .clk(CLK), .clr(RST));
  Multiplexer #(.select(1), .width(32), .disabled("Z"), .enable("false")) multiplexer_8 (
    .in0(MDin), .in1(bit_extender_1_out), .out(multiplexer_8_out), .sel(AluSrcB));
  Comparator #(.width(32), .mode("twosComplement")) comparator_7 (
    .a(regifile_1_r1), .b(32'h22), .eq(comparator_7_eq));  // open: gt, lt
  Button button_1 (.out(RST));
  Multiplexer #(.select(2), .width(32), .disabled("Z"), .enable("false")) multiplexer_9 (
    .in1(mEPC1_q), .in2(mEPC2_q), .in3(mEPC3_q), .out(RET_PC), .sel(\当前运行中断号 ));  // open: in0
  ALU alu_1 (
    .X(regifile_1_r1), .Y(multiplexer_8_out), .AluOP(AluOp), .Equal(equal), .Result(ALU_result),
    .out_6(tunnel));  // open: Result_2, out_4
  and and_12 (and_12_out, ecall, ~comparator_7_eq);  // AND_Gate
  Register #(.width(32), .trigger("rising"), .Select("low")) register_7 (
    .D(MDin), .en(and_13_out), .Q(LedData), .clk(CLK));  // open: clr
  and and_13 (and_13_out, comparator_7_eq, ecall);
  Multiplexer #(.select(1), .width(1), .disabled("Z"), .enable("false")) multiplexer_10 (
    .in0(and_12_out), .in1(1'b0), .out(halt), .sel(Go));
  D_Flip_Flop #(.trigger("high"), .Pre_Clr_Positions("LEGACY"), .NegatePresetClear("false"), .enable("true"), .NewFFLayout("false")) d_ff_3 (.Q(d_ff_3_q));  // open: clk, D, Qn, preset, en, reset
  // Probe on 13'hcd
  or or_19 (or_19_out, INT, uret);
  Decoder #(.select(2), .tristate("false"), .disabled("Z"), .enable("false")) decoder_2 (
    .out1(decoder_2_out1), .out2(decoder_2_out2), .out3(decoder_2_out3), .sel(\中断号 ));  // open: out0
  Comparator #(.width(13), .mode("twosComplement")) comparator_8 (
    .a(CNT_num), .b(13'hcd), .eq(comparator_8_eq), .lt(comparator_8_lt));  // open: gt
  Clock #(.highDuration(1), .lowDuration(1)) clock_2 (.out(clock_2_out));
  and and_14 (and_14_out, or_19_out, decoder_2_out1);
  and and_15 (and_15_out, or_19_out, decoder_2_out2);
  and and_16 (and_16_out, or_19_out, decoder_2_out3);
  Counter #(.width(13), .max('h1fff), .ongoal("stay"), .trigger("rising"), .behavior("old")) counter_2 (
    .count(comparator_8_lt), .Q(CNT_num), .clk(clock_2_out));  // open: load, D, carry, clr, preset
  not not_3 (not_3_out, clear1);
  not not_4 (not_4_out, clear2);
  not not_5 (not_5_out, clear3);
  Multiplexer #(.select(2), .width(8), .disabled("Z"), .enable("false")) multiplexer_11 (
    .in0(MDout[7:0]), .in1(MDout[15:8]), .in2(MDout[23:16]), .in3(MDout[31:24]), .out(multiplexer_11_out),
    .sel(ALU_result[1:0]));
  RAM #(.addrWidth(10), .dataWidth(32), .bus("separate"), .Select("high")) ram_1 (
    .addr(ALU_result[11:2]), .din(MDin), .data(MDout), .str(MemWrite), .clk(CLK));  // open: sel, ld, clr
  nand nand_1 (nand_1_out, d_ff_3_q, comparator_8_eq);
  Register #(.width(1), .trigger("rising"), .Select("low")) flag1 (
    .D(not_3_out), .en(and_14_out), .Q(flag1_q), .clk(CLK), .clr(RST));
  Register #(.width(1), .trigger("rising"), .Select("low")) flag2 (
    .D(not_4_out), .en(and_15_out), .Q(flag2_q), .clk(CLK), .clr(RST));
  Register #(.width(1), .trigger("rising"), .Select("low")) flag3 (
    .D(not_5_out), .en(and_16_out), .Q(flag3_q), .clk(CLK), .clr(RST));
  assign bit_extender_4_out = {{24{1'b0}}, multiplexer_11_out};  // Bit_Extender bit_extender_4
  Multiplexer #(.select(1), .width(32), .disabled("Z"), .enable("false")) multiplexer_12 (
    .in0(MDout), .in1(bit_extender_4_out), .out(multiplexer_12_out), .sel(lbu));
  assign CLK = nand_1_out ? clock_2_out : 1'bz;  // Controlled_Buffer controlled_buffer_1
  Pull_Resistor #(.pull(1)) pull_resistor_4 (.node(CLK));
  Multiplexer #(.select(2), .width(32), .disabled("Z"), .enable("false")) multiplexer_13 (
    .in0(ALU_result), .in1(multiplexer_12_out), .in2(PC_4), .out(RDin), .sel({or_20_out[1], MemToReg}));  // open: in3
  Priority_Encoder #(.select(2), .disabled("Z")) priority_encoder_3 (
    .in0(1'b1), .in1(flag1_q), .in2(flag2_q), .in3(flag3_q), .out(\当前运行中断号 ));  // open: gs, en_out, en_in
  Decoder #(.select(2), .tristate("false"), .disabled("Z"), .enable("false")) decoder_3 (
    .out1(decoder_3_out1), .out2(decoder_3_out2), .out3(decoder_3_out3), .sel(\当前运行中断号 ));  // open: out0
  or or_20 (or_20_out[1], jal, jalr);
  and and_17 (clear1, decoder_3_out1, uret);
  and and_18 (clear2, decoder_3_out2, uret);
  and and_19 (clear3, decoder_3_out3, uret);

  // Notes on the sheet:
  //   中断源
  //   中断等待指示
  //   总复位信号应将除ROM以外所有存储组件全部清零
  //   多级中断测试信号模拟器
  //   数码管输出
  //   数码管输出应该用寄存器锁存，否则显示数据只能一闪而过
  //   指令探针
  //   指令存储器
  //   rs1
  //   rs2
  //   指令字
  //   contents of rom_1 (hex, n*v repeats v):
  //   7d000113 100413 1f41993 41f9d993 433 c00913 800b13 140413 f47413 800293 100313 499993 89e9b3 1300533
  //   2200893 73 406282b3 fe0294e3 140413 f00f93 1f47433 1c41413 800293 100313 49d993 89e9b3 1300533
  //   2200893 73 406282b3 fe0294e3 1c45413 406b0b33 b0463 f95ff06f 2b3 fff2c293 1029293 fff2e293 500533
  //   2200893 73 f5dff06f 1112023 410113 a12023 410113 812023 410113 1312023 410113 1412023 410113 1512023
  //   410113 1612023 410113 40e073 100b13 300a13 100a93 1600433 441413 14469b3 1300533 2200893 73 fe0416e3
  //   415a0a33 fe0a10e3 40f073 ffc10113 12b03 ffc10113 12a83 ffc10113 12a03 ffc10113 12983 ffc10113 12403
  //   ffc10113 12503 ffc10113 12883 200073 1112023 410113 a12023 410113 812023 410113 1312023 410113
  //   1412023 410113 1512023 410113 1612023 410113 40e073 200b13 300a13 100a93 1600433 441413 14469b3
  //   1300533 2200893 73 fe0416e3 415a0a33 fe0a10e3 40f073 ffc10113 12b03 ffc10113 12a83 ffc10113 12a03
  //   ffc10113 12983 ffc10113 12403 ffc10113 12503 ffc10113 12883 200073 1112023 410113 a12023 410113
  //   812023 410113 1312023 410113 1412023 410113 1512023 410113 1612023 410113 40e073 300b13 300a13
  //   100a93 1600433 441413 14469b3 1300533 2200893 73 fe0416e3 415a0a33 fe0a10e3 40f073 ffc10113 12b03
  //   ffc10113 12a83 ffc10113 12a03 ffc10113 12983 ffc10113 12403 ffc10113 12503 ffc10113 12883 200073
  //   rd
  //   JAL
  //   JALR
  //   URET
  //   lbu
  //   bltu
  //   imm-lw
  //   imm-sw
  //   imm-b
  //   imm-jal
  //   Beq
  //   Bne
  //   AluOP
  //   AluSrcB
  //   RegWrite
  //   为方便自动评测，需要输出PC，IR，寄存器堆写如数据RDin
  //   MemToReg
  //   MemWrite
  //   RAM写使能MemWrite、RAM写入数据MDin等信号
  //   注意：测试单周期+单级中断时，需将寄存器堆改为上跳沿触发
  //   R[rs1]
  //   R[rs2]
  //   控制位
  //   暂停节拍，不能为0
  //   戳工具置1进入计数暂停模式，ctrl+k时钟自动运行到对应节拍暂停
  //   ctrl+k关闭时钟连续运行，将控制位置零，进入单步调试模式调试
  //   用这个时钟源需要去掉电路中的其他时钟源
  //   数据存储器
  //   可计数暂停的时钟源
endmodule

module \重定向流水中断  (
  input  IR1,
  input  IR2,
  input  IR3,
  output RegWrite,
  output MemWrite,
  output [31:0] IF_PC,
  output [31:0] ID_PC,
  output [31:0] EX_PC,
  output [31:0] M_PC,
  output [31:0] WB_PC,
  output [31:0] RDin,
  output [31:0] MDin,
  output [31:0] LedData
);

  wire and_1_out, and_2_out, and_3_out, and_4_out, and_5_out, and_10_out, and_11_out, and_12_out, and_14_out,
       Beq, bltu, Bne, BranchTaken, BT_1, BT_2, clear1, clear2, clear3, CLK, clock_1_out, clock_2_out,
       comparator_1_eq, comparator_2_eq, comparator_3_eq, comparator_4_eq, comparator_5_eq, comparator_5_lt,
       comparator_6_eq, d_ff_1_q, d_ff_2_q, d_ff_3_q, d_ff_4_q, d_ff_5_q, d_ff_6_q, d_ff_7_q, decoder_1_out1,
       decoder_1_out2, decoder_1_out3, ecall, equal, EX_ecall, EX_halt, EX_MEM_halt_2, EX_MEM_jal_2,
       EX_MEM_jalr_2, EX_MEM_memtoreg_2, EX_MemToReg, EX_RegWrite, EX_uret, flush, Go, halt, ID_EX_alusrcb_2,
       ID_EX_beq_2, ID_EX_bltu_2, ID_EX_bne_2, ID_EX_jal_2, ID_EX_lbu_2, ID_EX_memwrite_2, IE, INT, IR1_t,
       IR2_t, IR3_t, IRA, IRB, IRC, jal, jalr, lbu, LoadUse_1, MEM_lbu, MEM_RegWrite, mem_wb_1_halt_2,
       mem_wb_1_jal_2, mem_wb_1_jalr_2, nand_1_out, nor_1_out, nor_2_out, not_1_out, not_2_out, not_3_out,
       not_4_out, or_1_out, or_5_out, or_6_out, or_7_out, or_8_out, or_9_out, or_10_out, or_11_out,
       or_14_out, or_15_out, Rs1Used, Rs2Used, RST, S_type, stall, tunnel, uret, W1, W2, W3, \中断信号 ,
       \单周期硬布线控制器_1_alu_src , \单周期硬布线控制器_1_memtoreg , \单周期硬布线控制器_1_memwrite , \单周期硬布线控制器_1_regwrite ;
  wire [0:0] or_12_out;
  wire [1:0] ID_EX_rs1forward_2, ID_EX_rs2forward_2, mem_wb_1_memtoreg_2, PCSrc, register_1_q, Rs1Forward,
       Rs2Forward, \中断号 ;
  wire [3:0] ID_EX_aluop_2, \单周期硬布线控制器_1_alu_op ;
  wire [4:0] EX_WriteReg_num, MEM_WriteReg_num, rs1, rs2, WB_W_num;
  wire [7:0] multiplexer_14_out;
  wire [11:0] multiplexer_7_out;
  wire [12:0] CNT_num;
  wire [15:0] \LoadUse次数 , \总周期数 , \插入气泡数 , \无条件分支数 , \条件分支成功数 ;
  wire [31:0] ALU_result, bit_extender_1_out, bit_extender_2_out, bit_extender_3_out, bit_extender_4_out,
       branch_add, EX_IR, EX_PC_4, ID_EX_imm_2, ID_EX_r1_2, ID_EX_r2_2, ID_IR, ID_PC_4, IF_IR, IF_PC_4,
       INT_PC, MEM_AluResult, MEM_IR, MEM_PC_4, mem_wb_1_aluresuult_2, mem_wb_1_mdout_2, mem_wb_1_pc_4_2,
       multiplexer_1_out, multiplexer_2_out, multiplexer_3_out, multiplexer_8_out, multiplexer_9_out,
       multiplexer_10_out, multiplexer_11_out, multiplexer_12_out, multiplexer_13_out, multiplexer_15_out,
       ram_1_data, regifile_1_r1, regifile_1_r2, RET_PC, shifter_1_out, WB_IR;

  Button \u_总复位  (.out(RST));
  Button _1 ();  // open: out
  Button _2 ();  // open: out
  Button _3 ();  // open: out
  // Probe on \总周期数 
  // Probe on \总周期数 
  Button \u_继续运行  (.out(Go));
  LED #(.active("true")) led_1 (.in(W1));
  LED #(.active("true")) led_2 (.in(W2));
  LED #(.active("true")) led_3 (.in(W3));
  Hex_Digit_Display hex_digit_display_1 (.value(LedData[31:28]));  // open: dp
  // Probe on IF_PC[19:0]
  // RiscV_Probe riscv_probe_1: pin names not known; wires that end beside it: IR1_t, IR2_t, IR3_t, IF_IR
  Hex_Digit_Display hex_digit_display_2 (.value(LedData[27:24]));  // open: dp
  Hex_Digit_Display hex_digit_display_3 (.value(LedData[23:20]));  // open: dp
  // Probe on ID_PC[19:0]
  // RiscV_Probe riscv_probe_2: pin names not known; wires that end beside it: ID_IR
  Comparator #(.width(16), .mode("twosComplement")) comparator_1 (
    .a(16'h23b), .b(\总周期数 ), .eq(comparator_1_eq));  // open: gt, lt
  Comparator #(.width(16), .mode("twosComplement")) comparator_2 (
    .a(\总周期数 ), .b(16'h1), .eq(comparator_2_eq));  // open: gt, lt
  Comparator #(.width(16), .mode("twosComplement")) comparator_3 (
    .a(\总周期数 ), .b(16'h4), .eq(comparator_3_eq));  // open: gt, lt
  Comparator #(.width(16), .mode("twosComplement")) comparator_4 (
    .a(\总周期数 ), .b(16'h7), .eq(comparator_4_eq));  // open: gt, lt
  Multiplexer #(.select(2), .width(32), .disabled("Z"), .enable("false")) multiplexer_1 (
    .in0(IF_PC_4), .in1(ALU_result), .in2(branch_add), .out(multiplexer_1_out), .sel(PCSrc));  // open: in3
  Hex_Digit_Display hex_digit_display_4 (.value(LedData[19:16]));  // open: dp
  Hex_Digit_Display hex_digit_display_5 (.value(LedData[15:12]));  // open: dp
  or or_1 (or_1_out, comparator_1_eq, comparator_2_eq);
  Pull_Resistor #(.pull(0)) pull_resistor_1 (.node(IRA));
  assign IRA = or_1_out ? ~CLK : 1'bz;  // Controlled_Inverter controlled_inverter_1
  Pull_Resistor #(.pull(0)) pull_resistor_2 (.node(IRB));
  assign IRB = comparator_3_eq ? ~CLK : 1'bz;  // Controlled_Inverter controlled_inverter_2
  Pull_Resistor #(.pull(0)) pull_resistor_3 (.node(IRC));
  assign IRC = comparator_4_eq ? ~CLK : 1'bz;  // Controlled_Inverter controlled_inverter_3
  Multiplexer #(.select(1), .width(32), .disabled("Z"), .enable("false")) multiplexer_2 (
    .in0(multiplexer_1_out), .in1(INT_PC), .out(multiplexer_2_out), .sel(INT));
  Hex_Digit_Display hex_digit_display_6 (.value(LedData[11:8]));  // open: dp
  Hex_Digit_Display hex_digit_display_7 (.value(LedData[7:4]));  // open: dp
  Clock #(.highDuration(1), .lowDuration(1)) clock_1 (.out(clock_1_out));
  // Probe on EX_PC[19:0]
  // RiscV_Probe riscv_probe_3: pin names not known; wires that end beside it: clock_1_out, EX_IR, CLK
  \重定向相关处理逻辑  \u_重定向相关处理逻辑_1  (
    .Rs1Used(Rs1Used), .Rs1(rs1), .EX_WriteReg_num(EX_WriteReg_num), .EX_MemToReg(EX_MemToReg),
    .Rs2Used(Rs2Used), .Rs2(rs2), .MEM_WriteReg_num(MEM_WriteReg_num), .BranchTaken(BranchTaken),
    .EX_RegWrite(EX_RegWrite), .MEM_RegWrite(MEM_RegWrite), .ecall(ecall), .Stall(stall), .Flush(flush),
    .Rs1Foward(Rs1Forward), .Rs2Foward(Rs2Forward));
  Multiplexer #(.select(1), .width(32), .disabled("Z"), .enable("false")) multiplexer_3 (
    .in0(multiplexer_2_out), .in1(RET_PC), .out(multiplexer_3_out), .sel(EX_uret));
  nor nor_1 (nor_1_out, stall, halt);
  Hex_Digit_Display hex_digit_display_8 (.value(LedData[3:0]));  // open: dp
  Register #(.width(32), .trigger("rising"), .Select("low")) PC (
    .D(multiplexer_3_out), .en(nor_1_out), .Q(IF_PC), .clk(CLK), .clr(RST));
  // Probe on \总周期数 
  // Probe on M_PC[19:0]
  // RiscV_Probe riscv_probe_4: pin names not known; wires that end beside it: MEM_IR
  or or_2 (W1, d_ff_5_q, d_ff_1_q);
  or or_3 (W2, d_ff_6_q, d_ff_2_q);
  or or_4 (W3, d_ff_7_q, d_ff_3_q);
  // Probe on \总周期数 
  // Probe on \无条件分支数 
  // Probe on \条件分支成功数 
  // Probe on \插入气泡数 
  // Probe on \LoadUse次数 
  D_Flip_Flop #(.trigger("rising"), .Pre_Clr_Positions("LEGACY"), .NegatePresetClear("false"), .enable("true"), .NewFFLayout("false")) d_ff_1 (
    .clk(IR1_t), .D(1'b1), .Q(d_ff_1_q), .reset(or_5_out));  // open: Qn, preset, en
  or or_5 (or_5_out, d_ff_5_q, RST);
  D_Flip_Flop #(.trigger("rising"), .Pre_Clr_Positions("LEGACY"), .NegatePresetClear("false"), .enable("true"), .NewFFLayout("false")) d_ff_2 (
    .clk(IR2_t), .D(1'b1), .Q(d_ff_2_q), .reset(or_6_out));  // open: Qn, preset, en
  or or_6 (or_6_out, d_ff_6_q, RST);
  D_Flip_Flop #(.trigger("rising"), .Pre_Clr_Positions("LEGACY"), .NegatePresetClear("false"), .enable("true"), .NewFFLayout("false")) d_ff_3 (
    .clk(IR3_t), .D(1'b1), .Q(d_ff_3_q), .reset(or_7_out));  // open: Qn, preset, en
  or or_7 (or_7_out, d_ff_7_q, RST);
  Adder #(.width(32)) adder_1 (.a(IF_PC), .b(32'h4), .out(IF_PC_4));  // open: cin, cout
  // Probe on IF_PC[11:0]
  // Probe on WB_PC[19:0]
  // RiscV_Probe riscv_probe_5: pin names not known; wires that end beside it: WB_IR
  or or_8 (or_8_out, d_ff_1_q, d_ff_5_q);
  or or_9 (or_9_out, d_ff_2_q, d_ff_6_q);
  or or_10 (or_10_out, d_ff_3_q, d_ff_7_q);
  // RiscV_Probe riscv_probe_6: pin names not known; wires that end beside it: IF_IR
  ROM #(.addrWidth(10), .dataWidth(32), .Select("high")) rom_1 (.addr(IF_PC[11:2]), .data(IF_IR));
  // Probe on EX_PC[11:0]
  // Probe on ID_PC[11:0]
  and and_1 (and_1_out, or_8_out, ~clear1);  // AND_Gate
  and and_2 (and_2_out, or_9_out, ~clear2);  // AND_Gate
  and and_3 (and_3_out, or_10_out, ~clear3);  // AND_Gate
  nor nor_2 (nor_2_out, stall, halt);
  // Probe on M_PC[11:0]
  D_Flip_Flop #(.trigger("high"), .Pre_Clr_Positions("LEGACY"), .NegatePresetClear("false"), .enable("true"), .NewFFLayout("false")) d_ff_4 (.Q(d_ff_4_q));  // open: clk, D, Qn, preset, en, reset
  // Probe on 13'hea
  D_Flip_Flop #(.trigger("rising"), .Pre_Clr_Positions("LEGACY"), .NegatePresetClear("false"), .enable("true"), .NewFFLayout("false")) d_ff_5 (
    .clk(CLK), .D(and_1_out), .Q(d_ff_5_q), .reset(RST));  // open: Qn, preset, en
  D_Flip_Flop #(.trigger("rising"), .Pre_Clr_Positions("LEGACY"), .NegatePresetClear("false"), .enable("true"), .NewFFLayout("false")) d_ff_6 (
    .clk(CLK), .D(and_2_out), .Q(d_ff_6_q), .reset(RST));  // open: Qn, preset, en
  D_Flip_Flop #(.trigger("rising"), .Pre_Clr_Positions("LEGACY"), .NegatePresetClear("false"), .enable("true"), .NewFFLayout("false")) d_ff_7 (
    .clk(CLK), .D(and_3_out), .Q(d_ff_7_q), .reset(RST));  // open: Qn, preset, en
  or or_11 (or_11_out, BranchTaken, INT, EX_uret);
  IF_ID IF_ID (
    .IR(IF_IR), .PC(IF_PC), .PC_4(IF_PC_4), .Clk(and_4_out), .IR_2(ID_IR), .PC_2(ID_PC), .PC_4_2(ID_PC_4),
    .en(nor_2_out), .reset(RST), .flush(or_11_out));  // open: PredictJump, PredictJump_2
  and and_4 (and_4_out, CLK, ~halt);  // AND_Gate
  // Probe on WB_PC[11:0]
  Comparator #(.width(13), .mode("twosComplement")) comparator_5 (
    .a(CNT_num), .b(13'hea), .eq(comparator_5_eq), .lt(comparator_5_lt));  // open: gt
  Clock #(.highDuration(1), .lowDuration(1)) clock_2 (.out(clock_2_out));
  nand nand_1 (nand_1_out, d_ff_4_q, comparator_5_eq);
  Counter #(.width(13), .max('h1fff), .ongoal("stay"), .trigger("rising"), .behavior("old")) counter_1 (
    .count(comparator_5_lt), .Q(CNT_num), .clk(clock_2_out));  // open: load, D, carry, clr, preset
  Priority_Encoder #(.select(2), .disabled("Z")) priority_encoder_1 (
    .in1(d_ff_5_q), .in2(d_ff_6_q), .in3(d_ff_7_q), .out(\中断号 ), .gs(\中断信号 ));  // open: in0, en_out, en_in
  assign CLK = nand_1_out ? clock_2_out : 1'bz;  // Controlled_Buffer controlled_buffer_1
  Multiplexer #(.select(2), .width(32), .disabled("Z"), .enable("false")) multiplexer_4 (
    .in1(32'h30ac), .in2(32'h3150), .in3(32'h31f4), .out(INT_PC), .sel(\中断号 ));  // open: in0
  and and_5 (and_5_out, \中断信号 , ~EX_uret);  // AND_Gate
  Pull_Resistor #(.pull(1)) pull_resistor_4 (.node(CLK));
  Register #(.width(2), .trigger("rising"), .Select("low")) register_1 (
    .D(\中断号 ), .en(INT), .Q(register_1_q), .clk(CLK), .clr(RST));
  D_Flip_Flop #(.trigger("rising"), .Pre_Clr_Positions("LEGACY"), .NegatePresetClear("false"), .enable("true"), .NewFFLayout("false")) d_ff_8 (
    .clk(CLK), .D(and_5_out), .Qn(IE));  // open: Q, preset, en, reset
  \单周期硬布线控制器  \u_单周期硬布线控制器_1  (
    .Funct({ID_IR[30], ID_IR[25], ID_IR[14:12]}), .OP(ID_IR[6:2]), .ALU_OP(\单周期硬布线控制器_1_alu_op ),
    .MemToReg(\单周期硬布线控制器_1_memtoreg ), .MemWrite(\单周期硬布线控制器_1_memwrite ), .ALU_SRC(\单周期硬布线控制器_1_alu_src ),
    .RegWrite(\单周期硬布线控制器_1_regwrite ), .ecall(ecall), .S_type(S_type), .Jalr(jalr), .Beq(Beq), .JAL(jal),
    .Bne(Bne), .in_3(ID_IR[21]), .uret(uret), .lbu(lbu), .bltu(bltu), .Rs1Used(Rs1Used), .Rs2Used(Rs2Used));  // open: csrrsi, csrrci
  Multiplexer #(.select(1), .width(5), .disabled("Z"), .enable("false")) multiplexer_5 (
    .in0(ID_IR[19:15]), .in1(5'b10001), .out(rs1), .sel(ecall));
  Multiplexer #(.select(1), .width(5), .disabled("Z"), .enable("false")) multiplexer_6 (
    .in0(ID_IR[24:20]), .in1(5'b01010), .out(rs2), .sel(ecall));
  Multiplexer #(.select(1), .width(12), .disabled("Z"), .enable("false")) multiplexer_7 (
    .in0(ID_IR[31:20]), .in1({ID_IR[31:25], ID_IR[11:7]}), .out(multiplexer_7_out), .sel(S_type));
  assign bit_extender_1_out = {{20{multiplexer_7_out[11]}}, multiplexer_7_out};  // Bit_Extender bit_extender_1
  assign bit_extender_2_out = {{20{ID_IR[31]}}, {ID_IR[31], ID_IR[7], ID_IR[30:25], ID_IR[11:8]}};  // Bit_Extender bit_extender_2
  assign bit_extender_3_out = {{12{ID_IR[31]}}, {ID_IR[31], ID_IR[19:12], ID_IR[20], ID_IR[30:21]}};  // Bit_Extender bit_extender_3
  Decoder #(.select(2), .tristate("false"), .disabled("Z"), .enable("false")) decoder_1 (
    .out1(decoder_1_out1), .out2(decoder_1_out2), .out3(decoder_1_out3), .sel(register_1_q));  // open: out0
  and and_6 (INT, IE, \中断信号 );
  not not_1 (not_1_out, halt);
  Counter #(.width(16), .max('hffff), .ongoal("wrap"), .trigger("falling"), .behavior("new")) counter_2 (
    .count(not_1_out), .Q(\总周期数 ), .clk(CLK), .clr(RST));  // open: load, D, carry, preset, down
  Multiplexer #(.select(2), .width(32), .disabled("Z"), .enable("false")) multiplexer_8 (
    .in0(bit_extender_1_out), .in1(bit_extender_2_out), .in2(bit_extender_3_out), .out(multiplexer_8_out),
    .sel({jal, or_12_out[0]}));  // open: in3
  or or_12 (or_12_out[0], Bne, bltu, Beq);
  and and_7 (clear1, decoder_1_out1, uret);
  and and_8 (clear2, decoder_1_out2, uret);
  and and_9 (clear3, decoder_1_out3, uret);
  Button button_1 (.out(RST));
  Regifile regifile_1 (
    .Din(RDin), .Clk(CLK), .R1(regifile_1_r1), .R2(regifile_1_r2), .WE(RegWrite), .W_num(WB_W_num),
    .R1_num(rs1), .R2_num(rs2));
  or or_13 (IR1_t, IR1, IRA);
  or or_14 (or_14_out, INT, EX_uret, flush);
  // Probe on Rs1Forward
  ID_EX ID_EX (
    .ecall(ecall), .Beq(Beq), .Bne(Bne), .MemToReg(\单周期硬布线控制器_1_memtoreg ),
    .MemWrite(\单周期硬布线控制器_1_memwrite ), .RegWrite(\单周期硬布线控制器_1_regwrite ), .AluSrcB(\单周期硬布线控制器_1_alu_src ),
    .jal(jal), .jalr(jalr), .rd(ID_IR[11:7]), .AluOP(\单周期硬布线控制器_1_alu_op ), .imm(multiplexer_8_out),
    .PC(ID_PC), .PC_4(ID_PC_4), .reset(RST), .en(not_2_out), .Clk(CLK), .ecall_2(EX_ecall),
    .Beq_2(ID_EX_beq_2), .Bne_2(ID_EX_bne_2), .MemToReg_2(EX_MemToReg), .MemWrite_2(ID_EX_memwrite_2),
    .RegWrite_2(EX_RegWrite), .AluSrcB_2(ID_EX_alusrcb_2), .jal_2(ID_EX_jal_2), .jalr_2(PCSrc[0]),
    .rd_2(EX_WriteReg_num), .AluOP_2(ID_EX_aluop_2), .imm_2(ID_EX_imm_2), .PC_2(EX_PC), .PC_4_2(EX_PC_4),
    .R1(regifile_1_r1), .R1_2(ID_EX_r1_2), .R2(regifile_1_r2), .R2_2(ID_EX_r2_2), .IR(ID_IR), .IR_2(EX_IR),
    .flush(or_14_out), .lbu(lbu), .lbu_2(ID_EX_lbu_2), .bltu(bltu), .bltu_2(ID_EX_bltu_2),
    .Rs1Forward(Rs1Forward), .Rs1Forward_2(ID_EX_rs1forward_2), .Rs2Forward(Rs2Forward),
    .Rs2Forward_2(ID_EX_rs2forward_2), .uret(uret), .uret_2(EX_uret));  // open: PredictJump, PredictJump_2
  // Probe on Rs2Forward
  not not_2 (not_2_out, halt);
  Register #(.width(1), .trigger("rising"), .Select("low")) register_2 (
    .D(BranchTaken), .Q(BT_2), .clk(CLK), .clr(RST));  // open: en
  Register #(.width(1), .trigger("rising"), .Select("low")) register_3 (
    .D(stall), .Q(LoadUse_1), .clk(CLK), .clr(RST));  // open: en
  or or_15 (or_15_out, LoadUse_1, BT_1);
  Multiplexer #(.select(1), .width(32), .disabled("Z"), .enable("false")) multiplexer_9 (
    .in0(EX_PC), .in1(ID_PC), .out(multiplexer_9_out), .sel(or_15_out));
  or or_16 (IR2_t, IR2, IRB);
  Multiplexer #(.select(1), .width(32), .disabled("Z"), .enable("false")) multiplexer_10 (
    .in0(multiplexer_9_out), .in1(IF_PC), .out(multiplexer_10_out), .sel(BT_2));
  Register #(.width(1), .trigger("rising"), .Select("low")) register_4 (
    .D(BT_2), .Q(BT_1), .clk(CLK), .clr(RST));  // open: en
  Register #(.width(32), .trigger("rising"), .Select("low")) mEPC (
    .D(multiplexer_10_out), .en(INT), .Q(RET_PC), .clk(CLK), .clr(RST));
  or or_17 (PCSrc[1], ID_EX_jal_2, and_10_out, and_12_out, and_11_out);
  and and_10 (and_10_out, ID_EX_beq_2, equal);
  or or_18 (IR3_t, IR3, IRC);
  and and_11 (and_11_out, ID_EX_bltu_2, tunnel);
  and and_12 (and_12_out, ~equal, ID_EX_bne_2);  // AND_Gate
  or or_19 (BranchTaken, PCSrc[1], PCSrc[0]);
  Multiplexer #(.select(2), .width(32), .disabled("Z"), .enable("false")) multiplexer_11 (
    .in0(ID_EX_r1_2), .in1(RDin), .in2(MEM_AluResult), .out(multiplexer_11_out), .sel(ID_EX_rs1forward_2));  // open: in3
  Multiplexer #(.select(2), .width(32), .disabled("Z"), .enable("false")) multiplexer_12 (
    .in0(ID_EX_r2_2), .in1(RDin), .in2(MEM_AluResult), .out(multiplexer_12_out), .sel(ID_EX_rs2forward_2));  // open: in3
  Multiplexer #(.select(1), .width(32), .disabled("Z"), .enable("false")) multiplexer_13 (
    .in0(multiplexer_12_out), .in1(ID_EX_imm_2), .out(multiplexer_13_out), .sel(ID_EX_alusrcb_2));
  Shifter #(.width(32), .shift("ll")) shifter_1 (.in(ID_EX_imm_2), .\dist (5'b00001), .out(shifter_1_out));
  ALU alu_1 (
    .X(multiplexer_11_out), .Y(multiplexer_13_out), .AluOP(ID_EX_aluop_2), .Equal(equal),
    .Result(ALU_result), .out_6(tunnel));  // open: Result_2, out_4
  Adder #(.width(32)) adder_2 (.a(shifter_1_out), .b(EX_PC), .out(branch_add));  // open: cin, cout
  Comparator #(.width(32), .mode("twosComplement")) comparator_6 (
    .a(multiplexer_11_out), .b(32'h22), .eq(comparator_6_eq));  // open: gt, lt
  and and_13 (EX_halt, EX_ecall, ~comparator_6_eq);  // AND_Gate
  and and_14 (and_14_out, comparator_6_eq, EX_ecall);
  Register #(.width(32), .trigger("rising"), .Select("low")) register_5 (
    .D(multiplexer_12_out), .en(and_14_out), .Q(LedData), .clk(CLK));  // open: clr
  not not_3 (not_3_out, halt);
  EX_MEM EX_MEM (
    .MemToReg(EX_MemToReg), .MemWrite(ID_EX_memwrite_2), .RegWrite(EX_RegWrite), .halt(EX_halt),
    .rd(EX_WriteReg_num), .PC(EX_PC), .PC_4(EX_PC_4), .IR(EX_IR), .MDin(multiplexer_12_out),
    .AluResuult(ALU_result), .MemToReg_2(EX_MEM_memtoreg_2), .MemWrite_2(MemWrite),
    .RegWrite_2(MEM_RegWrite), .halt_2(EX_MEM_halt_2), .rd_2(MEM_WriteReg_num), .PC_2(M_PC),
    .PC_4_2(MEM_PC_4), .IR_2(MEM_IR), .MDin_2(MDin), .AluResuult_2(MEM_AluResult), .reset(RST),
    .en(not_3_out), .Clk(CLK), .jal(ID_EX_jal_2), .jal_2(EX_MEM_jal_2), .jalr(PCSrc[0]),
    .jalr_2(EX_MEM_jalr_2), .lbu(ID_EX_lbu_2), .lbu_2(MEM_lbu), .flush(INT));
  // Probe on MEM_AluResult
  RAM #(.addrWidth(10), .dataWidth(32), .bus("separate"), .Select("high")) ram_1 (
    .addr(MEM_AluResult[11:2]), .din(MDin), .data(ram_1_data), .str(MemWrite), .clk(CLK));  // open: sel, ld, clr
  // Probe on MEM_WriteReg_num
  Multiplexer #(.select(2), .width(8), .disabled("Z"), .enable("false")) multiplexer_14 (
    .in0(ram_1_data[7:0]), .in1(ram_1_data[15:8]), .in2(ram_1_data[23:16]), .in3(ram_1_data[31:24]),
    .out(multiplexer_14_out), .sel(MEM_AluResult[1:0]));
  assign bit_extender_4_out = {{24{1'b0}}, multiplexer_14_out};  // Bit_Extender bit_extender_4
  Multiplexer #(.select(1), .width(32), .disabled("Z"), .enable("false")) multiplexer_15 (
    .in0(ram_1_data), .in1(bit_extender_4_out), .out(multiplexer_15_out), .sel(MEM_lbu));
  MEM_WB mem_wb_1 (
    .jal(EX_MEM_jal_2), .jalr(EX_MEM_jalr_2), .MemToReg(EX_MEM_memtoreg_2), .RegWrite(MEM_RegWrite),
    .halt(EX_MEM_halt_2), .rd(MEM_WriteReg_num), .PC(M_PC), .PC_4(MEM_PC_4), .IR(MEM_IR),
    .AluResuult(MEM_AluResult), .jal_2(mem_wb_1_jal_2), .jalr_2(mem_wb_1_jalr_2),
    .MemToReg_2(mem_wb_1_memtoreg_2[0]), .RegWrite_2(RegWrite), .halt_2(mem_wb_1_halt_2), .rd_2(WB_W_num),
    .PC_2(WB_PC), .PC_4_2(mem_wb_1_pc_4_2), .IR_2(WB_IR), .AluResuult_2(mem_wb_1_aluresuult_2), .reset(RST),
    .en(not_4_out), .Clk(CLK), .MDout(multiplexer_15_out), .MDout_2(mem_wb_1_mdout_2));
  not not_4 (not_4_out, halt);
  or or_20 (mem_wb_1_memtoreg_2[1], mem_wb_1_jalr_2, mem_wb_1_jal_2);
  D_Flip_Flop #(.trigger("rising"), .Pre_Clr_Positions("ABOVE_BELOW"), .NegatePresetClear("false"), .enable("true"), .NewFFLayout("true")) d_ff_9 (
    .clk(mem_wb_1_halt_2), .D(1'b1), .Q(halt), .en(1'b1), .reset(Go));  // open: Qn, preset
  Multiplexer #(.select(2), .width(32), .disabled("Z"), .enable("false")) multiplexer_16 (
    .in0(mem_wb_1_aluresuult_2), .in1(mem_wb_1_mdout_2), .in2(mem_wb_1_pc_4_2), .out(RDin),
    .sel(mem_wb_1_memtoreg_2));  // open: in3

  // Other names for the same wires on the sheet: MEM_PC[31:0] = M_PC

  // Notes on the sheet:
  //   中断源
  //   时空图监测，可删除
  //   中断等待指示
  //   单级中断测试信号模拟器
  //   数码管输出
  //   指令存储器
  //   指令探针
  //   contents of rom_1 (hex, n*v repeats v):
  //   7d000113 100413 1f41993 41f9d993 433 c00913 800b13 140413 f47413 800293 100313 499993 89e9b3 1300533
  //   2200893 73 406282b3 fe0294e3 140413 f00f93 1f47433 1c41413 800293 100313 49d993 89e9b3 1300533
  //   2200893 73 406282b3 fe0294e3 1c45413 406b0b33 b0463 f95ff06f 2b3 fff2c293 1029293 fff2e293 500533
  //   2200893 73 f5dff06f 1112023 410113 a12023 410113 812023 410113 1312023 410113 1412023 410113 1512023
  //   410113 1612023 410113 100b13 300a13 100a93 1600433 441413 14469b3 1300533 2200893 73 fe0416e3
  //   415a0a33 fe0a10e3 ffc10113 12b03 ffc10113 12a83 ffc10113 12a03 ffc10113 12983 ffc10113 12403
  //   ffc10113 12503 ffc10113 12883 200073 1112023 410113 a12023 410113 812023 410113 1312023 410113
  //   1412023 410113 1512023 410113 1612023 410113 200b13 300a13 100a93 1600433 441413 14469b3 1300533
  //   2200893 73 fe0416e3 415a0a33 fe0a10e3 ffc10113 12b03 ffc10113 12a83 ffc10113 12a03 ffc10113 12983
  //   ffc10113 12403 ffc10113 12503 ffc10113 12883 200073 1112023 410113 a12023 410113 812023 410113
  //   1312023 410113 1412023 410113 1512023 410113 1612023 410113 300b13 300a13 100a93 1600433 441413
  //   14469b3 1300533 2200893 73 fe0416e3 415a0a33 fe0a10e3 ffc10113 12b03 ffc10113 12a83 ffc10113 12a03
  //   ffc10113 12983 ffc10113 12403 ffc10113 12503 ffc10113 12883 200073
  //   控制位
  //   流水调试日志用
  //   暂停节拍，不能为0
  //   戳工具置1进入计数暂停模式，ctrl+k时钟自动运行到对应节拍暂停
  //   ctrl+k关闭时钟连续运行，将控制位置零，进入单步调试模式调试
  //   指令字
  //   可计数暂停的时钟源
  //   rs1
  //   rs2
  //   rd
  //   imm-lw
  //   imm-sw
  //   imm-b
  //   imm-jal
  //   JAL
  //   JALR
  //   URET
  //   lbu
  //   bltu
  //   Beq
  //   Bne
  //   MemToReg
  //   MemWrite
  //   AluOP
  //   AluSrcB
  //   RegWrite
  //   注意：测试流水线时，需将寄存器堆改为下跳沿触发
  //   为方便自动评测，需要输出流水线各段保存的PC值，注意是PC不是PC+4，另外ID段寄存器写入信息，Mem段内存写入信息也要输出
  //   R[rs1]
  //   R[rs2]
  //   数据存储器
endmodule

module \重定向动态分支预测  (
  output RegWrite,
  output MemWrite,
  output [31:0] IF_PC,
  output [31:0] ID_PC,
  output [31:0] EX_PC,
  output [31:0] M_PC,
  output [31:0] WB_PC,
  output [31:0] RDin,
  output [31:0] MDin,
  output [31:0] LedData
);

  wire and_1_out, and_2_out, and_3_out, and_4_out, and_5_out, Beq, bltu, Bne, BranchTaken, CLK, clock_1_out,
       clock_2_out, comparator_1_eq, comparator_1_lt, comparator_2_eq, comparator_3_eq, d_ff_1_q, ecall,
       equal, EX_Beq, EX_bltu, EX_Bne, EX_Branch, EX_ecall, EX_halt, EX_jal, EX_jalr, EX_MEM_halt_2,
       EX_MEM_jal_2, EX_MEM_jalr_2, EX_MEM_memtoreg_2, EX_MemToReg, EX_PredictErr, EX_RegWrite, flush, Go,
       halt, ID_EX_alusrcb_2, ID_EX_lbu_2, ID_EX_memwrite_2, ID_EX_predictjump_2, IF_ID_predictjump_2, IR1,
       IR2, IR3, jal, jalr, lbu, MEM_lbu, MEM_RegWrite, mem_wb_1_halt_2, mem_wb_1_jal_2, mem_wb_1_jalr_2,
       nand_1_out, nor_1_out, nor_2_out, not_1_out, not_2_out, not_4_out, not_5_out, or_2_out, PredictJump,
       Rs1Used, Rs2Used, RST, S_type, stall, tunnel, W1, W2, W3, \单周期硬布线控制器_1_alu_src ,
       \单周期硬布线控制器_1_memtoreg , \单周期硬布线控制器_1_memwrite , \单周期硬布线控制器_1_regwrite , \单周期硬布线控制器_1_uret ;
  wire [0:0] or_1_out;
  wire [1:0] ID_EX_rs1forward_2, ID_EX_rs2forward_2, mem_wb_1_memtoreg_2, Rs1Forward, Rs2Forward;
  wire [1:1] PCSrc;
  wire [3:0] ID_EX_aluop_2, \单周期硬布线控制器_1_alu_op ;
  wire [4:0] EX_WriteReg_num, MEM_WriteReg_num, rs1, rs2, WB_W_num;
  wire [7:0] multiplexer_12_out;
  wire [11:0] multiplexer_5_out;
  wire [12:0] CNT_num;
  wire [15:0] \LoadUse次数 , \总周期数 , \插入气泡数 , \无条件分支数 , \条件分支成功数 ;
  wire [31:0] ALU_result, bit_extender_1_out, bit_extender_2_out, bit_extender_3_out, bit_extender_4_out,
       branch_add, btb_1_jumpadrr, EX_BranchAddr, EX_IR, EX_PC_4, ID_EX_imm_2, ID_EX_r1_2, ID_EX_r2_2, ID_IR,
       ID_PC_4, IF_IR, IF_PC_4, MEM_AluResult, MEM_IR, MEM_PC_4, mem_wb_1_aluresuult_2, mem_wb_1_mdout_2,
       mem_wb_1_pc_4_2, multiplexer_2_out, multiplexer_4_out, multiplexer_8_out, multiplexer_9_out,
       multiplexer_10_out, multiplexer_11_out, multiplexer_13_out, PredictJumpAddr, ram_1_data,
       regifile_1_r1, regifile_1_r2, shifter_1_out, WB_IR;

  Button \u_总复位  (.out(RST));
  Button _1 (.out(IR1));
  Button _2 (.out(IR2));
  Button _3 (.out(IR3));
  // Probe on \总周期数 
  // Probe on \总周期数 
  Button \u_继续运行  (.out(Go));
  LED #(.active("true")) led_1 (.in(W1));
  LED #(.active("true")) led_2 (.in(W2));
  LED #(.active("true")) led_3 (.in(W3));
  Hex_Digit_Display hex_digit_display_1 (.value(LedData[31:28]));  // open: dp
  // Probe on IF_PC[19:0]
  // RiscV_Probe riscv_probe_1: pin names not known; wires that end beside it: IF_IR
  Hex_Digit_Display hex_digit_display_2 (.value(LedData[27:24]));  // open: dp
  Hex_Digit_Display hex_digit_display_3 (.value(LedData[23:20]));  // open: dp
  // Probe on ID_PC[19:0]
  // RiscV_Probe riscv_probe_2: pin names not known; wires that end beside it: ID_IR
  Multiplexer #(.select(1), .width(32), .disabled("Z"), .enable("false")) multiplexer_1 (
    .in0(branch_add), .in1(ALU_result), .out(EX_BranchAddr), .sel(EX_jalr));
  Hex_Digit_Display hex_digit_display_4 (.value(LedData[15:12]));  // open: dp
  Hex_Digit_Display hex_digit_display_5 (.value(LedData[19:16]));  // open: dp
  Multiplexer #(.select(2), .width(32), .disabled("Z"), .enable("false")) multiplexer_2 (
    .in0(EX_PC_4), .in1(ALU_result), .in2(branch_add), .out(multiplexer_2_out), .sel({PCSrc[1], EX_jalr}));  // open: in3
  Hex_Digit_Display hex_digit_display_6 (.value(LedData[7:4]));  // open: dp
  Hex_Digit_Display hex_digit_display_7 (.value(LedData[11:8]));  // open: dp
  Clock #(.highDuration(1), .lowDuration(1)) clock_1 (.out(clock_1_out));
  // Probe on EX_PC[19:0]
  // RiscV_Probe riscv_probe_3: pin names not known; wires that end beside it: clock_1_out, EX_IR, CLK
  BTB btb_1 (
    .CLK(CLK), .EX_Branch(EX_Branch), .EX_BranchTaken(BranchTaken), .PC(IF_PC), .EX_PC(EX_PC),
    .EX_BranchAddr(EX_BranchAddr), .PredictJump(PredictJump), .JumpAdrr(btb_1_jumpadrr));
  Hex_Digit_Display hex_digit_display_8 (.value(LedData[3:0]));  // open: dp
  Multiplexer #(.select(1), .width(32), .disabled("Z"), .enable("false")) multiplexer_3 (
    .in0(IF_PC_4), .in1(btb_1_jumpadrr), .out(PredictJumpAddr), .sel(PredictJump));
  Multiplexer #(.select(1), .width(32), .disabled("Z"), .enable("false")) multiplexer_4 (
    .in0(PredictJumpAddr), .in1(multiplexer_2_out), .out(multiplexer_4_out), .sel(EX_PredictErr));
  nor nor_1 (nor_1_out, stall, halt);
  // Probe on \总周期数 
  // Probe on M_PC[19:0]
  // RiscV_Probe riscv_probe_4: pin names not known; wires that end beside it: MEM_IR
  Register #(.width(32), .trigger("rising"), .Select("low")) PC (
    .D(multiplexer_4_out), .en(nor_1_out), .Q(IF_PC), .clk(CLK), .clr(RST));
  // Probe on \总周期数 
  // Probe on \无条件分支数 
  // Probe on \条件分支成功数 
  // Probe on \插入气泡数 
  // Probe on \LoadUse次数 
  // Probe on IF_PC[11:0]
  // Probe on WB_PC[19:0]
  // RiscV_Probe riscv_probe_5: pin names not known; wires that end beside it: WB_IR
  \重定向相关处理逻辑  \u_重定向相关处理逻辑_1  (
    .Rs1Used(Rs1Used), .Rs1(rs1), .EX_WriteReg_num(EX_WriteReg_num), .EX_MemToReg(EX_MemToReg),
    .Rs2Used(Rs2Used), .Rs2(rs2), .MEM_WriteReg_num(MEM_WriteReg_num), .BranchTaken(BranchTaken),
    .EX_RegWrite(EX_RegWrite), .MEM_RegWrite(MEM_RegWrite), .ecall(ecall), .Stall(stall), .Flush(flush),
    .Rs1Foward(Rs1Forward), .Rs2Foward(Rs2Forward));
  // Probe on EX_PC[11:0]
  // Probe on ID_PC[11:0]
  Adder #(.width(32)) adder_1 (.a(IF_PC), .b(32'h4), .out(IF_PC_4));  // open: cin, cout
  // Probe on M_PC[11:0]
  D_Flip_Flop #(.trigger("high"), .Pre_Clr_Positions("LEGACY"), .NegatePresetClear("false"), .enable("true"), .NewFFLayout("false")) d_ff_1 (.Q(d_ff_1_q));  // open: clk, D, Qn, preset, en, reset
  // Probe on 13'h342
  // Probe on WB_PC[11:0]
  Comparator #(.width(13), .mode("twosComplement")) comparator_1 (
    .a(CNT_num), .b(13'h342), .eq(comparator_1_eq), .lt(comparator_1_lt));  // open: gt
  Clock #(.highDuration(1), .lowDuration(1)) clock_2 (.out(clock_2_out));
  // RiscV_Probe riscv_probe_6: pin names not known; wires that end beside it: IF_IR
  ROM #(.addrWidth(10), .dataWidth(32), .Select("high")) rom_1 (.addr(IF_PC[11:2]), .data(IF_IR));
  nand nand_1 (nand_1_out, d_ff_1_q, comparator_1_eq);
  Counter #(.width(13), .max('h1fff), .ongoal("stay"), .trigger("rising"), .behavior("old")) counter_1 (
    .count(comparator_1_lt), .Q(CNT_num), .clk(clock_2_out));  // open: load, D, carry, clr, preset
  IF_ID IF_ID (
    .IR(IF_IR), .PC(IF_PC), .PC_4(IF_PC_4), .Clk(and_1_out), .IR_2(ID_IR), .PC_2(ID_PC), .PC_4_2(ID_PC_4),
    .en(nor_2_out), .reset(RST), .flush(EX_PredictErr), .PredictJump(PredictJump),
    .PredictJump_2(IF_ID_predictjump_2));
  nor nor_2 (nor_2_out, stall, halt);
  and and_1 (and_1_out, CLK, ~halt);  // AND_Gate
  assign CLK = nand_1_out ? clock_2_out : 1'bz;  // Controlled_Buffer controlled_buffer_1
  Pull_Resistor #(.pull(1)) pull_resistor_1 (.node(CLK));
  not not_1 (not_1_out, halt);
  Counter #(.width(16), .max('hffff), .ongoal("wrap"), .trigger("falling"), .behavior("new")) counter_2 (
    .count(not_1_out), .Q(\总周期数 ), .clk(CLK), .clr(RST));  // open: load, D, carry, preset, down
  Multiplexer #(.select(1), .width(12), .disabled("Z"), .enable("false")) multiplexer_5 (
    .in0(ID_IR[31:20]), .in1({ID_IR[31:25], ID_IR[11:7]}), .out(multiplexer_5_out), .sel(S_type));
  \单周期硬布线控制器  \u_单周期硬布线控制器_1  (
    .Funct({ID_IR[30], ID_IR[25], ID_IR[14:12]}), .OP(ID_IR[6:2]), .ALU_OP(\单周期硬布线控制器_1_alu_op ),
    .MemToReg(\单周期硬布线控制器_1_memtoreg ), .MemWrite(\单周期硬布线控制器_1_memwrite ), .ALU_SRC(\单周期硬布线控制器_1_alu_src ),
    .RegWrite(\单周期硬布线控制器_1_regwrite ), .ecall(ecall), .S_type(S_type), .Jalr(jalr), .Beq(Beq), .JAL(jal),
    .Bne(Bne), .in_3(ID_IR[21]), .uret(\单周期硬布线控制器_1_uret ), .lbu(lbu), .bltu(bltu), .Rs1Used(Rs1Used),
    .Rs2Used(Rs2Used));  // open: csrrsi, csrrci
  Multiplexer #(.select(1), .width(5), .disabled("Z"), .enable("false")) multiplexer_6 (
    .in0(ID_IR[19:15]), .in1(5'b10001), .out(rs1), .sel(ecall));
  Multiplexer #(.select(1), .width(5), .disabled("Z"), .enable("false")) multiplexer_7 (
    .in0(ID_IR[24:20]), .in1(5'b01010), .out(rs2), .sel(ecall));
  assign bit_extender_1_out = {{20{multiplexer_5_out[11]}}, multiplexer_5_out};  // Bit_Extender bit_extender_1
  assign bit_extender_2_out = {{20{ID_IR[31]}}, {ID_IR[31], ID_IR[7], ID_IR[30:25], ID_IR[11:8]}};  // Bit_Extender bit_extender_2
  assign bit_extender_3_out = {{12{ID_IR[31]}}, {ID_IR[31], ID_IR[19:12], ID_IR[20], ID_IR[30:21]}};  // Bit_Extender bit_extender_3
  or or_1 (or_1_out[0], Bne, bltu, Beq);
  Multiplexer #(.select(2), .width(32), .disabled("Z"), .enable("false")) multiplexer_8 (
    .in0(bit_extender_1_out), .in1(bit_extender_2_out), .in2(bit_extender_3_out), .out(multiplexer_8_out),
    .sel({jal, or_1_out[0]}));  // open: in3
  Regifile regifile_1 (
    .Din(RDin), .Clk(CLK), .R1(regifile_1_r1), .R2(regifile_1_r2), .WE(RegWrite), .W_num(WB_W_num),
    .R1_num(rs1), .R2_num(rs2));
  or or_2 (or_2_out, EX_PredictErr, stall);
  ID_EX ID_EX (
    .ecall(ecall), .Beq(Beq), .Bne(Bne), .MemToReg(\单周期硬布线控制器_1_memtoreg ),
    .MemWrite(\单周期硬布线控制器_1_memwrite ), .RegWrite(\单周期硬布线控制器_1_regwrite ), .AluSrcB(\单周期硬布线控制器_1_alu_src ),
    .jal(jal), .jalr(jalr), .rd(ID_IR[11:7]), .AluOP(\单周期硬布线控制器_1_alu_op ), .imm(multiplexer_8_out),
    .PC(ID_PC), .PC_4(ID_PC_4), .reset(RST), .en(not_2_out), .Clk(CLK), .ecall_2(EX_ecall), .Beq_2(EX_Beq),
    .Bne_2(EX_Bne), .MemToReg_2(EX_MemToReg), .MemWrite_2(ID_EX_memwrite_2), .RegWrite_2(EX_RegWrite),
    .AluSrcB_2(ID_EX_alusrcb_2), .jal_2(EX_jal), .jalr_2(EX_jalr), .rd_2(EX_WriteReg_num),
    .AluOP_2(ID_EX_aluop_2), .imm_2(ID_EX_imm_2), .PC_2(EX_PC), .PC_4_2(EX_PC_4), .R1(regifile_1_r1),
    .R1_2(ID_EX_r1_2), .R2(regifile_1_r2), .R2_2(ID_EX_r2_2), .IR(ID_IR), .IR_2(EX_IR), .flush(or_2_out),
    .lbu(lbu), .lbu_2(ID_EX_lbu_2), .bltu(bltu), .bltu_2(EX_bltu), .Rs1Forward(Rs1Forward),
    .Rs1Forward_2(ID_EX_rs1forward_2), .Rs2Forward(Rs2Forward), .Rs2Forward_2(ID_EX_rs2forward_2),
    .PredictJump(IF_ID_predictjump_2), .PredictJump_2(ID_EX_predictjump_2));  // open: uret, uret_2
  not not_2 (not_2_out, halt);
  or or_3 (EX_Branch, EX_bltu, EX_jalr, EX_jal, EX_Beq, EX_Bne);
  Comparator #(.width(1), .mode("unsigned")) comparator_2 (
    .a(ID_EX_predictjump_2), .b(BranchTaken), .eq(comparator_2_eq));  // open: gt, lt
  not not_3 (EX_PredictErr, comparator_2_eq);
  or or_4 (PCSrc[1], EX_jal, and_2_out, and_3_out, and_4_out);
  and and_2 (and_2_out, EX_Beq, equal);
  and and_3 (and_3_out, ~equal, EX_Bne);  // AND_Gate
  and and_4 (and_4_out, EX_bltu, tunnel);
  Multiplexer #(.select(2), .width(32), .disabled("Z"), .enable("false")) multiplexer_9 (
    .in0(ID_EX_r1_2), .in1(RDin), .in2(MEM_AluResult), .out(multiplexer_9_out), .sel(ID_EX_rs1forward_2));  // open: in3
  or or_5 (BranchTaken, PCSrc[1], EX_jalr);
  Multiplexer #(.select(2), .width(32), .disabled("Z"), .enable("false")) multiplexer_10 (
    .in0(ID_EX_r2_2), .in1(RDin), .in2(MEM_AluResult), .out(multiplexer_10_out), .sel(ID_EX_rs2forward_2));  // open: in3
  Shifter #(.width(32), .shift("ll")) shifter_1 (.in(ID_EX_imm_2), .\dist (5'b00001), .out(shifter_1_out));
  Multiplexer #(.select(1), .width(32), .disabled("Z"), .enable("false")) multiplexer_11 (
    .in0(multiplexer_10_out), .in1(ID_EX_imm_2), .out(multiplexer_11_out), .sel(ID_EX_alusrcb_2));
  Adder #(.width(32)) adder_2 (.a(shifter_1_out), .b(EX_PC), .out(branch_add));  // open: cin, cout
  Comparator #(.width(32), .mode("twosComplement")) comparator_3 (
    .a(multiplexer_9_out), .b(32'h22), .eq(comparator_3_eq));  // open: gt, lt
  ALU alu_1 (
    .X(multiplexer_9_out), .Y(multiplexer_11_out), .AluOP(ID_EX_aluop_2), .Equal(equal), .Result(ALU_result),
    .out_6(tunnel));  // open: Result_2, out_4
  and and_5 (and_5_out, comparator_3_eq, EX_ecall);
  and and_6 (EX_halt, EX_ecall, ~comparator_3_eq);  // AND_Gate
  Register #(.width(32), .trigger("rising"), .Select("low")) register_1 (
    .D(multiplexer_10_out), .en(and_5_out), .Q(LedData), .clk(CLK));  // open: clr
  not not_4 (not_4_out, halt);
  EX_MEM EX_MEM (
    .MemToReg(EX_MemToReg), .MemWrite(ID_EX_memwrite_2), .RegWrite(EX_RegWrite), .halt(EX_halt),
    .rd(EX_WriteReg_num), .PC(EX_PC), .PC_4(EX_PC_4), .IR(EX_IR), .MDin(multiplexer_10_out),
    .AluResuult(ALU_result), .MemToReg_2(EX_MEM_memtoreg_2), .MemWrite_2(MemWrite),
    .RegWrite_2(MEM_RegWrite), .halt_2(EX_MEM_halt_2), .rd_2(MEM_WriteReg_num), .PC_2(M_PC),
    .PC_4_2(MEM_PC_4), .IR_2(MEM_IR), .MDin_2(MDin), .AluResuult_2(MEM_AluResult), .reset(RST),
    .en(not_4_out), .Clk(CLK), .jal(EX_jal), .jal_2(EX_MEM_jal_2), .jalr(EX_jalr), .jalr_2(EX_MEM_jalr_2),
    .lbu(ID_EX_lbu_2), .lbu_2(MEM_lbu), .flush(1'b0));
  // Probe on MEM_AluResult
  RAM #(.addrWidth(10), .dataWidth(32), .bus("separate"), .Select("high")) ram_1 (
    .addr(MEM_AluResult[11:2]), .din(MDin), .data(ram_1_data), .str(MemWrite), .clk(CLK));  // open: sel, ld, clr
  // Probe on MEM_WriteReg_num
  Multiplexer #(.select(2), .width(8), .disabled("Z"), .enable("false")) multiplexer_12 (
    .in0(ram_1_data[7:0]), .in1(ram_1_data[15:8]), .in2(ram_1_data[23:16]), .in3(ram_1_data[31:24]),
    .out(multiplexer_12_out), .sel(MEM_AluResult[1:0]));
  assign bit_extender_4_out = {{24{1'b0}}, multiplexer_12_out};  // Bit_Extender bit_extender_4
  MEM_WB mem_wb_1 (
    .jal(EX_MEM_jal_2), .jalr(EX_MEM_jalr_2), .MemToReg(EX_MEM_memtoreg_2), .RegWrite(MEM_RegWrite),
    .halt(EX_MEM_halt_2), .rd(MEM_WriteReg_num), .PC(M_PC), .PC_4(MEM_PC_4), .IR(MEM_IR),
    .AluResuult(MEM_AluResult), .jal_2(mem_wb_1_jal_2), .jalr_2(mem_wb_1_jalr_2),
    .MemToReg_2(mem_wb_1_memtoreg_2[0]), .RegWrite_2(RegWrite), .halt_2(mem_wb_1_halt_2), .rd_2(WB_W_num),
    .PC_2(WB_PC), .PC_4_2(mem_wb_1_pc_4_2), .IR_2(WB_IR), .AluResuult_2(mem_wb_1_aluresuult_2), .reset(RST),
    .en(not_5_out), .Clk(CLK), .MDout(multiplexer_13_out), .MDout_2(mem_wb_1_mdout_2));
  Multiplexer #(.select(1), .width(32), .disabled("Z"), .enable("false")) multiplexer_13 (
    .in0(ram_1_data), .in1(bit_extender_4_out), .out(multiplexer_13_out), .sel(MEM_lbu));
  not not_5 (not_5_out, halt);
  or or_6 (mem_wb_1_memtoreg_2[1], mem_wb_1_jalr_2, mem_wb_1_jal_2);
  D_Flip_Flop #(.trigger("rising"), .Pre_Clr_Positions("ABOVE_BELOW"), .NegatePresetClear("false"), .enable("true"), .NewFFLayout("true")) d_ff_2 (
    .clk(mem_wb_1_halt_2), .D(1'b1), .Q(halt), .en(1'b1), .reset(Go));  // open: Qn, preset
  Multiplexer #(.select(2), .width(32), .disabled("Z"), .enable("false")) multiplexer_14 (
    .in0(mem_wb_1_aluresuult_2), .in1(mem_wb_1_mdout_2), .in2(mem_wb_1_pc_4_2), .out(RDin),
    .sel(mem_wb_1_memtoreg_2));  // open: in3

  // Other names for the same wires on the sheet: MEM_PC[31:0] = M_PC; PCSrc[0] = EX_jalr

  // Notes on the sheet:
  //   中断源
  //   时空图监测，可删除
  //   中断等待指示
  //   数码管输出
  //   控制位
  //   流水调试日志用
  //   暂停节拍，不能为0
  //   指令探针
  //   指令存储器
  //   戳工具置1进入计数暂停模式，ctrl+k时钟自动运行到对应节拍暂停
  //   ctrl+k关闭时钟连续运行，将控制位置零，进入单步调试模式调试
  //   contents of rom_1 (hex, n*v repeats v):
  //   100493 100006f 100493 200913 300993 100006f 100493 200913 300993 100006f 100493 200913 300993
  //   100006f 100493 200913 300993 3c4000ef 100413 100493 1f49493 900533 2200893 73 24d493 48463 fedff06f
  //   900533 2200893 73 100493 249493 900533 2200893 73 48463 fedff06f 100493 1f49493 900533 2200893 73
  //   4034d493 900533 2200893 73 4044d493 900533 2200893 73 4044d493 900533 2200893 73 4044d493 900533
  //   2200893 73 4044d493 900533 2200893 73 4044d493 900533 2200893 73 4044d493 900533 2200893 73 4044d493
  //   900533 2200893 73 100413 1f41993 41f9d993 433 c00913 300b13 140413 f47413 800293 100313 499993
  //   89e9b3 1300533 2200893 73 406282b3 fe0294e3 140413 f00f93 1f47433 1c41413 800293 100313 49d993
  //   89e9b3 1300533 2200893 73 406282b3 fe0294e3 1c45413 406b0b33 b0463 f95ff06f 2b3 fff2c293 829293
  //   ff2e293 500533 2200893 73 fff00413 493 84a023 140413 448493 84a023 140413 448493 84a023 140413
  //   448493 84a023 140413 448493 84a023 140413 448493 84a023 140413 448493 84a023 140413 448493 84a023
  //   140413 448493 84a023 140413 448493 84a023 140413 448493 84a023 140413 448493 84a023 140413 448493
  //   84a023 140413 448493 84a023 140413 448493 84a023 140413 448493 84a023 140413 448493 140413 433
  //   3c00493 42983 4aa03 149a2b3 28663 134a023 1442023 ffc48493 fe9412e3 800533 2200893 73 440413 3c00493
  //   fc9416e3 3200893 73 100293 300313 800493 849493 7648493 900533 2200893 73 800e13 5494b3 6494b3
  //   900533 2200893 73 fffe0e13 fe0e14e3 a00893 73 fff00293 313 1900413 841413 9700493 940533 2200893 73
  //   5484b3 494b313 fe0306e3 a00893 73 313 1000e13 8400493 849493 8348493 400913 891913 490913 849493
  //   8248493 849493 8148493 891913 490913 891913 490913 932023 12484b3 430313 fffe0e13 fe0e18e3 2000e13
  //   313 34483 900533 2200893 73 130313 fffe0e13 fe0e14e3 a00893 73 ff100493 900533 2200893 73 148493
  //   fe9068e3 900533 2200893 73 a00893 73 413 140413 800533 2200893 73 240413 800533 2200893 73 340413
  //   800533 2200893 73 440413 800533 2200893 73 540413 800533 2200893 73 640413 800533 2200893 73 740413
  //   800533 2200893 73 840413 800533 2200893 2200893 73 8067
  //   可计数暂停的时钟源
  //   指令字
  //   rs1
  //   rs2
  //   rd
  //   imm-lw
  //   imm-sw
  //   imm-b
  //   imm-jal
  //   JAL
  //   JALR
  //   URET
  //   lbu
  //   bltu
  //   为方便自动评测，需要输出流水线各段保存的PC值，注意是PC不是PC+4，另外ID段寄存器写入信息，Mem段内存写入信息也要输出
  //   Beq
  //   Bne
  //   MemToReg
  //   MemWrite
  //   AluOP
  //   AluSrcB
  //   RegWrite
  //   注意：测试流水线时，需将寄存器堆改为下跳沿触发
  //   R[rs1]
  //   R[rs2]
  //   数据存储器
endmodule

module \封装正确性测试  (
);

  wire IR1, IR2, IR3, MemW, RegW;
  wire [31:0] EX_PC, ID_PC, IF_PC, IR, LED, MDin, MDinr, MEM_PC, PC, RDin, RDinr, WB_PC;

  \单周期RISC_V  \u_单周期risc_v_1  (
    .IR1(IR1), .IR2(IR2), .IR3(IR3), .RegWrite(RegW), .MemWrite(MemW), .PC(PC), .IR(IR), .RDin(RDin),
    .MDin(MDin), .LedData(LED));
  \气泡流水线  \u_气泡流水线_1  (
    .RegWrite(RegW), .MemWrite(MemW), .IF_PC(IF_PC), .ID_PC(ID_PC), .EX_PC(EX_PC), .M_PC(MEM_PC),
    .WB_PC(WB_PC), .RDin(RDinr), .MDin(MDinr), .LedData(LED));
  \单周期_单级中断  \u_单周期_单级中断_1  (
    .IR1(IR1), .IR2(IR2), .IR3(IR3), .RegWrite(RegW), .MemWrite(MemW), .PC(PC), .IR(IR), .RDin(RDin),
    .MDin(MDin), .LedData(LED));
  \理想流水线  \u_理想流水线_1  (
    .RegWrite(RegW), .MemWrite(MemW), .IF_PC(IF_PC), .ID_PC(ID_PC), .EX_PC(EX_PC), .M_PC(MEM_PC),
    .WB_PC(WB_PC), .RDin(RDinr), .MDin(MDinr), .LedData(LED));
  \重定向流水线  \u_重定向流水线_1  (
    .RegWrite(RegW), .MemWrite(MemW), .IF_PC(IF_PC), .ID_PC(ID_PC), .EX_PC(EX_PC), .M_PC(MEM_PC),
    .WB_PC(WB_PC), .RDin(RDinr), .MDin(MDinr), .LedData(LED));
  \单周期_多级中断  \u_单周期_多级中断_1  (
    .IR1(IR1), .IR2(IR2), .IR3(IR3), .RegWrite(RegW), .MemWrite(MemW), .PC(PC), .IR(IR), .RDin(RDin),
    .MDin(MDin), .LedData(LED));

  // Notes on the sheet:
  //   单周期封装测试
  //   气泡流水封装测试
  //   单周期+单级中断封装测试
  //   请检查上面封装有无位宽不匹配，引脚标签是否和连接的标签相对应，否则无法在educoder平台上正确测试
  //   理想流水封装测试
  //   重定向流水封装测试
  //   单周期+多级中断封装测试
endmodule

module IF_ID (
  input  PredictJump,
  input  [31:0] IR,
  input  [31:0] PC,
  input  [31:0] PC_4,
  input  en,
  input  reset,
  input  flush,
  input  Clk,
  output PredictJump_2,
  output [31:0] IR_2,
  output [31:0] PC_2,
  output [31:0] PC_4_2
);

  wire multiplexer_1_out, or_1_out;
  wire [31:0] multiplexer_2_out, multiplexer_3_out, multiplexer_4_out;

  or or_1 (or_1_out, reset, flush);
  Multiplexer #(.select(1), .width(1), .disabled("Z"), .enable("false")) multiplexer_1 (
    .in0(PredictJump), .in1(1'b0), .out(multiplexer_1_out), .sel(or_1_out));
  Multiplexer #(.select(1), .width(32), .disabled("Z"), .enable("false")) multiplexer_2 (
    .in0(IR), .in1({32{1'b0}}), .out(multiplexer_2_out), .sel(or_1_out));
  Multiplexer #(.select(1), .width(32), .disabled("Z"), .enable("false")) multiplexer_3 (
    .in0(PC), .in1({32{1'b0}}), .out(multiplexer_3_out), .sel(or_1_out));
  Multiplexer #(.select(1), .width(32), .disabled("Z"), .enable("false")) multiplexer_4 (
    .in0(PC_4), .in1({32{1'b0}}), .out(multiplexer_4_out), .sel(or_1_out));
  Register #(.width(1), .trigger("rising"), .Select("low")) register_1 (
    .D(multiplexer_1_out), .en(en), .Q(PredictJump_2), .clk(Clk));  // open: clr
  Register #(.width(32), .trigger("rising"), .Select("low")) register_2 (
    .D(multiplexer_2_out), .en(en), .Q(IR_2), .clk(Clk));  // open: clr
  Register #(.width(32), .trigger("rising"), .Select("low")) register_3 (
    .D(multiplexer_3_out), .en(en), .Q(PC_2), .clk(Clk));  // open: clr
  Register #(.width(32), .trigger("rising"), .Select("low")) register_4 (
    .D(multiplexer_4_out), .en(en), .Q(PC_4_2), .clk(Clk));  // open: clr
endmodule

module ID_EX (
  input  [1:0] Rs1Forward,
  input  [1:0] Rs2Forward,
  input  lbu,
  input  bltu,
  input  ecall,
  input  Beq,
  input  Bne,
  input  MemToReg,
  input  MemWrite,
  input  RegWrite,
  input  AluSrcB,
  input  jal,
  input  jalr,
  input  uret,
  input  PredictJump,
  input  [4:0] rd,
  input  [3:0] AluOP,
  input  [31:0] imm,
  input  [31:0] PC,
  input  [31:0] PC_4,
  input  [31:0] R1,
  input  [31:0] R2,
  input  [31:0] IR,
  input  en,
  input  reset,
  input  Clk,
  input  flush,
  output [1:0] Rs1Forward_2,
  output [1:0] Rs2Forward_2,
  output lbu_2,
  output bltu_2,
  output ecall_2,
  output Beq_2,
  output Bne_2,
  output MemToReg_2,
  output MemWrite_2,
  output RegWrite_2,
  output AluSrcB_2,
  output jal_2,
  output jalr_2,
  output uret_2,
  output PredictJump_2,
  output [4:0] rd_2,
  output [3:0] AluOP_2,
  output [31:0] imm_2,
  output [31:0] PC_2,
  output [31:0] PC_4_2,
  output [31:0] R1_2,
  output [31:0] R2_2,
  output [31:0] IR_2
);

  wire multiplexer_3_out, multiplexer_4_out, multiplexer_5_out, multiplexer_6_out, multiplexer_7_out,
       multiplexer_8_out, multiplexer_9_out, multiplexer_10_out, multiplexer_11_out, multiplexer_12_out,
       multiplexer_13_out, multiplexer_14_out, multiplexer_15_out, or_1_out;
  wire [1:0] multiplexer_1_out, multiplexer_2_out;
  wire [3:0] multiplexer_17_out;
  wire [4:0] multiplexer_16_out;
  wire [31:0] multiplexer_18_out, multiplexer_19_out, multiplexer_20_out, multiplexer_21_out,
       multiplexer_22_out, multiplexer_23_out;

  or or_1 (or_1_out, reset, flush);
  Multiplexer #(.select(1), .width(2), .disabled("Z"), .enable("false")) multiplexer_1 (
    .in0(Rs1Forward), .in1(2'b00), .out(multiplexer_1_out), .sel(or_1_out));
  Multiplexer #(.select(1), .width(2), .disabled("Z"), .enable("false")) multiplexer_2 (
    .in0(Rs2Forward), .in1(2'b00), .out(multiplexer_2_out), .sel(or_1_out));
  Multiplexer #(.select(1), .width(1), .disabled("Z"), .enable("false")) multiplexer_3 (
    .in0(lbu), .in1(1'b0), .out(multiplexer_3_out), .sel(or_1_out));
  Multiplexer #(.select(1), .width(1), .disabled("Z"), .enable("false")) multiplexer_4 (
    .in0(bltu), .in1(1'b0), .out(multiplexer_4_out), .sel(or_1_out));
  Multiplexer #(.select(1), .width(1), .disabled("Z"), .enable("false")) multiplexer_5 (
    .in0(ecall), .in1(1'b0), .out(multiplexer_5_out), .sel(or_1_out));
  Multiplexer #(.select(1), .width(1), .disabled("Z"), .enable("false")) multiplexer_6 (
    .in0(Beq), .in1(1'b0), .out(multiplexer_6_out), .sel(or_1_out));
  Multiplexer #(.select(1), .width(1), .disabled("Z"), .enable("false")) multiplexer_7 (
    .in0(Bne), .in1(1'b0), .out(multiplexer_7_out), .sel(or_1_out));
  Multiplexer #(.select(1), .width(1), .disabled("Z"), .enable("false")) multiplexer_8 (
    .in0(MemToReg), .in1(1'b0), .out(multiplexer_8_out), .sel(or_1_out));
  Multiplexer #(.select(1), .width(1), .disabled("Z"), .enable("false")) multiplexer_9 (
    .in0(MemWrite), .in1(1'b0), .out(multiplexer_9_out), .sel(or_1_out));
  Multiplexer #(.select(1), .width(1), .disabled("Z"), .enable("false")) multiplexer_10 (
    .in0(RegWrite), .in1(1'b0), .out(multiplexer_10_out), .sel(or_1_out));
  Multiplexer #(.select(1), .width(1), .disabled("Z"), .enable("false")) multiplexer_11 (
    .in0(AluSrcB), .in1(1'b0), .out(multiplexer_11_out), .sel(or_1_out));
  Multiplexer #(.select(1), .width(1), .disabled("Z"), .enable("false")) multiplexer_12 (
    .in0(jal), .in1(1'b0), .out(multiplexer_12_out), .sel(or_1_out));
  Multiplexer #(.select(1), .width(1), .disabled("Z"), .enable("false")) multiplexer_13 (
    .in0(jalr), .in1(1'b0), .out(multiplexer_13_out), .sel(or_1_out));
  Multiplexer #(.select(1), .width(1), .disabled("Z"), .enable("false")) multiplexer_14 (
    .in0(uret), .in1(1'b0), .out(multiplexer_14_out), .sel(or_1_out));
  Multiplexer #(.select(1), .width(1), .disabled("Z"), .enable("false")) multiplexer_15 (
    .in0(PredictJump), .in1(1'b0), .out(multiplexer_15_out), .sel(or_1_out));
  Multiplexer #(.select(1), .width(5), .disabled("Z"), .enable("false")) multiplexer_16 (
    .in0(rd), .in1({5{1'b0}}), .out(multiplexer_16_out), .sel(or_1_out));
  Multiplexer #(.select(1), .width(4), .disabled("Z"), .enable("false")) multiplexer_17 (
    .in0(AluOP), .in1(4'b0000), .out(multiplexer_17_out), .sel(or_1_out));
  Multiplexer #(.select(1), .width(32), .disabled("Z"), .enable("false")) multiplexer_18 (
    .in0(imm), .in1({32{1'b0}}), .out(multiplexer_18_out), .sel(or_1_out));
  Multiplexer #(.select(1), .width(32), .disabled("Z"), .enable("false")) multiplexer_19 (
    .in0(PC), .in1({32{1'b0}}), .out(multiplexer_19_out), .sel(or_1_out));
  Multiplexer #(.select(1), .width(32), .disabled("Z"), .enable("false")) multiplexer_20 (
    .in0(PC_4), .in1({32{1'b0}}), .out(multiplexer_20_out), .sel(or_1_out));
  Multiplexer #(.select(1), .width(32), .disabled("Z"), .enable("false")) multiplexer_21 (
    .in0(R1), .in1({32{1'b0}}), .out(multiplexer_21_out), .sel(or_1_out));
  Multiplexer #(.select(1), .width(32), .disabled("Z"), .enable("false")) multiplexer_22 (
    .in0(R2), .in1({32{1'b0}}), .out(multiplexer_22_out), .sel(or_1_out));
  Multiplexer #(.select(1), .width(32), .disabled("Z"), .enable("false")) multiplexer_23 (
    .in0(IR), .in1({32{1'b0}}), .out(multiplexer_23_out), .sel(or_1_out));
  Register #(.width(2), .trigger("rising"), .Select("low")) register_1 (
    .D(multiplexer_1_out), .en(en), .Q(Rs1Forward_2), .clk(Clk));  // open: clr
  Register #(.width(2), .trigger("rising"), .Select("low")) register_2 (
    .D(multiplexer_2_out), .en(en), .Q(Rs2Forward_2), .clk(Clk));  // open: clr
  Register #(.width(1), .trigger("rising"), .Select("low")) register_3 (
    .D(multiplexer_3_out), .en(en), .Q(lbu_2), .clk(Clk));  // open: clr
  Register #(.width(1), .trigger("rising"), .Select("low")) register_4 (
    .D(multiplexer_4_out), .en(en), .Q(bltu_2), .clk(Clk));  // open: clr
  Register #(.width(1), .trigger("rising"), .Select("low")) register_5 (
    .D(multiplexer_5_out), .en(en), .Q(ecall_2), .clk(Clk));  // open: clr
  Register #(.width(1), .trigger("rising"), .Select("low")) register_6 (
    .D(multiplexer_6_out), .en(en), .Q(Beq_2), .clk(Clk));  // open: clr
  Register #(.width(1), .trigger("rising"), .Select("low")) register_7 (
    .D(multiplexer_7_out), .en(en), .Q(Bne_2), .clk(Clk));  // open: clr
  Register #(.width(1), .trigger("rising"), .Select("low")) register_8 (
    .D(multiplexer_8_out), .en(en), .Q(MemToReg_2), .clk(Clk));  // open: clr
  Register #(.width(1), .trigger("rising"), .Select("low")) register_9 (
    .D(multiplexer_9_out), .en(en), .Q(MemWrite_2), .clk(Clk));  // open: clr
  Register #(.width(1), .trigger("rising"), .Select("low")) register_10 (
    .D(multiplexer_10_out), .en(en), .Q(RegWrite_2), .clk(Clk));  // open: clr
  Register #(.width(1), .trigger("rising"), .Select("low")) register_11 (
    .D(multiplexer_11_out), .en(en), .Q(AluSrcB_2), .clk(Clk));  // open: clr
  Register #(.width(1), .trigger("rising"), .Select("low")) register_12 (
    .D(multiplexer_12_out), .en(en), .Q(jal_2), .clk(Clk));  // open: clr
  Register #(.width(1), .trigger("rising"), .Select("low")) register_13 (
    .D(multiplexer_13_out), .en(en), .Q(jalr_2), .clk(Clk));  // open: clr
  Register #(.width(1), .trigger("rising"), .Select("low")) register_14 (
    .D(multiplexer_14_out), .en(en), .Q(uret_2), .clk(Clk));  // open: clr
  Register #(.width(1), .trigger("rising"), .Select("low")) register_15 (
    .D(multiplexer_15_out), .en(en), .Q(PredictJump_2), .clk(Clk));  // open: clr
  Register #(.width(5), .trigger("rising"), .Select("low")) register_16 (
    .D(multiplexer_16_out), .en(en), .Q(rd_2), .clk(Clk));  // open: clr
  Register #(.width(4), .trigger("rising"), .Select("low")) register_17 (
    .D(multiplexer_17_out), .en(en), .Q(AluOP_2), .clk(Clk));  // open: clr
  Register #(.width(32), .trigger("rising"), .Select("low")) register_18 (
    .D(multiplexer_18_out), .en(en), .Q(imm_2), .clk(Clk));  // open: clr
  Register #(.width(32), .trigger("rising"), .Select("low")) register_19 (
    .D(multiplexer_19_out), .en(en), .Q(PC_2), .clk(Clk));  // open: clr
  Register #(.width(32), .trigger("rising"), .Select("low")) register_20 (
    .D(multiplexer_20_out), .en(en), .Q(PC_4_2), .clk(Clk));  // open: clr
  Register #(.width(32), .trigger("rising"), .Select("low")) register_21 (
    .D(multiplexer_21_out), .en(en), .Q(R1_2), .clk(Clk));  // open: clr
  Register #(.width(32), .trigger("rising"), .Select("low")) register_22 (
    .D(multiplexer_22_out), .en(en), .Q(R2_2), .clk(Clk));  // open: clr
  Register #(.width(32), .trigger("rising"), .Select("low")) register_23 (
    .D(multiplexer_23_out), .en(en), .Q(IR_2), .clk(Clk));  // open: clr
endmodule

module EX_MEM (
  input  lbu,
  input  jal,
  input  jalr,
  input  MemToReg,
  input  MemWrite,
  input  RegWrite,
  input  halt,
  input  [4:0] rd,
  input  [31:0] PC,
  input  [31:0] PC_4,
  input  [31:0] IR,
  input  [31:0] MDin,
  input  [31:0] AluResuult,
  input  en,
  input  Clk,
  input  reset,
  input  flush,
  output lbu_2,
  output jal_2,
  output jalr_2,
  output MemToReg_2,
  output MemWrite_2,
  output RegWrite_2,
  output halt_2,
  output [4:0] rd_2,
  output [31:0] PC_2,
  output [31:0] PC_4_2,
  output [31:0] IR_2,
  output [31:0] MDin_2,
  output [31:0] AluResuult_2
);

  wire multiplexer_1_out, multiplexer_2_out, multiplexer_3_out, multiplexer_4_out, multiplexer_5_out,
       multiplexer_6_out, multiplexer_7_out, or_1_out;
  wire [4:0] multiplexer_8_out;
  wire [31:0] multiplexer_9_out, multiplexer_10_out, multiplexer_11_out, multiplexer_12_out,
       multiplexer_13_out;

  or or_1 (or_1_out, reset, flush);
  Multiplexer #(.select(1), .width(1), .disabled("Z"), .enable("false")) multiplexer_1 (
    .in0(lbu), .in1(1'b0), .out(multiplexer_1_out), .sel(or_1_out));
  Multiplexer #(.select(1), .width(1), .disabled("Z"), .enable("false")) multiplexer_2 (
    .in0(jal), .in1(1'b0), .out(multiplexer_2_out), .sel(or_1_out));
  Multiplexer #(.select(1), .width(1), .disabled("Z"), .enable("false")) multiplexer_3 (
    .in0(jalr), .in1(1'b0), .out(multiplexer_3_out), .sel(or_1_out));
  Multiplexer #(.select(1), .width(1), .disabled("Z"), .enable("false")) multiplexer_4 (
    .in0(MemToReg), .in1(1'b0), .out(multiplexer_4_out), .sel(or_1_out));
  Multiplexer #(.select(1), .width(1), .disabled("Z"), .enable("false")) multiplexer_5 (
    .in0(MemWrite), .in1(1'b0), .out(multiplexer_5_out), .sel(or_1_out));
  Multiplexer #(.select(1), .width(1), .disabled("Z"), .enable("false")) multiplexer_6 (
    .in0(RegWrite), .in1(1'b0), .out(multiplexer_6_out), .sel(or_1_out));
  Multiplexer #(.select(1), .width(1), .disabled("Z"), .enable("false")) multiplexer_7 (
    .in0(halt), .in1(1'b0), .out(multiplexer_7_out), .sel(or_1_out));
  Multiplexer #(.select(1), .width(5), .disabled("Z"), .enable("false")) multiplexer_8 (
    .in0(rd), .in1({5{1'b0}}), .out(multiplexer_8_out), .sel(or_1_out));
  Multiplexer #(.select(1), .width(32), .disabled("Z"), .enable("false")) multiplexer_9 (
    .in0(PC), .in1({32{1'b0}}), .out(multiplexer_9_out), .sel(or_1_out));
  Multiplexer #(.select(1), .width(32), .disabled("Z"), .enable("false")) multiplexer_10 (
    .in0(PC_4), .in1({32{1'b0}}), .out(multiplexer_10_out), .sel(or_1_out));
  Multiplexer #(.select(1), .width(32), .disabled("Z"), .enable("false")) multiplexer_11 (
    .in0(IR), .in1({32{1'b0}}), .out(multiplexer_11_out), .sel(or_1_out));
  Multiplexer #(.select(1), .width(32), .disabled("Z"), .enable("false")) multiplexer_12 (
    .in0(MDin), .in1({32{1'b0}}), .out(multiplexer_12_out), .sel(or_1_out));
  Multiplexer #(.select(1), .width(32), .disabled("Z"), .enable("false")) multiplexer_13 (
    .in0(AluResuult), .in1({32{1'b0}}), .out(multiplexer_13_out), .sel(or_1_out));
  Register #(.width(1), .trigger("rising"), .Select("low")) register_1 (
    .D(multiplexer_1_out), .en(en), .Q(lbu_2), .clk(Clk));  // open: clr
  Register #(.width(1), .trigger("rising"), .Select("low")) register_2 (
    .D(multiplexer_2_out), .en(en), .Q(jal_2), .clk(Clk));  // open: clr
  Register #(.width(1), .trigger("rising"), .Select("low")) register_3 (
    .D(multiplexer_3_out), .en(en), .Q(jalr_2), .clk(Clk));  // open: clr
  Register #(.width(1), .trigger("rising"), .Select("low")) register_4 (
    .D(multiplexer_4_out), .en(en), .Q(MemToReg_2), .clk(Clk));  // open: clr
  Register #(.width(1), .trigger("rising"), .Select("low")) register_5 (
    .D(multiplexer_5_out), .en(en), .Q(MemWrite_2), .clk(Clk));  // open: clr
  Register #(.width(1), .trigger("rising"), .Select("low")) register_6 (
    .D(multiplexer_6_out), .en(en), .Q(RegWrite_2), .clk(Clk));  // open: clr
  Register #(.width(1), .trigger("rising"), .Select("low")) register_7 (
    .D(multiplexer_7_out), .en(en), .Q(halt_2), .clk(Clk));  // open: clr
  Register #(.width(5), .trigger("rising"), .Select("low")) register_8 (
    .D(multiplexer_8_out), .en(en), .Q(rd_2), .clk(Clk));  // open: clr
  Register #(.width(32), .trigger("rising"), .Select("low")) register_9 (
    .D(multiplexer_9_out), .en(en), .Q(PC_2), .clk(Clk));  // open: clr
  Register #(.width(32), .trigger("rising"), .Select("low")) register_10 (
    .D(multiplexer_10_out), .en(en), .Q(PC_4_2), .clk(Clk));  // open: clr
  Register #(.width(32), .trigger("rising"), .Select("low")) register_11 (
    .D(multiplexer_11_out), .en(en), .Q(IR_2), .clk(Clk));  // open: clr
  Register #(.width(32), .trigger("rising"), .Select("low")) register_12 (
    .D(multiplexer_12_out), .en(en), .Q(MDin_2), .clk(Clk));  // open: clr
  Register #(.width(32), .trigger("rising"), .Select("low")) register_13 (
    .D(multiplexer_13_out), .en(en), .Q(AluResuult_2), .clk(Clk));  // open: clr
endmodule

module MEM_WB (
  input  jal,
  input  jalr,
  input  MemToReg,
  input  RegWrite,
  input  halt,
  input  [4:0] rd,
  input  [31:0] PC,
  input  [31:0] PC_4,
  input  [31:0] IR,
  input  [31:0] AluResuult,
  input  [31:0] MDout,
  input  reset,
  input  en,
  input  Clk,
  output jal_2,
  output jalr_2,
  output MemToReg_2,
  output RegWrite_2,
  output halt_2,
  output [4:0] rd_2,
  output [31:0] PC_2,
  output [31:0] PC_4_2,
  output [31:0] IR_2,
  output [31:0] AluResuult_2,
  output [31:0] MDout_2
);

  wire multiplexer_1_out, multiplexer_2_out, multiplexer_3_out, multiplexer_4_out, multiplexer_5_out;
  wire [4:0] multiplexer_6_out;
  wire [31:0] multiplexer_7_out, multiplexer_8_out, multiplexer_9_out, multiplexer_10_out, multiplexer_11_out;

  Multiplexer #(.select(1), .width(1), .disabled("Z"), .enable("false")) multiplexer_1 (
    .in0(jal), .in1(1'b0), .out(multiplexer_1_out), .sel(reset));
  Multiplexer #(.select(1), .width(1), .disabled("Z"), .enable("false")) multiplexer_2 (
    .in0(jalr), .in1(1'b0), .out(multiplexer_2_out), .sel(reset));
  Multiplexer #(.select(1), .width(1), .disabled("Z"), .enable("false")) multiplexer_3 (
    .in0(MemToReg), .in1(1'b0), .out(multiplexer_3_out), .sel(reset));
  Multiplexer #(.select(1), .width(1), .disabled("Z"), .enable("false")) multiplexer_4 (
    .in0(RegWrite), .in1(1'b0), .out(multiplexer_4_out), .sel(reset));
  Multiplexer #(.select(1), .width(1), .disabled("Z"), .enable("false")) multiplexer_5 (
    .in0(halt), .in1(1'b0), .out(multiplexer_5_out), .sel(reset));
  Multiplexer #(.select(1), .width(5), .disabled("Z"), .enable("false")) multiplexer_6 (
    .in0(rd), .in1({5{1'b0}}), .out(multiplexer_6_out), .sel(reset));
  Multiplexer #(.select(1), .width(32), .disabled("Z"), .enable("false")) multiplexer_7 (
    .in0(PC), .in1({32{1'b0}}), .out(multiplexer_7_out), .sel(reset));
  Multiplexer #(.select(1), .width(32), .disabled("Z"), .enable("false")) multiplexer_8 (
    .in0(PC_4), .in1({32{1'b0}}), .out(multiplexer_8_out), .sel(reset));
  Multiplexer #(.select(1), .width(32), .disabled("Z"), .enable("false")) multiplexer_9 (
    .in0(IR), .in1({32{1'b0}}), .out(multiplexer_9_out), .sel(reset));
  Multiplexer #(.select(1), .width(32), .disabled("Z"), .enable("false")) multiplexer_10 (
    .in0(AluResuult), .in1({32{1'b0}}), .out(multiplexer_10_out), .sel(reset));
  Multiplexer #(.select(1), .width(32), .disabled("Z"), .enable("false")) multiplexer_11 (
    .in0(MDout), .in1({32{1'b0}}), .out(multiplexer_11_out), .sel(reset));
  Register #(.width(1), .trigger("rising"), .Select("low")) register_1 (
    .D(multiplexer_1_out), .en(en), .Q(jal_2), .clk(Clk));  // open: clr
  Register #(.width(1), .trigger("rising"), .Select("low")) register_2 (
    .D(multiplexer_2_out), .en(en), .Q(jalr_2), .clk(Clk));  // open: clr
  Register #(.width(1), .trigger("rising"), .Select("low")) register_3 (
    .D(multiplexer_3_out), .en(en), .Q(MemToReg_2), .clk(Clk));  // open: clr
  Register #(.width(1), .trigger("rising"), .Select("low")) register_4 (
    .D(multiplexer_4_out), .en(en), .Q(RegWrite_2), .clk(Clk));  // open: clr
  Register #(.width(1), .trigger("rising"), .Select("low")) register_5 (
    .D(multiplexer_5_out), .en(en), .Q(halt_2), .clk(Clk));  // open: clr
  Register #(.width(5), .trigger("rising"), .Select("low")) register_6 (
    .D(multiplexer_6_out), .en(en), .Q(rd_2), .clk(Clk));  // open: clr
  Register #(.width(32), .trigger("rising"), .Select("low")) register_7 (
    .D(multiplexer_7_out), .en(en), .Q(PC_2), .clk(Clk));  // open: clr
  Register #(.width(32), .trigger("rising"), .Select("low")) register_8 (
    .D(multiplexer_8_out), .en(en), .Q(PC_4_2), .clk(Clk));  // open: clr
  Register #(.width(32), .trigger("rising"), .Select("low")) register_9 (
    .D(multiplexer_9_out), .en(en), .Q(IR_2), .clk(Clk));  // open: clr
  Register #(.width(32), .trigger("rising"), .Select("low")) register_10 (
    .D(multiplexer_10_out), .en(en), .Q(AluResuult_2), .clk(Clk));  // open: clr
  Register #(.width(32), .trigger("rising"), .Select("low")) register_11 (
    .D(multiplexer_11_out), .en(en), .Q(MDout_2), .clk(Clk));  // open: clr
endmodule

module \气泡处理逻辑  (
  input  EX_RegWrite,
  input  MEM_RegWrite,
  input  [4:0] EX_WriteReg_num,
  input  [4:0] MEM_WriteReg_num,
  input  Rs1Used,
  input  [4:0] Rs1,
  input  Rs2Used,
  input  [4:0] Rs2,
  input  BranchTaken,
  input  ecall,
  output Stall,
  output Flush
);

  wire and_1_out, and_2_out, and_3_out, and_4_out, and_5_out, and_6_out, comparator_1_eq, comparator_2_eq,
       comparator_3_eq, comparator_4_eq, comparator_5_eq, comparator_6_eq, comparator_7_eq, comparator_8_eq,
       comparator_9_eq, comparator_10_eq, not_1_out, not_2_out, or_1_out, or_2_out;

  not not_1 (not_1_out, comparator_1_eq);
  Comparator #(.width(5), .mode("unsigned")) comparator_1 (
    .a(Rs1), .b({5{1'b0}}), .eq(comparator_1_eq));  // open: gt, lt
  Comparator #(.width(5), .mode("unsigned")) comparator_2 (
    .a(Rs1), .b(EX_WriteReg_num), .eq(comparator_2_eq));  // open: gt, lt
  Comparator #(.width(5), .mode("unsigned")) comparator_3 (
    .a(Rs1), .b(MEM_WriteReg_num), .eq(comparator_3_eq));  // open: gt, lt
  Comparator #(.width(5), .mode("unsigned")) comparator_4 (
    .a(Rs2), .b({5{1'b0}}), .eq(comparator_4_eq));  // open: gt, lt
  not not_2 (not_2_out, comparator_4_eq);
  Comparator #(.width(5), .mode("unsigned")) comparator_5 (
    .a(Rs2), .b(EX_WriteReg_num), .eq(comparator_5_eq));  // open: gt, lt
  Comparator #(.width(5), .mode("unsigned")) comparator_6 (
    .a(Rs2), .b(MEM_WriteReg_num), .eq(comparator_6_eq));  // open: gt, lt
  Comparator #(.width(5), .mode("unsigned")) comparator_7 (
    .a(5'b01010), .b(EX_WriteReg_num), .eq(comparator_7_eq));  // open: gt, lt
  Comparator #(.width(5), .mode("unsigned")) comparator_8 (
    .a(EX_WriteReg_num), .b(5'b10001), .eq(comparator_8_eq));  // open: gt, lt
  Comparator #(.width(5), .mode("unsigned")) comparator_9 (
    .a(5'b01010), .b(MEM_WriteReg_num), .eq(comparator_9_eq));  // open: gt, lt
  Comparator #(.width(5), .mode("unsigned")) comparator_10 (
    .a(MEM_WriteReg_num), .b(5'b10001), .eq(comparator_10_eq));  // open: gt, lt
  or or_1 (or_1_out, comparator_7_eq, comparator_8_eq);
  or or_2 (or_2_out, comparator_9_eq, comparator_10_eq);
  and and_1 (and_1_out, Rs1Used, EX_RegWrite, not_1_out, comparator_2_eq);
  and and_2 (and_2_out, Rs1Used, MEM_RegWrite, not_1_out, comparator_3_eq);
  and and_3 (and_3_out, Rs2Used, EX_RegWrite, not_2_out, comparator_5_eq);
  and and_4 (and_4_out, Rs2Used, MEM_RegWrite, not_2_out, comparator_6_eq);
  and and_5 (and_5_out, ecall, EX_RegWrite, or_1_out);
  and and_6 (and_6_out, ecall, MEM_RegWrite, or_2_out);
  or or_3 (Stall, and_1_out, and_2_out, and_3_out, and_4_out, and_5_out, and_6_out);
  or or_4 (Flush, Stall, BranchTaken);

  // Other names for the same wires on the sheet: DataHazzard = Stall
endmodule

module \重定向相关处理逻辑  (
  input  Rs1Used,
  input  [4:0] Rs1,
  input  [4:0] EX_WriteReg_num,
  input  EX_MemToReg,
  input  Rs2Used,
  input  [4:0] Rs2,
  input  [4:0] MEM_WriteReg_num,
  input  BranchTaken,
  input  EX_RegWrite,
  input  MEM_RegWrite,
  input  ecall,
  output Stall,
  output Flush,
  output [1:0] Rs1Foward,
  output [1:0] Rs2Foward
);

  wire and_1_out, and_2_out, and_3_out, and_4_out, and_5_out, and_6_out, and_9_out, and_10_out, and_11_out,
       and_12_out, comparator_1_eq, comparator_2_eq, comparator_3_eq, comparator_4_eq, comparator_5_eq,
       comparator_6_eq, comparator_7_eq, comparator_8_eq, comparator_9_eq, comparator_10_eq,
       comparator_11_eq, comparator_12_eq, comparator_13_eq, comparator_14_eq, ecall1, ecall2, ecall3,
       ecall4, not_1_out, not_2_out, not_3_out, not_4_out, or_3_out, or_5_out;

  Comparator #(.width(5), .mode("twosComplement")) comparator_1 (
    .a(Rs1), .b({5{1'b0}}), .eq(comparator_1_eq));  // open: gt, lt
  not not_1 (not_1_out, comparator_1_eq);
  Comparator #(.width(5), .mode("twosComplement")) comparator_2 (
    .a(Rs1), .b(EX_WriteReg_num), .eq(comparator_2_eq));  // open: gt, lt
  not not_2 (not_2_out, comparator_3_eq);
  Comparator #(.width(5), .mode("twosComplement")) comparator_3 (
    .a(Rs2), .b({5{1'b0}}), .eq(comparator_3_eq));  // open: gt, lt
  Comparator #(.width(5), .mode("twosComplement")) comparator_4 (
    .a(Rs2), .b(EX_WriteReg_num), .eq(comparator_4_eq));  // open: gt, lt
  not not_3 (not_3_out, comparator_5_eq);
  Comparator #(.width(5), .mode("unsigned")) comparator_5 (
    .a(Rs1), .b({5{1'b0}}), .eq(comparator_5_eq));  // open: gt, lt
  Comparator #(.width(5), .mode("unsigned")) comparator_6 (
    .a(Rs1), .b(EX_WriteReg_num), .eq(comparator_6_eq));  // open: gt, lt
  Comparator #(.width(5), .mode("unsigned")) comparator_7 (
    .a(Rs1), .b(MEM_WriteReg_num), .eq(comparator_7_eq));  // open: gt, lt
  Comparator #(.width(5), .mode("unsigned")) comparator_8 (
    .a(Rs2), .b({5{1'b0}}), .eq(comparator_8_eq));  // open: gt, lt
  not not_4 (not_4_out, comparator_8_eq);
  Comparator #(.width(5), .mode("unsigned")) comparator_9 (
    .a(Rs2), .b(EX_WriteReg_num), .eq(comparator_9_eq));  // open: gt, lt
  Comparator #(.width(5), .mode("unsigned")) comparator_10 (
    .a(Rs2), .b(MEM_WriteReg_num), .eq(comparator_10_eq));  // open: gt, lt
  and and_1 (and_1_out, Rs1Used, not_1_out, comparator_2_eq, EX_MemToReg);
  and and_2 (and_2_out, Rs2Used, not_2_out, comparator_4_eq, EX_MemToReg);
  or or_1 (Stall, and_1_out, and_2_out);
  and and_3 (and_3_out, Rs1Used, EX_RegWrite, not_3_out, comparator_6_eq);
  and and_4 (and_4_out, not_3_out, Rs1Used, MEM_RegWrite, comparator_7_eq);
  and and_5 (and_5_out, Rs2Used, EX_RegWrite, not_4_out, comparator_9_eq);
  and and_6 (and_6_out, not_4_out, Rs2Used, MEM_RegWrite, comparator_10_eq);
  or or_2 (Rs1Foward[1], ecall1, and_3_out);
  or or_3 (or_3_out, and_4_out, ecall2);
  or or_4 (Rs2Foward[1], ecall3, and_5_out);
  or or_5 (or_5_out, and_6_out, ecall4);
  and and_7 (Rs1Foward[0], ~Rs1Foward[1], or_3_out);  // AND_Gate
  and and_8 (Rs2Foward[0], ~Rs2Foward[1], or_5_out);  // AND_Gate
  and and_9 (and_9_out, EX_RegWrite, ecall);
  and and_10 (and_10_out, MEM_RegWrite, ecall);
  and and_11 (and_11_out, EX_RegWrite, ecall);
  and and_12 (and_12_out, MEM_RegWrite, ecall);
  or or_6 (Flush, Stall, BranchTaken);
  Comparator #(.width(5), .mode("unsigned")) comparator_11 (
    .a(EX_WriteReg_num), .b(5'b10001), .eq(comparator_11_eq));  // open: gt, lt
  Comparator #(.width(5), .mode("unsigned")) comparator_12 (
    .a(5'b10001), .b(MEM_WriteReg_num), .eq(comparator_12_eq));  // open: gt, lt
  Comparator #(.width(5), .mode("unsigned")) comparator_13 (
    .a(EX_WriteReg_num), .b(5'b01010), .eq(comparator_13_eq));  // open: gt, lt
  Comparator #(.width(5), .mode("unsigned")) comparator_14 (
    .a(5'b01010), .b(MEM_WriteReg_num), .eq(comparator_14_eq));  // open: gt, lt
  and and_13 (ecall1, and_9_out, comparator_11_eq);
  and and_14 (ecall2, and_10_out, comparator_12_eq);
  and and_15 (ecall3, and_11_out, comparator_13_eq);
  and and_16 (ecall4, and_12_out, comparator_14_eq);

  // Other names for the same wires on the sheet: LoadUse = Stall
endmodule
module BTB (
  input  CLK,
  input  EX_Branch,
  input  EX_BranchTaken,
  input  [31:0] PC,
  input  [31:0] EX_PC,
  input  [31:0] EX_BranchAddr,
  output PredictJump,
  output [31:0] JumpAdrr
);

  wire and_17_out, and_26_out, and_27_out, and_28_out, and_29_out, and_30_out, and_31_out, and_32_out,
       and_33_out, comparator_1_eq, comparator_2_eq, comparator_3_eq, comparator_4_eq, comparator_5_eq,
       comparator_6_eq, comparator_7_eq, comparator_8_eq, comparator_9_eq, comparator_10_eq,
       comparator_11_eq, comparator_12_eq, comparator_13_eq, comparator_14_eq, comparator_15_eq,
       comparator_16_eq, d_ff_1_q, d_ff_2_q, d_ff_3_q, d_ff_4_q, d_ff_5_q, d_ff_6_q, d_ff_7_q, d_ff_8_q,
       decoder_1_out0, decoder_1_out1, decoder_1_out2, decoder_1_out3, decoder_1_out4, decoder_1_out5,
       decoder_1_out6, decoder_1_out7, decoder_2_out0, decoder_2_out1, decoder_2_out2, decoder_2_out3,
       decoder_2_out4, decoder_2_out5, decoder_2_out6, decoder_2_out7, EX_hit, EX_miss, L0, L1, L2, L3, L4,
       L5, L6, L7, not_1_out, not_2_out, not_3_out, not_4_out, not_5_out, not_6_out, not_7_out, not_8_out,
       or_1_out, or_2_out, or_3_out, or_4_out, or_5_out, or_6_out, or_7_out, or_8_out, or_10_out, or_11_out,
       or_12_out, or_13_out, or_14_out, or_15_out, or_16_out, or_17_out, or_18_out, or_19_out, or_20_out,
       or_21_out, or_22_out, or_23_out, or_24_out, or_25_out, priority_encoder_1_gs, v0, v1, v2, v3, v4, v5,
       v6, v7, w0, w1, w2, w3, w4, w5, w6, w7, WriteL0, WriteL1, WriteL2, WriteL3, WriteL4, WriteL5, WriteL6,
       WriteL7;
  wire [0:0] controlled_buffer_9_out, controlled_buffer_10_out, controlled_buffer_11_out,
       controlled_buffer_12_out, controlled_buffer_13_out, controlled_buffer_14_out,
       controlled_buffer_15_out, controlled_buffer_16_out;
  wire [1:0] predict0, predict1, predict2, predict3, predict4, predict5, predict6, predict7,
       \双位预测状态转换_1_nextlow , \双位预测状态转换_2_nextlow , \双位预测状态转换_3_nextlow , \双位预测状态转换_4_nextlow ,
       \双位预测状态转换_5_nextlow , \双位预测状态转换_6_nextlow , \双位预测状态转换_7_nextlow , \双位预测状态转换_8_nextlow ;
  wire [2:0] max2_1_max_num, max2_2_max_num, max2_3_max_num, max2_4_max_num, max2_5_max_num, max2_6_max_num,
       max2_7_max_num, priority_encoder_1_out;
  wire [31:0] c0, c1, c2, c3, c4, c5, c6, c7, max2_1_max, max2_2_max, max2_3_max, max2_4_max, max2_5_max,
       max2_6_max, register_17_q, register_18_q, register_19_q, register_20_q, register_21_q, register_22_q,
       register_23_q, register_24_q, Tag0, Tag1, Tag2, Tag3, Tag4, Tag5, Tag6, Tag7;

  Register #(.width(1), .trigger("rising"), .Select("low")) register_1 (
    .D(1'b1), .en(WriteL0), .Q(v0), .clk(CLK));  // open: clr
  Register #(.width(1), .trigger("rising"), .Select("low")) register_2 (
    .D(1'b1), .en(WriteL1), .Q(v1), .clk(CLK));  // open: clr
  Register #(.width(1), .trigger("rising"), .Select("low")) register_3 (
    .D(1'b1), .en(WriteL2), .Q(v2), .clk(CLK));  // open: clr
  Register #(.width(1), .trigger("rising"), .Select("low")) register_4 (
    .D(1'b1), .en(WriteL3), .Q(v3), .clk(CLK));  // open: clr
  Register #(.width(1), .trigger("rising"), .Select("low")) register_5 (
    .D(1'b1), .en(WriteL4), .Q(v4), .clk(CLK));  // open: clr
  Register #(.width(1), .trigger("rising"), .Select("low")) register_6 (
    .D(1'b1), .en(WriteL5), .Q(v5), .clk(CLK));  // open: clr
  Register #(.width(1), .trigger("rising"), .Select("low")) register_7 (
    .D(1'b1), .en(WriteL6), .Q(v6), .clk(CLK));  // open: clr
  Register #(.width(1), .trigger("rising"), .Select("low")) register_8 (
    .D(1'b1), .en(WriteL7), .Q(v7), .clk(CLK));  // open: clr
  Register #(.width(32), .trigger("rising"), .Select("low")) register_9 (
    .D(EX_PC), .en(WriteL0), .Q(Tag0), .clk(CLK));  // open: clr
  Register #(.width(32), .trigger("rising"), .Select("low")) register_10 (
    .D(EX_PC), .en(WriteL1), .Q(Tag1), .clk(CLK));  // open: clr
  Register #(.width(32), .trigger("rising"), .Select("low")) register_11 (
    .D(EX_PC), .en(WriteL2), .Q(Tag2), .clk(CLK));  // open: clr
  Register #(.width(32), .trigger("rising"), .Select("low")) register_12 (
    .D(EX_PC), .en(WriteL3), .Q(Tag3), .clk(CLK));  // open: clr
  Register #(.width(32), .trigger("rising"), .Select("low")) register_13 (
    .D(EX_PC), .en(WriteL4), .Q(Tag4), .clk(CLK));  // open: clr
  Register #(.width(32), .trigger("rising"), .Select("low")) register_14 (
    .D(EX_PC), .en(WriteL5), .Q(Tag5), .clk(CLK));  // open: clr
  Register #(.width(32), .trigger("rising"), .Select("low")) register_15 (
    .D(EX_PC), .en(WriteL6), .Q(Tag6), .clk(CLK));  // open: clr
  Register #(.width(32), .trigger("rising"), .Select("low")) register_16 (
    .D(EX_PC), .en(WriteL7), .Q(Tag7), .clk(CLK));  // open: clr
  or or_1 (or_1_out, WriteL0, L0);
  or or_2 (or_2_out, WriteL1, L1);
  or or_3 (or_3_out, WriteL2, L2);
  or or_4 (or_4_out, WriteL3, L3);
  or or_5 (or_5_out, WriteL4, L4);
  or or_6 (or_6_out, WriteL5, L5);
  or or_7 (or_7_out, WriteL6, L6);
  or or_8 (or_8_out, WriteL7, L7);
  Counter #(.width(32), .max('hffffffff), .ongoal("wrap"), .trigger("rising"), .behavior("new")) counter_1 (
    .Q(c0), .clk(CLK), .clr(d_ff_1_q));  // open: load, D, count, carry, preset, down
  D_Flip_Flop #(.trigger("rising"), .Pre_Clr_Positions("LEGACY"), .NegatePresetClear("false"), .enable("true"), .NewFFLayout("false")) d_ff_1 (
    .clk(CLK), .D(or_1_out), .Q(d_ff_1_q));  // open: Qn, preset, en, reset
  Counter #(.width(32), .max('hffffffff), .ongoal("wrap"), .trigger("rising"), .behavior("new")) counter_2 (
    .Q(c1), .clk(CLK), .clr(d_ff_2_q));  // open: load, D, count, carry, preset, down
  D_Flip_Flop #(.trigger("rising"), .Pre_Clr_Positions("LEGACY"), .NegatePresetClear("false"), .enable("true"), .NewFFLayout("false")) d_ff_2 (
    .clk(CLK), .D(or_2_out), .Q(d_ff_2_q));  // open: Qn, preset, en, reset
  Counter #(.width(32), .max('hffffffff), .ongoal("wrap"), .trigger("rising"), .behavior("new")) counter_3 (
    .Q(c2), .clk(CLK), .clr(d_ff_3_q));  // open: load, D, count, carry, preset, down
  D_Flip_Flop #(.trigger("rising"), .Pre_Clr_Positions("LEGACY"), .NegatePresetClear("false"), .enable("true"), .NewFFLayout("false")) d_ff_3 (
    .clk(CLK), .D(or_3_out), .Q(d_ff_3_q));  // open: Qn, preset, en, reset
  Counter #(.width(32), .max('hffffffff), .ongoal("wrap"), .trigger("rising"), .behavior("new")) counter_4 (
    .Q(c3), .clk(CLK), .clr(d_ff_4_q));  // open: load, D, count, carry, preset, down
  D_Flip_Flop #(.trigger("rising"), .Pre_Clr_Positions("LEGACY"), .NegatePresetClear("false"), .enable("true"), .NewFFLayout("false")) d_ff_4 (
    .clk(CLK), .D(or_4_out), .Q(d_ff_4_q));  // open: Qn, preset, en, reset
  Counter #(.width(32), .max('hffffffff), .ongoal("wrap"), .trigger("rising"), .behavior("new")) counter_5 (
    .Q(c4), .clk(CLK), .clr(d_ff_5_q));  // open: load, D, count, carry, preset, down
  D_Flip_Flop #(.trigger("rising"), .Pre_Clr_Positions("LEGACY"), .NegatePresetClear("false"), .enable("true"), .NewFFLayout("false")) d_ff_5 (
    .clk(CLK), .D(or_5_out), .Q(d_ff_5_q));  // open: Qn, preset, en, reset
  Counter #(.width(32), .max('hffffffff), .ongoal("wrap"), .trigger("rising"), .behavior("new")) counter_6 (
    .Q(c5), .clk(CLK), .clr(d_ff_6_q));  // open: load, D, count, carry, preset, down
  D_Flip_Flop #(.trigger("rising"), .Pre_Clr_Positions("LEGACY"), .NegatePresetClear("false"), .enable("true"), .NewFFLayout("false")) d_ff_6 (
    .clk(CLK), .D(or_6_out), .Q(d_ff_6_q));  // open: Qn, preset, en, reset
  Counter #(.width(32), .max('hffffffff), .ongoal("wrap"), .trigger("rising"), .behavior("new")) counter_7 (
    .Q(c6), .clk(CLK), .clr(d_ff_7_q));  // open: load, D, count, carry, preset, down
  D_Flip_Flop #(.trigger("rising"), .Pre_Clr_Positions("LEGACY"), .NegatePresetClear("false"), .enable("true"), .NewFFLayout("false")) d_ff_7 (
    .clk(CLK), .D(or_7_out), .Q(d_ff_7_q));  // open: Qn, preset, en, reset
  Counter #(.width(32), .max('hffffffff), .ongoal("wrap"), .trigger("rising"), .behavior("new")) counter_8 (
    .Q(c7), .clk(CLK), .clr(d_ff_8_q));  // open: load, D, count, carry, preset, down
  D_Flip_Flop #(.trigger("rising"), .Pre_Clr_Positions("LEGACY"), .NegatePresetClear("false"), .enable("true"), .NewFFLayout("false")) d_ff_8 (
    .clk(CLK), .D(or_8_out), .Q(d_ff_8_q));  // open: Qn, preset, en, reset
  assign JumpAdrr = L0 ? register_17_q : 32'bz;  // Controlled_Buffer controlled_buffer_1
  Register #(.width(32), .trigger("rising"), .Select("low")) register_17 (
    .D(EX_BranchAddr), .en(WriteL0), .Q(register_17_q), .clk(CLK));  // open: clr
  Register #(.width(32), .trigger("rising"), .Select("low")) register_18 (
    .D(EX_BranchAddr), .en(WriteL1), .Q(register_18_q), .clk(CLK));  // open: clr
  assign JumpAdrr = L1 ? register_18_q : 32'bz;  // Controlled_Buffer controlled_buffer_2
  Register #(.width(32), .trigger("rising"), .Select("low")) register_19 (
    .D(EX_BranchAddr), .en(WriteL2), .Q(register_19_q), .clk(CLK));  // open: clr
  assign JumpAdrr = L2 ? register_19_q : 32'bz;  // Controlled_Buffer controlled_buffer_3
  Register #(.width(32), .trigger("rising"), .Select("low")) register_20 (
    .D(EX_BranchAddr), .en(WriteL3), .Q(register_20_q), .clk(CLK));  // open: clr
  assign JumpAdrr = L3 ? register_20_q : 32'bz;  // Controlled_Buffer controlled_buffer_4
  Register #(.width(32), .trigger("rising"), .Select("low")) register_21 (
    .D(EX_BranchAddr), .en(WriteL4), .Q(register_21_q), .clk(CLK));  // open: clr
  assign JumpAdrr = L4 ? register_21_q : 32'bz;  // Controlled_Buffer controlled_buffer_5
  assign JumpAdrr = L5 ? register_22_q : 32'bz;  // Controlled_Buffer controlled_buffer_6
  Register #(.width(32), .trigger("rising"), .Select("low")) register_22 (
    .D(EX_BranchAddr), .en(WriteL5), .Q(register_22_q), .clk(CLK));  // open: clr
  assign JumpAdrr = L6 ? register_23_q : 32'bz;  // Controlled_Buffer controlled_buffer_7
  Register #(.width(32), .trigger("rising"), .Select("low")) register_23 (
    .D(EX_BranchAddr), .en(WriteL6), .Q(register_23_q), .clk(CLK));  // open: clr
  Register #(.width(32), .trigger("rising"), .Select("low")) register_24 (
    .D(EX_BranchAddr), .en(WriteL7), .Q(register_24_q), .clk(CLK));  // open: clr
  assign JumpAdrr = L7 ? register_24_q : 32'bz;  // Controlled_Buffer controlled_buffer_8
  Comparator #(.width(32), .mode("twosComplement")) comparator_1 (
    .a(PC), .b(Tag0), .eq(comparator_1_eq));  // open: gt, lt
  Comparator #(.width(32), .mode("twosComplement")) comparator_2 (
    .a(Tag0), .b(EX_PC), .eq(comparator_2_eq));  // open: gt, lt
  Comparator #(.width(32), .mode("twosComplement")) comparator_3 (
    .a(PC), .b(Tag1), .eq(comparator_3_eq));  // open: gt, lt
  Comparator #(.width(32), .mode("twosComplement")) comparator_4 (
    .a(Tag1), .b(EX_PC), .eq(comparator_4_eq));  // open: gt, lt
  Comparator #(.width(32), .mode("twosComplement")) comparator_5 (
    .a(PC), .b(Tag2), .eq(comparator_5_eq));  // open: gt, lt
  Comparator #(.width(32), .mode("twosComplement")) comparator_6 (
    .a(Tag2), .b(EX_PC), .eq(comparator_6_eq));  // open: gt, lt
  Comparator #(.width(32), .mode("twosComplement")) comparator_7 (
    .a(PC), .b(Tag3), .eq(comparator_7_eq));  // open: gt, lt
  Comparator #(.width(32), .mode("twosComplement")) comparator_8 (
    .a(Tag3), .b(EX_PC), .eq(comparator_8_eq));  // open: gt, lt
  Comparator #(.width(32), .mode("twosComplement")) comparator_9 (
    .a(PC), .b(Tag4), .eq(comparator_9_eq));  // open: gt, lt
  Comparator #(.width(32), .mode("twosComplement")) comparator_10 (
    .a(Tag4), .b(EX_PC), .eq(comparator_10_eq));  // open: gt, lt
  Comparator #(.width(32), .mode("twosComplement")) comparator_11 (
    .a(PC), .b(Tag5), .eq(comparator_11_eq));  // open: gt, lt
  Comparator #(.width(32), .mode("twosComplement")) comparator_12 (
    .a(Tag5), .b(EX_PC), .eq(comparator_12_eq));  // open: gt, lt
  Comparator #(.width(32), .mode("twosComplement")) comparator_13 (
    .a(PC), .b(Tag6), .eq(comparator_13_eq));  // open: gt, lt
  Comparator #(.width(32), .mode("twosComplement")) comparator_14 (
    .a(Tag6), .b(EX_PC), .eq(comparator_14_eq));  // open: gt, lt
  Comparator #(.width(32), .mode("twosComplement")) comparator_15 (
    .a(PC), .b(Tag7), .eq(comparator_15_eq));  // open: gt, lt
  Comparator #(.width(32), .mode("twosComplement")) comparator_16 (
    .a(Tag7), .b(EX_PC), .eq(comparator_16_eq));  // open: gt, lt
  and and_1 (L0, comparator_1_eq, v0);
  and and_2 (w0, v0, comparator_2_eq);
  and and_3 (L1, comparator_3_eq, v1);
  and and_4 (w1, v1, comparator_4_eq);
  and and_5 (L2, comparator_5_eq, v2);
  and and_6 (w2, v2, comparator_6_eq);
  and and_7 (L3, comparator_7_eq, v3);
  and and_8 (w3, v3, comparator_8_eq);
  and and_9 (L4, comparator_9_eq, v4);
  and and_10 (w4, v4, comparator_10_eq);
  and and_11 (L5, comparator_11_eq, v5);
  and and_12 (w5, v5, comparator_12_eq);
  and and_13 (L6, comparator_13_eq, v6);
  and and_14 (w6, v6, comparator_14_eq);
  and and_15 (L7, comparator_15_eq, v7);
  and and_16 (w7, v7, comparator_16_eq);
  MAX2 max2_1 (.x(c0), .y(c1), .x_num(3'b000), .y_num(3'b001), .MAX(max2_1_max), .MAX_num(max2_1_max_num));
  MAX2 max2_2 (.x(c2), .y(c3), .x_num(3'b010), .y_num(3'b011), .MAX(max2_2_max), .MAX_num(max2_2_max_num));
  MAX2 max2_3 (.x(c4), .y(c5), .x_num(3'b100), .y_num(3'b101), .MAX(max2_3_max), .MAX_num(max2_3_max_num));
  MAX2 max2_4 (.x(c6), .y(c7), .x_num(3'b110), .y_num(3'b111), .MAX(max2_4_max), .MAX_num(max2_4_max_num));
  not not_1 (not_1_out, v7);
  not not_2 (not_2_out, v6);
  not not_3 (not_3_out, v5);
  not not_4 (not_4_out, v4);
  not not_5 (not_5_out, v3);
  not not_6 (not_6_out, v2);
  not not_7 (not_7_out, v1);
  not not_8 (not_8_out, v0);
  MAX2 max2_5 (
    .x(max2_1_max), .y(max2_2_max), .x_num(max2_1_max_num), .y_num(max2_2_max_num), .MAX(max2_5_max),
    .MAX_num(max2_5_max_num));
  MAX2 max2_6 (
    .x(max2_3_max), .y(max2_4_max), .x_num(max2_3_max_num), .y_num(max2_4_max_num), .MAX(max2_6_max),
    .MAX_num(max2_6_max_num));
  Priority_Encoder #(.select(3), .disabled("Z")) priority_encoder_1 (
    .in0(not_1_out), .in1(not_2_out), .in2(not_3_out), .in3(not_4_out), .in4(not_5_out), .in5(not_6_out),
    .in6(not_7_out), .in7(not_8_out), .out(priority_encoder_1_out), .gs(priority_encoder_1_gs));  // open: en_out, en_in
  MAX2 max2_7 (
    .x(max2_5_max), .y(max2_6_max), .x_num(max2_5_max_num), .y_num(max2_6_max_num), .MAX_num(max2_7_max_num));  // open: MAX
  and and_17 (and_17_out, v0, v1, v2, v3, v4, v5, v6, v7);
  or or_9 (EX_hit, w0, w1, w2, w3, w4, w5, w6, w7);
  Decoder #(.select(3), .tristate("false"), .disabled(0), .enable("true")) decoder_1 (
    .out0(decoder_1_out0), .out1(decoder_1_out1), .out2(decoder_1_out2), .out3(decoder_1_out3),
    .out4(decoder_1_out4), .out5(decoder_1_out5), .out6(decoder_1_out6), .out7(decoder_1_out7),
    .sel(priority_encoder_1_out), .en(priority_encoder_1_gs));
  Decoder #(.select(3), .tristate("false"), .disabled(0), .enable("true")) decoder_2 (
    .out0(decoder_2_out0), .out1(decoder_2_out1), .out2(decoder_2_out2), .out3(decoder_2_out3),
    .out4(decoder_2_out4), .out5(decoder_2_out5), .out6(decoder_2_out6), .out7(decoder_2_out7),
    .sel(max2_7_max_num), .en(and_17_out));
  not not_9 (EX_miss, EX_hit);
  or or_10 (or_10_out, decoder_2_out0, decoder_1_out7);
  or or_11 (or_11_out, decoder_2_out1, decoder_1_out6);
  or or_12 (or_12_out, decoder_2_out2, decoder_1_out5);
  or or_13 (or_13_out, decoder_2_out3, decoder_1_out4);
  or or_14 (or_14_out, decoder_2_out4, decoder_1_out3);
  or or_15 (or_15_out, decoder_2_out5, decoder_1_out2);
  or or_16 (or_16_out, decoder_2_out6, decoder_1_out1);
  or or_17 (or_17_out, decoder_2_out7, decoder_1_out0);
  and and_18 (WriteL0, or_10_out, EX_miss, EX_Branch);
  and and_19 (WriteL1, or_11_out, EX_miss, EX_Branch);
  and and_20 (WriteL2, or_12_out, EX_miss, EX_Branch);
  and and_21 (WriteL3, or_13_out, EX_miss, EX_Branch);
  and and_22 (WriteL4, or_14_out, EX_miss, EX_Branch);
  and and_23 (WriteL5, or_15_out, EX_miss, EX_Branch);
  and and_24 (WriteL6, or_16_out, EX_miss, EX_Branch);
  and and_25 (WriteL7, or_17_out, EX_miss, EX_Branch);
  \双位预测状态转换  \u_双位预测状态转换_1  (
    .high(predict0[1]), .low(predict0[0]), .jump(EX_BranchTaken), .nexthigh(\双位预测状态转换_1_nextlow [1]),
    .nextlow(\双位预测状态转换_1_nextlow [0]), .write(WriteL0));
  \双位预测状态转换  \u_双位预测状态转换_2  (
    .high(predict1[1]), .low(predict1[0]), .jump(EX_BranchTaken), .nexthigh(\双位预测状态转换_2_nextlow [1]),
    .nextlow(\双位预测状态转换_2_nextlow [0]), .write(WriteL1));
  \双位预测状态转换  \u_双位预测状态转换_3  (
    .high(predict2[1]), .low(predict2[0]), .jump(EX_BranchTaken), .nexthigh(\双位预测状态转换_3_nextlow [1]),
    .nextlow(\双位预测状态转换_3_nextlow [0]), .write(WriteL2));
  \双位预测状态转换  \u_双位预测状态转换_4  (
    .high(predict3[1]), .low(predict3[0]), .jump(EX_BranchTaken), .nexthigh(\双位预测状态转换_4_nextlow [1]),
    .nextlow(\双位预测状态转换_4_nextlow [0]), .write(WriteL3));
  \双位预测状态转换  \u_双位预测状态转换_5  (
    .high(predict4[1]), .low(predict4[0]), .jump(EX_BranchTaken), .nexthigh(\双位预测状态转换_5_nextlow [1]),
    .nextlow(\双位预测状态转换_5_nextlow [0]), .write(WriteL4));
  \双位预测状态转换  \u_双位预测状态转换_6  (
    .high(predict5[1]), .low(predict5[0]), .jump(EX_BranchTaken), .nexthigh(\双位预测状态转换_6_nextlow [1]),
    .nextlow(\双位预测状态转换_6_nextlow [0]), .write(WriteL5));
  \双位预测状态转换  \u_双位预测状态转换_7  (
    .high(predict6[1]), .low(predict6[0]), .jump(EX_BranchTaken), .nexthigh(\双位预测状态转换_7_nextlow [1]),
    .nextlow(\双位预测状态转换_7_nextlow [0]), .write(WriteL6));
  \双位预测状态转换  \u_双位预测状态转换_8  (
    .high(predict7[1]), .low(predict7[0]), .jump(EX_BranchTaken), .nexthigh(\双位预测状态转换_8_nextlow [1]),
    .nextlow(\双位预测状态转换_8_nextlow [0]), .write(WriteL7));
  and and_26 (and_26_out, EX_Branch, w0);
  and and_27 (and_27_out, EX_Branch, w1);
  and and_28 (and_28_out, EX_Branch, w2);
  and and_29 (and_29_out, EX_Branch, w3);
  and and_30 (and_30_out, EX_Branch, w4);
  and and_31 (and_31_out, EX_Branch, w5);
  and and_32 (and_32_out, EX_Branch, w6);
  and and_33 (and_33_out, EX_Branch, w7);
  or or_18 (or_18_out, and_26_out, WriteL0);
  or or_19 (or_19_out, and_27_out, WriteL1);
  or or_20 (or_20_out, and_28_out, WriteL2);
  or or_21 (or_21_out, and_29_out, WriteL3);
  or or_22 (or_22_out, and_30_out, WriteL4);
  or or_23 (or_23_out, and_31_out, WriteL5);
  or or_24 (or_24_out, and_32_out, WriteL6);
  or or_25 (or_25_out, and_33_out, WriteL7);
  Register #(.width(2), .trigger("rising"), .Select("low")) register_25 (
    .D(\双位预测状态转换_1_nextlow ), .en(or_18_out), .Q(predict0), .clk(CLK));  // open: clr
  Register #(.width(2), .trigger("rising"), .Select("low")) register_26 (
    .D(\双位预测状态转换_2_nextlow ), .en(or_19_out), .Q(predict1), .clk(CLK));  // open: clr
  Register #(.width(2), .trigger("rising"), .Select("low")) register_27 (
    .D(\双位预测状态转换_3_nextlow ), .en(or_20_out), .Q(predict2), .clk(CLK));  // open: clr
  Register #(.width(2), .trigger("rising"), .Select("low")) register_28 (
    .D(\双位预测状态转换_4_nextlow ), .en(or_21_out), .Q(predict3), .clk(CLK));  // open: clr
  Register #(.width(2), .trigger("rising"), .Select("low")) register_29 (
    .D(\双位预测状态转换_5_nextlow ), .en(or_22_out), .Q(predict4), .clk(CLK));  // open: clr
  Register #(.width(2), .trigger("rising"), .Select("low")) register_30 (
    .D(\双位预测状态转换_6_nextlow ), .en(or_23_out), .Q(predict5), .clk(CLK));  // open: clr
  Register #(.width(2), .trigger("rising"), .Select("low")) register_31 (
    .D(\双位预测状态转换_7_nextlow ), .en(or_24_out), .Q(predict6), .clk(CLK));  // open: clr
  Register #(.width(2), .trigger("rising"), .Select("low")) register_32 (
    .D(\双位预测状态转换_8_nextlow ), .en(or_25_out), .Q(predict7), .clk(CLK));  // open: clr
  assign {PredictJump, controlled_buffer_9_out[0]} = L0 ? predict0 : 2'bz;  // Controlled_Buffer controlled_buffer_9
  assign {PredictJump, controlled_buffer_10_out[0]} = L1 ? predict1 : 2'bz;  // Controlled_Buffer controlled_buffer_10
  assign {PredictJump, controlled_buffer_11_out[0]} = L2 ? predict2 : 2'bz;  // Controlled_Buffer controlled_buffer_11
  assign {PredictJump, controlled_buffer_12_out[0]} = L3 ? predict3 : 2'bz;  // Controlled_Buffer controlled_buffer_12
  assign {PredictJump, controlled_buffer_13_out[0]} = L4 ? predict4 : 2'bz;  // Controlled_Buffer controlled_buffer_13
  assign {PredictJump, controlled_buffer_14_out[0]} = L5 ? predict5 : 2'bz;  // Controlled_Buffer controlled_buffer_14
  assign {PredictJump, controlled_buffer_15_out[0]} = L6 ? predict6 : 2'bz;  // Controlled_Buffer controlled_buffer_15
  assign {PredictJump, controlled_buffer_16_out[0]} = L7 ? predict7 : 2'bz;  // Controlled_Buffer controlled_buffer_16
  Pull_Resistor #(.pull(0)) pull_resistor_1 (.node(PredictJump));

  // Other names for the same wires on the sheet: JumpAddr[31:0] = JumpAdrr; Tag[31:0] = EX_PC
endmodule

// MAX
module MAX2 (
  input  [31:0] x,
  input  [31:0] y,
  input  [2:0] x_num,
  input  [2:0] y_num,
  output [31:0] MAX,
  output [2:0] MAX_num
);

  wire comparator_1_lt;

  Comparator #(.width(32), .mode("unsigned")) comparator_1 (.a(x), .b(y), .lt(comparator_1_lt));  // open: gt, eq
  Multiplexer #(.select(1), .width(32), .disabled("Z"), .enable("false")) multiplexer_1 (
    .in0(x), .in1(y), .out(MAX), .sel(comparator_1_lt));
  Multiplexer #(.select(1), .width(3), .disabled("Z"), .enable("false")) multiplexer_2 (
    .in0(x_num), .in1(y_num), .out(MAX_num), .sel(comparator_1_lt));
endmodule

// 状态转换
module \双位预测状态转换  (
  input  high,
  input  low,
  input  jump,
  input  write,
  output nexthigh,
  output nextlow
);

  wire and_1_out, and_2_out, and_3_out, and_4_out, multiplexer_1_out, multiplexer_2_out, not_1_out,
       not_2_out, not_3_out, not_4_out, not_5_out, or_1_out, or_2_out;

  not not_1 (not_1_out, low);
  not not_2 (not_2_out, high);
  not not_3 (not_3_out, low);
  not not_4 (not_4_out, low);
  not not_5 (not_5_out, jump);
  and and_1 (and_1_out, low, jump);
  and and_2 (and_2_out, high, not_1_out);
  and and_3 (and_3_out, not_2_out, not_3_out, jump);
  and and_4 (and_4_out, high, not_4_out, not_5_out);
  or or_1 (or_1_out, and_1_out, and_2_out);
  or or_2 (or_2_out, and_3_out, and_4_out);
  Multiplexer #(.select(1), .width(1), .disabled("Z"), .enable("false")) multiplexer_1 (
    .in0(1'b0), .in1(1'b1), .out(multiplexer_1_out), .sel(jump));
  Multiplexer #(.select(1), .width(1), .disabled("Z"), .enable("false")) multiplexer_2 (
    .in0(1'b1), .in1(1'b0), .out(multiplexer_2_out), .sel(jump));
  Multiplexer #(.select(1), .width(1), .disabled("Z"), .enable("false")) multiplexer_3 (
    .in0(or_1_out), .in1(multiplexer_1_out), .out(nexthigh), .sel(write));
  Multiplexer #(.select(1), .width(1), .disabled("Z"), .enable("false")) multiplexer_4 (
    .in0(or_2_out), .in1(multiplexer_2_out), .out(nextlow), .sel(write));
endmodule
